// Logisim project Assignment1.circ as structural Verilog: 8 circuits, main circuit main
module main (
  input  SetTime,
  input  Set_alarm,
  input  in_3,
  input  Power,
  input  StopTimer,
  input  in_6,
  input  in_7
);

  wire and_1_out, and_2_out, and_3_out, and_4_out, and_5_out, and_6_out, and_7_out, and_8_out, and_9_out,
       and_10_out, and_11_out, and_12_out, and_13_out, and_14_out, and_15_out, and_16_out, and_17_out,
       and_18_out, and_19_out, and_20_out, and_21_out, and_22_out, and_23_out, and_24_out, and_25_out,
       and_26_out, and_27_out, and_28_out, and_29_out, and_30_out, and_31_out, and_32_out, and_33_out,
       and_34_out, and_35_out, and_36_out, and_37_out, and_38_out, and_39_out, and_40_out, and_41_out,
       and_42_out, and_43_out, and_44_out, and_45_out, and_46_out, and_47_out, and_48_out, and_49_out,
       and_50_out, and_51_out, and_52_out, and_53_out, and_54_out, and_55_out, and_56_out, and_57_out,
       and_58_out, and_59_out, and_60_out, and_61_out, and_62_out, and_63_out, and_64_out, and_65_out,
       and_66_out, and_67_out, and_68_out, and_69_out, and_70_out, and_71_out, and_72_out, and_73_out,
       and_74_out, and_75_out, and_76_out, and_77_out, and_78_out, and_79_out, and_80_out, and_81_out,
       and_82_out, and_83_out, and_84_out, and_85_out, and_86_out, and_87_out, and_88_out, and_89_out,
       and_90_out, and_91_out, and_92_out, and_93_out, and_94_out, and_95_out, and_96_out, and_97_out,
       and_98_out, and_99_out, and_100_out, and_101_out, and_102_out, and_103_out, button_1_out,
       button_2_out, button_3_out, button_4_out, button_5_out, button_6_out, button_7_out, clock_1_out,
       clock_2_out, d_ff_1_q, d_ff_2_q, d_ff_3_q, d_ff_4_q, d_ff_5_q, d_ff_6_q, d_ff_7_q, d_ff_11_q,
       d_ff_12_q, d_ff_14_q, d_ff_15_q, d_ff_18_q, d_ff_20_q, d_ff_22_q, d_ff_23_q, d_ff_26_q, d_ff_29_q,
       d_ff_30_q, d_ff_31_q, d_ff_32_q, d_ff_33_q, d_ff_34_q, d_ff_35_q, d_ff_36_q, d_ff_37_q, d_ff_38_q,
       d_ff_39_q, d_ff_40_q, d_ff_41_q, d_ff_42_q, d_ff_43_q, d_ff_44_q, d_ff_45_q, j_k_ff_1_q, j_k_ff_2_q,
       j_k_ff_3_q, j_k_ff_4_q, j_k_ff_5_q, j_k_ff_6_q, j_k_ff_7_q, j_k_ff_8_q, j_k_ff_9_q, j_k_ff_10_q,
       j_k_ff_11_q, j_k_ff_12_q, j_k_ff_13_q, j_k_ff_14_q, j_k_ff_15_q, j_k_ff_16_q, j_k_ff_17_q,
       j_k_ff_18_q, j_k_ff_19_q, j_k_ff_20_q, j_k_ff_21_q, j_k_ff_22_q, j_k_ff_23_q, j_k_ff_24_q,
       j_k_ff_25_q, j_k_ff_25_qn, j_k_ff_26_q, j_k_ff_27_q, j_k_ff_28_q, j_k_ff_29_q, j_k_ff_30_q,
       j_k_ff_31_q, j_k_ff_32_q, j_k_ff_33_q, j_k_ff_34_q, j_k_ff_35_q, j_k_ff_36_q, j_k_ff_37_q,
       j_k_ff_38_q, j_k_ff_39_q, j_k_ff_40_q, nand_1_out, nand_2_out, nand_3_out, not_1_out, not_2_out,
       not_3_out, not_4_out, not_5_out, not_6_out, not_7_out, or_1_out, or_2_out, or_3_out, or_4_out,
       or_5_out, or_6_out, or_7_out, or_8_out, or_9_out, or_10_out, or_11_out, or_12_out, or_13_out,
       or_14_out, or_15_out, or_16_out, or_17_out, or_18_out, or_19_out, or_20_out, or_30_out, or_31_out,
       or_35_out, or_36_out, or_37_out, or_38_out, or_39_out, or_40_out, or_41_out, switch_1_p2, xnor_1_out,
       xnor_2_out, xnor_3_out, xnor_4_out, xnor_5_out, xnor_6_out, xnor_7_out, xnor_8_out, xnor_9_out,
       xnor_10_out, xnor_11_out, xnor_12_out, xnor_13_out;
  wire [0:0] d_ff_10_q, or_23_out;
  wire [2:0] d_ff_13_q, or_25_out;
  wire [3:0] d_ff_8_q, d_ff_9_q, or_27_out, or_34_out;

  and and_1 (and_1_out, and_3_out, j_k_ff_12_q);
  or or_1 (or_1_out, and_1_out, and_4_out);
  or or_2 (or_2_out, or_1_out, and_9_out);
  and and_2 (and_2_out, and_7_out, j_k_ff_10_q);
  D_Flip_Flop d_ff_1 (.D(and_14_out), .clk(and_42_out), .Q(d_ff_1_q));  // open: Qn, preset, reset
  and and_3 (and_3_out, and_14_out, or_9_out);
  D_Flip_Flop d_ff_2 (.D(and_3_out), .clk(and_42_out), .Q(d_ff_2_q));  // open: Qn, preset, reset
  and and_4 (and_4_out, and_3_out, and_9_out);
  D_Flip_Flop d_ff_3 (.D(or_2_out), .clk(and_42_out), .Q(d_ff_3_q));  // open: Qn, preset, reset
  D_Flip_Flop d_ff_4 (.D(and_7_out), .clk(or_17_out), .Q(d_ff_4_q));  // open: Qn, preset, reset
  and and_5 (and_5_out, and_7_out, and_8_out);
  or or_3 (or_3_out, and_2_out, and_5_out);
  or or_4 (or_4_out, or_3_out, and_8_out);
  D_Flip_Flop d_ff_5 (.D(or_4_out), .clk(or_17_out), .Q(d_ff_5_q));  // open: Qn, preset, reset
  and and_6 (and_6_out, d_ff_5_q, nand_1_out);
  D_Flip_Flop d_ff_6 (.D(and_13_out), .clk(or_17_out), .Q(d_ff_6_q));  // open: Qn, preset, reset
  and and_7 (and_7_out, and_13_out, or_6_out);
  and and_8 (and_8_out, j_k_ff_21_q, j_k_ff_5_q);
  and and_9 (and_9_out, j_k_ff_24_q, j_k_ff_8_q);
  and and_10 (and_10_out, d_ff_3_q, nand_2_out);
  or or_5 (or_5_out, and_10_out, and_45_out);
  and and_11 (and_11_out, j_k_ff_4_q, j_k_ff_20_q);
  or or_6 (or_6_out, and_11_out, and_54_out);
  or or_7 (or_7_out, d_ff_4_q, and_54_out);
  or or_8 (or_8_out, and_6_out, and_25_out);
  J_K_Flip_Flop j_k_ff_1 (
    .J(switch_1_p2), .K(switch_1_p2), .clk(and_42_out), .Q(j_k_ff_1_q), .reset(or_14_out));  // open: Qn, preset
  and and_12 (and_12_out, j_k_ff_7_q, j_k_ff_23_q);
  or or_9 (or_9_out, and_12_out, and_43_out);
  or or_10 (or_10_out, d_ff_2_q, and_43_out);
  J_K_Flip_Flop j_k_ff_2 (
    .J(and_9_out), .K(and_9_out), .clk(or_5_out), .Q(j_k_ff_2_q), .reset(or_11_out));  // open: Qn, preset
  J_K_Flip_Flop j_k_ff_3 (
    .J(Power), .K(Power), .clk(or_17_out), .Q(j_k_ff_3_q), .reset(and_26_out));  // open: Qn, preset
  and and_13 (and_13_out, j_k_ff_3_q, j_k_ff_19_q);
  J_K_Flip_Flop j_k_ff_4 (
    .J(and_13_out), .K(and_13_out), .clk(d_ff_6_q), .Q(j_k_ff_4_q), .reset(and_27_out));  // open: Qn, preset
  J_K_Flip_Flop j_k_ff_5 (.J(or_6_out), .K(or_6_out), .clk(or_7_out), .Q(j_k_ff_5_q));  // open: Qn, preset, reset
  J_K_Flip_Flop j_k_ff_6 (
    .J(and_8_out), .K(and_8_out), .clk(or_8_out), .Q(j_k_ff_6_q), .reset(and_32_out));  // open: Qn, preset
  and and_14 (and_14_out, j_k_ff_1_q, j_k_ff_22_q);
  J_K_Flip_Flop j_k_ff_7 (
    .J(and_14_out), .K(and_14_out), .clk(d_ff_1_q), .Q(j_k_ff_7_q), .reset(or_15_out));  // open: Qn, preset
  J_K_Flip_Flop j_k_ff_8 (
    .J(or_9_out), .K(or_9_out), .clk(or_10_out), .Q(j_k_ff_8_q), .reset(button_7_out));  // open: Qn, preset
  or or_11 (or_11_out, button_7_out, and_33_out);
  D_Flip_Flop #(.trigger("falling")) d_ff_7 (
    .D(j_k_ff_2_q), .clk(or_5_out), .Q(d_ff_7_q), .reset(button_7_out));  // open: Qn, preset
  D_Flip_Flop d_ff_8 (.D(j_k_ff_3_q), .clk(or_17_out), .Q(d_ff_8_q[0]));  // open: Qn, preset, reset
  D_Flip_Flop #(.trigger("falling")) d_ff_9 (
    .D(j_k_ff_5_q), .clk(or_7_out), .Q(d_ff_9_q[0]));  // open: Qn, preset, reset
  D_Flip_Flop #(.trigger("falling")) d_ff_10 (
    .D(j_k_ff_6_q), .clk(or_8_out), .Q(d_ff_10_q[0]));  // open: Qn, preset, reset
  D_Flip_Flop d_ff_11 (.D(j_k_ff_1_q), .clk(and_42_out), .Q(d_ff_11_q), .reset(button_7_out));  // open: Qn, preset
  D_Flip_Flop #(.trigger("falling")) d_ff_12 (
    .D(j_k_ff_8_q), .clk(or_10_out), .Q(d_ff_12_q), .reset(button_7_out));  // open: Qn, preset
  J_K_Flip_Flop j_k_ff_9 (
    .J(j_k_ff_3_q), .K(j_k_ff_3_q), .clk(or_17_out), .Q(j_k_ff_9_q), .reset(and_26_out));  // open: Qn, preset
  D_Flip_Flop #(.trigger("falling")) d_ff_13 (
    .D(j_k_ff_4_q), .clk(d_ff_6_q), .Q(d_ff_13_q[0]));  // open: Qn, preset, reset
  J_K_Flip_Flop j_k_ff_10 (
    .J(j_k_ff_5_q), .K(j_k_ff_5_q), .clk(or_7_out), .Q(j_k_ff_10_q), .reset(or_16_out));  // open: Qn, preset
  J_K_Flip_Flop j_k_ff_11 (
    .J(j_k_ff_1_q), .K(j_k_ff_1_q), .clk(and_42_out), .Q(j_k_ff_11_q), .reset(or_14_out));  // open: Qn, preset
  D_Flip_Flop #(.trigger("falling")) d_ff_14 (
    .D(j_k_ff_7_q), .clk(d_ff_1_q), .Q(d_ff_14_q), .reset(button_7_out));  // open: Qn, preset
  J_K_Flip_Flop j_k_ff_12 (
    .J(j_k_ff_8_q), .K(j_k_ff_8_q), .clk(or_10_out), .Q(j_k_ff_12_q), .reset(or_12_out));  // open: Qn, preset
  J_K_Flip_Flop j_k_ff_13 (
    .J(j_k_ff_4_q), .K(j_k_ff_4_q), .clk(d_ff_6_q), .Q(j_k_ff_13_q), .reset(and_27_out));  // open: Qn, preset
  D_Flip_Flop d_ff_15 (.D(j_k_ff_11_q), .clk(and_42_out), .Q(d_ff_15_q), .reset(button_7_out));  // open: Qn, preset
  J_K_Flip_Flop j_k_ff_14 (
    .J(j_k_ff_7_q), .K(j_k_ff_7_q), .clk(d_ff_1_q), .Q(j_k_ff_14_q), .reset(or_15_out));  // open: Qn, preset
  and and_15 (and_15_out, j_k_ff_3_q, j_k_ff_9_q);
  J_K_Flip_Flop j_k_ff_15 (
    .J(and_15_out), .K(and_15_out), .clk(or_17_out), .Q(j_k_ff_15_q), .reset(and_26_out));  // open: Qn, preset
  D_Flip_Flop d_ff_16 (.D(j_k_ff_9_q), .clk(or_17_out), .Q(d_ff_8_q[1]));  // open: Qn, preset, reset
  and and_16 (and_16_out, j_k_ff_5_q, j_k_ff_10_q);
  D_Flip_Flop #(.trigger("falling")) d_ff_17 (
    .D(j_k_ff_10_q), .clk(or_7_out), .Q(d_ff_9_q[1]));  // open: Qn, preset, reset
  and and_17 (and_17_out, j_k_ff_1_q, j_k_ff_11_q);
  J_K_Flip_Flop j_k_ff_16 (
    .J(and_17_out), .K(and_17_out), .clk(and_42_out), .Q(j_k_ff_16_q), .reset(or_14_out));  // open: Qn, preset
  and and_18 (and_18_out, j_k_ff_8_q, j_k_ff_12_q);
  J_K_Flip_Flop j_k_ff_17 (
    .J(and_18_out), .K(and_18_out), .clk(or_10_out), .Q(j_k_ff_17_q), .reset(or_12_out));  // open: Qn, preset
  D_Flip_Flop #(.trigger("falling")) d_ff_18 (
    .D(j_k_ff_12_q), .clk(or_10_out), .Q(d_ff_18_q), .reset(button_7_out));  // open: Qn, preset
  D_Flip_Flop #(.trigger("falling")) d_ff_19 (
    .D(j_k_ff_13_q), .clk(d_ff_6_q), .Q(d_ff_13_q[1]));  // open: Qn, preset, reset
  J_K_Flip_Flop j_k_ff_18 (
    .J(and_16_out), .K(and_16_out), .clk(or_7_out), .Q(j_k_ff_18_q), .reset(or_16_out));  // open: Qn, preset
  D_Flip_Flop #(.trigger("falling")) d_ff_20 (
    .D(j_k_ff_14_q), .clk(d_ff_1_q), .Q(d_ff_20_q), .reset(button_7_out));  // open: Qn, preset
  D_Flip_Flop d_ff_21 (.D(j_k_ff_15_q), .clk(or_17_out), .Q(d_ff_8_q[2]));  // open: Qn, preset, reset
  and and_19 (and_19_out, j_k_ff_4_q, j_k_ff_13_q);
  D_Flip_Flop d_ff_22 (.D(j_k_ff_16_q), .clk(and_42_out), .Q(d_ff_22_q), .reset(button_7_out));  // open: Qn, preset
  and and_20 (and_20_out, j_k_ff_7_q, j_k_ff_14_q);
  D_Flip_Flop #(.trigger("falling")) d_ff_23 (
    .D(j_k_ff_17_q), .clk(or_10_out), .Q(d_ff_23_q), .reset(button_7_out));  // open: Qn, preset
  and and_21 (and_21_out, and_15_out, j_k_ff_15_q);
  J_K_Flip_Flop j_k_ff_19 (
    .J(and_21_out), .K(and_21_out), .clk(or_17_out), .Q(j_k_ff_19_q), .reset(and_26_out));  // open: Qn, preset
  J_K_Flip_Flop j_k_ff_20 (
    .J(and_19_out), .K(and_19_out), .clk(d_ff_6_q), .Q(j_k_ff_20_q), .reset(and_27_out));  // open: Qn, preset
  and and_22 (and_22_out, and_16_out, j_k_ff_18_q);
  J_K_Flip_Flop j_k_ff_21 (
    .J(and_22_out), .K(and_22_out), .clk(or_7_out), .Q(j_k_ff_21_q), .reset(or_16_out));  // open: Qn, preset
  D_Flip_Flop #(.trigger("falling")) d_ff_24 (
    .D(j_k_ff_18_q), .clk(or_7_out), .Q(d_ff_9_q[2]));  // open: Qn, preset, reset
  and and_23 (and_23_out, and_17_out, j_k_ff_16_q);
  J_K_Flip_Flop j_k_ff_22 (
    .J(and_23_out), .K(and_23_out), .clk(and_42_out), .Q(j_k_ff_22_q), .reset(or_14_out));  // open: Qn, preset
  J_K_Flip_Flop j_k_ff_23 (
    .J(and_20_out), .K(and_20_out), .clk(d_ff_1_q), .Q(j_k_ff_23_q), .reset(or_15_out));  // open: Qn, preset
  and and_24 (and_24_out, and_18_out, j_k_ff_17_q);
  J_K_Flip_Flop j_k_ff_24 (
    .J(and_24_out), .K(and_24_out), .clk(or_10_out), .Q(j_k_ff_24_q), .reset(or_12_out));  // open: Qn, preset
  or or_12 (or_12_out, button_7_out, or_13_out);
  D_Flip_Flop #(.trigger("falling")) d_ff_25 (
    .D(j_k_ff_20_q), .clk(d_ff_6_q), .Q(d_ff_13_q[2]));  // open: Qn, preset, reset
  and and_25 (and_25_out, and_54_out, StopTimer);
  D_Flip_Flop #(.trigger("falling")) d_ff_26 (
    .D(j_k_ff_23_q), .clk(d_ff_1_q), .Q(d_ff_26_q), .reset(button_7_out));  // open: Qn, preset
  or or_13 (or_13_out, and_31_out, and_33_out);
  and and_26 (and_26_out, j_k_ff_19_q, j_k_ff_9_q);
  D_Flip_Flop d_ff_27 (.D(j_k_ff_19_q), .clk(or_17_out), .Q(d_ff_8_q[3]));  // open: Qn, preset, reset
  and and_27 (and_27_out, j_k_ff_20_q, j_k_ff_13_q);
  and and_28 (and_28_out, j_k_ff_21_q, j_k_ff_10_q);
  D_Flip_Flop #(.trigger("falling")) d_ff_28 (
    .D(j_k_ff_21_q), .clk(or_7_out), .Q(d_ff_9_q[3]));  // open: Qn, preset, reset
  and and_29 (and_29_out, j_k_ff_22_q, j_k_ff_11_q);
  or or_14 (or_14_out, and_29_out, button_7_out);
  D_Flip_Flop d_ff_29 (.D(j_k_ff_22_q), .clk(and_42_out), .Q(d_ff_29_q), .reset(button_7_out));  // open: Qn, preset
  and and_30 (and_30_out, j_k_ff_23_q, j_k_ff_14_q);
  or or_15 (or_15_out, and_30_out, button_7_out);
  and and_31 (and_31_out, j_k_ff_24_q, j_k_ff_12_q);
  D_Flip_Flop #(.trigger("falling")) d_ff_30 (
    .D(j_k_ff_24_q), .clk(or_10_out), .Q(d_ff_30_q), .reset(button_7_out));  // open: Qn, preset
  or or_16 (or_16_out, and_28_out, and_32_out);
  or or_17 (or_17_out, and_38_out, and_34_out);
  Hex_Digit_Display hex_digit_display_1 (.value({{3{in_7}}, d_ff_10_q[0]}));  // open: dp
  Hex_Digit_Display hex_digit_display_2 (.value(d_ff_9_q));  // open: dp
  Hex_Digit_Display hex_digit_display_3 (.value({in_6, d_ff_13_q}));  // open: dp
  and and_32 (and_32_out, and_16_out, j_k_ff_6_q);
  and and_33 (and_33_out, and_18_out, j_k_ff_2_q);
  and and_34 (and_34_out, StopTimer, button_1_out);
  Hex_Digit_Display hex_digit_display_4 (.value(d_ff_8_q));  // open: dp
  or or_18 (or_18_out, and_42_out, and_43_out, and_44_out);
  J_K_Flip_Flop j_k_ff_25 (
    .J(j_k_ff_25_qn), .K(j_k_ff_25_qn), .clk(or_18_out), .Q(j_k_ff_25_q), .Qn(j_k_ff_25_qn),
    .reset(button_7_out));  // open: preset
  not not_1 (not_1_out, and_44_out);
  and and_35 (and_35_out, j_k_ff_2_q, d_ff_18_q);
  and and_36 (and_36_out, not_1_out, and_35_out);
  and and_37 (and_37_out, j_k_ff_2_q, nand_2_out);
  and and_38 (and_38_out, clock_1_out, nand_1_out);
  LED led_1 (.in(j_k_ff_26_q));
  and and_39 (and_39_out, d_ff_9_q[1], and_40_out);
  and and_40 (and_40_out, j_k_ff_6_q, nand_1_out);
  or or_19 (or_19_out, and_44_out, and_36_out, and_41_out);
  and and_41 (and_41_out, d_ff_18_q, and_37_out);
  Clock clock_1 (.out(clock_1_out));
  nand nand_1 (nand_1_out, Power, StopTimer);
  Button button_1 (.out(button_1_out));
  Button button_2 (.out(button_2_out));
  Button button_3 (.out(button_3_out));
  J_K_Flip_Flop j_k_ff_26 (.J(Power), .K(Power), .clk(or_20_out), .Q(j_k_ff_26_q));  // open: Qn, preset, reset
  or or_20 (or_20_out, and_39_out, and_64_out);
  nand nand_2 (nand_2_out, switch_1_p2, Set_alarm);
  and and_42 (and_42_out, Set_alarm, button_4_out);
  and and_43 (and_43_out, Set_alarm, button_5_out);
  and and_44 (and_44_out, Set_alarm, button_6_out);
  and and_45 (and_45_out, and_43_out, Set_alarm);
  J_K_Flip_Flop j_k_ff_27 (
    .J(switch_1_p2), .K(switch_1_p2), .clk(or_19_out), .Q(j_k_ff_27_q));  // open: Qn, preset, reset
  Hex_Digit_Display hex_digit_display_5 (.value({{3{in_3}}, or_23_out[0]}));  // open: dp
  or or_21 (or_25_out[1], and_46_out, and_47_out);
  and and_46 (and_46_out, Set_alarm, d_ff_20_q);
  and and_47 (and_47_out, d_ff_40_q, not_3_out);
  or or_22 (or_27_out[2], and_48_out, and_49_out);
  and and_48 (and_48_out, Set_alarm, d_ff_23_q);
  and and_49 (and_49_out, d_ff_42_q, not_4_out);
  or or_23 (or_23_out[0], and_50_out, and_53_out);
  and and_50 (and_50_out, Set_alarm, d_ff_7_q);
  xnor xnor_1 (xnor_1_out, d_ff_7_q, d_ff_34_q);
  xnor xnor_2 (xnor_2_out, d_ff_30_q, d_ff_45_q);
  LED led_2 (.in(j_k_ff_25_q));
  not not_2 (not_2_out, or_38_out);
  LED led_3 (.in(not_2_out));
  Hex_Digit_Display hex_digit_display_6 (.value(or_27_out));  // open: dp
  Hex_Digit_Display hex_digit_display_7 (.value({in_3, or_25_out}));  // open: dp
  or or_24 (or_27_out[3], and_51_out, and_52_out);
  and and_51 (and_51_out, Set_alarm, d_ff_30_q);
  and and_52 (and_52_out, d_ff_45_q, not_4_out);
  and and_53 (and_53_out, d_ff_34_q, not_4_out);
  xnor xnor_3 (xnor_3_out, d_ff_23_q, d_ff_42_q);
  xnor xnor_4 (xnor_4_out, d_ff_18_q, d_ff_39_q);
  and and_54 (and_54_out, StopTimer, button_2_out);
  LED led_4 (.in(and_68_out));
  LED led_5 (.in(not_5_out));
  LED led_6 (.in(Set_alarm));
  LED led_7 (.in(or_38_out));
  Hex_Digit_Display hex_digit_display_8 (.value(or_34_out));  // open: dp
  or or_25 (or_25_out[0], and_55_out, and_56_out);
  and and_55 (and_55_out, Set_alarm, d_ff_14_q);
  and and_56 (and_56_out, d_ff_36_q, not_3_out);
  or or_26 (or_25_out[2], and_57_out, and_58_out);
  and and_57 (and_57_out, Set_alarm, d_ff_26_q);
  and and_58 (and_58_out, d_ff_43_q, not_3_out);
  not not_3 (not_3_out, Set_alarm);
  or or_27 (or_27_out[0], and_59_out, and_60_out);
  and and_59 (and_59_out, Set_alarm, d_ff_12_q);
  and and_60 (and_60_out, d_ff_37_q, not_4_out);
  or or_28 (or_27_out[1], and_61_out, and_62_out);
  and and_61 (and_61_out, Set_alarm, d_ff_18_q);
  and and_62 (and_62_out, d_ff_39_q, not_4_out);
  not not_4 (not_4_out, Set_alarm);
  xnor xnor_5 (xnor_5_out, d_ff_14_q, d_ff_36_q);
  xnor xnor_6 (xnor_6_out, d_ff_12_q, d_ff_37_q);
  and and_63 (and_63_out, xnor_1_out, xnor_2_out, xnor_3_out, xnor_4_out, xnor_6_out, xnor_5_out, xnor_7_out, xnor_8_out, xnor_9_out, xnor_10_out, xnor_11_out, xnor_12_out, xnor_13_out);
  and and_64 (and_64_out, StopTimer, button_3_out);
  or or_29 (or_34_out[3], and_65_out, and_66_out);
  and and_65 (and_65_out, Set_alarm, d_ff_29_q);
  and and_66 (and_66_out, d_ff_44_q, not_3_out);
  and and_67 (and_67_out, and_71_out, j_k_ff_33_q);
  or or_30 (or_30_out, and_67_out, and_72_out);
  or or_31 (or_31_out, or_30_out, and_77_out);
  xnor xnor_7 (xnor_7_out, d_ff_20_q, d_ff_40_q);
  xnor xnor_8 (xnor_8_out, d_ff_26_q, d_ff_43_q);
  and and_68 (and_68_out, j_k_ff_25_q, and_63_out);
  not not_5 (not_5_out, Set_alarm);
  or or_32 (or_34_out[2], and_69_out, and_70_out);
  and and_69 (and_69_out, Set_alarm, d_ff_22_q);
  and and_70 (and_70_out, d_ff_41_q, not_3_out);
  D_Flip_Flop d_ff_31 (.D(and_79_out), .clk(and_91_out), .Q(d_ff_31_q));  // open: Qn, preset, reset
  and and_71 (and_71_out, and_79_out, or_36_out);
  D_Flip_Flop d_ff_32 (.D(and_71_out), .clk(and_91_out), .Q(d_ff_32_q));  // open: Qn, preset, reset
  and and_72 (and_72_out, and_71_out, and_77_out);
  D_Flip_Flop d_ff_33 (.D(or_31_out), .clk(and_91_out), .Q(d_ff_33_q));  // open: Qn, preset, reset
  xnor xnor_9 (xnor_9_out, d_ff_11_q, d_ff_35_q);
  xnor xnor_10 (xnor_10_out, d_ff_15_q, d_ff_38_q);
  or or_33 (or_34_out[1], and_73_out, and_74_out);
  and and_73 (and_73_out, Set_alarm, d_ff_15_q);
  and and_74 (and_74_out, d_ff_38_q, not_3_out);
  xnor xnor_11 (xnor_11_out, d_ff_22_q, d_ff_41_q);
  xnor xnor_12 (xnor_12_out, d_ff_29_q, d_ff_44_q);
  or or_34 (or_34_out[0], and_75_out, and_76_out);
  and and_75 (and_75_out, Set_alarm, d_ff_11_q);
  and and_76 (and_76_out, d_ff_35_q, not_3_out);
  and and_77 (and_77_out, j_k_ff_39_q, j_k_ff_30_q);
  J_K_Flip_Flop j_k_ff_28 (
    .J(and_77_out), .K(and_77_out), .clk(or_35_out), .Q(j_k_ff_28_q), .reset(and_92_out));  // open: Qn, preset
  and and_78 (and_78_out, d_ff_33_q, nand_3_out);
  or or_35 (or_35_out, and_78_out, and_103_out);
  xnor xnor_13 (xnor_13_out, j_k_ff_27_q, j_k_ff_40_q);
  J_K_Flip_Flop j_k_ff_29 (
    .J(switch_1_p2), .K(switch_1_p2), .clk(and_91_out), .Q(j_k_ff_29_q), .reset(and_88_out));  // open: Qn, preset
  and and_79 (and_79_out, j_k_ff_29_q, j_k_ff_37_q);
  and and_80 (and_80_out, j_k_ff_31_q, j_k_ff_38_q);
  or or_36 (or_36_out, and_80_out, and_102_out);
  J_K_Flip_Flop j_k_ff_30 (.J(or_36_out), .K(or_36_out), .clk(or_37_out), .Q(j_k_ff_30_q));  // open: Qn, preset, reset
  or or_37 (or_37_out, d_ff_32_q, and_102_out);
  D_Flip_Flop #(.trigger("falling")) d_ff_34 (
    .D(j_k_ff_28_q), .clk(or_35_out), .Q(d_ff_34_q));  // open: Qn, preset, reset
  D_Flip_Flop d_ff_35 (.D(j_k_ff_29_q), .clk(and_91_out), .Q(d_ff_35_q));  // open: Qn, preset, reset
  and and_81 (and_81_out, Set_alarm, j_k_ff_27_q);
  J_K_Flip_Flop j_k_ff_31 (
    .J(and_79_out), .K(and_79_out), .clk(d_ff_31_q), .Q(j_k_ff_31_q), .reset(and_89_out));  // open: Qn, preset
  or or_38 (or_38_out, and_81_out, and_82_out);
  and and_82 (and_82_out, j_k_ff_40_q, not_3_out);
  D_Flip_Flop #(.trigger("falling")) d_ff_36 (
    .D(j_k_ff_31_q), .clk(d_ff_31_q), .Q(d_ff_36_q));  // open: Qn, preset, reset
  D_Flip_Flop #(.trigger("falling")) d_ff_37 (
    .D(j_k_ff_30_q), .clk(or_37_out), .Q(d_ff_37_q));  // open: Qn, preset, reset
  J_K_Flip_Flop j_k_ff_32 (
    .J(j_k_ff_29_q), .K(j_k_ff_29_q), .clk(and_91_out), .Q(j_k_ff_32_q), .reset(and_88_out));  // open: Qn, preset
  J_K_Flip_Flop j_k_ff_33 (
    .J(j_k_ff_30_q), .K(j_k_ff_30_q), .clk(or_37_out), .Q(j_k_ff_33_q), .reset(or_39_out));  // open: Qn, preset
  D_Flip_Flop d_ff_38 (.D(j_k_ff_32_q), .clk(and_91_out), .Q(d_ff_38_q));  // open: Qn, preset, reset
  J_K_Flip_Flop j_k_ff_34 (
    .J(j_k_ff_31_q), .K(j_k_ff_31_q), .clk(d_ff_31_q), .Q(j_k_ff_34_q), .reset(and_89_out));  // open: Qn, preset
  D_Flip_Flop #(.trigger("falling")) d_ff_39 (
    .D(j_k_ff_33_q), .clk(or_37_out), .Q(d_ff_39_q));  // open: Qn, preset, reset
  and and_83 (and_83_out, j_k_ff_29_q, j_k_ff_32_q);
  J_K_Flip_Flop j_k_ff_35 (
    .J(and_83_out), .K(and_83_out), .clk(and_91_out), .Q(j_k_ff_35_q), .reset(and_88_out));  // open: Qn, preset
  and and_84 (and_84_out, j_k_ff_30_q, j_k_ff_33_q);
  J_K_Flip_Flop j_k_ff_36 (
    .J(and_84_out), .K(and_84_out), .clk(or_37_out), .Q(j_k_ff_36_q), .reset(or_39_out));  // open: Qn, preset
  and and_85 (and_85_out, j_k_ff_31_q, j_k_ff_34_q);
  D_Flip_Flop #(.trigger("falling")) d_ff_40 (
    .D(j_k_ff_34_q), .clk(d_ff_31_q), .Q(d_ff_40_q));  // open: Qn, preset, reset
  D_Flip_Flop d_ff_41 (.D(j_k_ff_35_q), .clk(and_91_out), .Q(d_ff_41_q));  // open: Qn, preset, reset
  D_Flip_Flop #(.trigger("falling")) d_ff_42 (
    .D(j_k_ff_36_q), .clk(or_37_out), .Q(d_ff_42_q));  // open: Qn, preset, reset
  and and_86 (and_86_out, and_83_out, j_k_ff_35_q);
  J_K_Flip_Flop j_k_ff_37 (
    .J(and_86_out), .K(and_86_out), .clk(and_91_out), .Q(j_k_ff_37_q), .reset(and_88_out));  // open: Qn, preset
  J_K_Flip_Flop j_k_ff_38 (
    .J(and_85_out), .K(and_85_out), .clk(d_ff_31_q), .Q(j_k_ff_38_q), .reset(and_89_out));  // open: Qn, preset
  and and_87 (and_87_out, and_84_out, j_k_ff_36_q);
  J_K_Flip_Flop j_k_ff_39 (
    .J(and_87_out), .K(and_87_out), .clk(or_37_out), .Q(j_k_ff_39_q), .reset(or_39_out));  // open: Qn, preset
  and and_88 (and_88_out, j_k_ff_37_q, j_k_ff_32_q);
  and and_89 (and_89_out, j_k_ff_38_q, j_k_ff_34_q);
  D_Flip_Flop #(.trigger("falling")) d_ff_43 (
    .D(j_k_ff_38_q), .clk(d_ff_31_q), .Q(d_ff_43_q));  // open: Qn, preset, reset
  or or_39 (or_39_out, and_90_out, and_92_out);
  D_Flip_Flop d_ff_44 (.D(j_k_ff_37_q), .clk(and_91_out), .Q(d_ff_44_q));  // open: Qn, preset, reset
  and and_90 (and_90_out, j_k_ff_39_q, j_k_ff_33_q);
  D_Flip_Flop #(.trigger("falling")) d_ff_45 (
    .D(j_k_ff_39_q), .clk(or_37_out), .Q(d_ff_45_q));  // open: Qn, preset, reset
  and and_91 (and_91_out, not_7_out, or_40_out);
  or or_40 (or_40_out, and_93_out, and_99_out);
  and and_92 (and_92_out, and_84_out, j_k_ff_28_q);
  and and_93 (and_93_out, clock_2_out, nand_3_out);
  not not_6 (not_6_out, and_98_out);
  and and_94 (and_94_out, j_k_ff_28_q, d_ff_39_q);
  and and_95 (and_95_out, not_6_out, and_94_out);
  and and_96 (and_96_out, d_ff_39_q, and_97_out);
  and and_97 (and_97_out, j_k_ff_28_q, nand_3_out);
  Clock clock_2 (.out(clock_2_out));
  and and_98 (and_98_out, not_7_out, and_101_out);
  J_K_Flip_Flop j_k_ff_40 (
    .J(switch_1_p2), .K(switch_1_p2), .clk(or_41_out), .Q(j_k_ff_40_q));  // open: Qn, preset, reset
  or or_41 (or_41_out, and_98_out, and_95_out, and_96_out);
  not not_7 (not_7_out, Set_alarm);
  nand nand_3 (nand_3_out, switch_1_p2, SetTime);
  and and_99 (and_99_out, SetTime, button_4_out);
  and and_100 (and_100_out, SetTime, button_5_out);
  and and_101 (and_101_out, SetTime, button_6_out);
  and and_102 (and_102_out, not_7_out, and_100_out);
  and and_103 (and_103_out, and_102_out, SetTime);
  Button button_4 (.out(button_4_out));
  Button button_5 (.out(button_5_out));
  Button button_6 (.out(button_6_out));
  // Switch switch_1: pin names not known; wires that end beside it: 1'b1, switch_1_p2
  Button button_7 (.out(button_7_out));

  // Notes on the sheet:
  //   Clock
  //   Hour 0-1
  //   Full Version
  //   Hour 0-9
  //   Minute 0-5
  //   Minute 0-9
  //   time
  //   on (red) = pm
  //   if alarm is off => no alarm
  //   off (black) = am
  //   am/pm
  //   time
  //   alarm line
  //   Set minute
  //   Set hour
  //   Set am/pm
  //   alarm line
  //   Set minute
  //   Set hour
  //   Set am/pm
  //   alarm on/off
  //   a.m
  //   alarm line
  //   alarm
  //   clock mode
  //   alarm mode
  //   p.m
  //   Comparing 2 output value to light up the alarm
  //   clock line
  //   clock line
  //   Hour 0-1
  //   Minute 0-9
  //   Minute 0-5
  //   Hour 0-9
  //   Power on/off
  //   Reset Alarm
  //   m+
  //   hr+
  //   Set am/pm
endmodule

module newest_version (
  input  StopTimer,
  input  Set_alarm,
  input  in_3
);

  wire and_1_out, and_2_out, and_3_out, and_4_out, and_5_out, and_6_out, and_7_out, and_8_out, and_9_out,
       and_10_out, and_11_out, and_12_out, and_13_out, and_14_out, and_15_out, and_16_out, and_17_out,
       and_18_out, and_19_out, and_20_out, and_21_out, and_22_out, and_23_out, and_24_out, and_25_out,
       and_26_out, and_27_out, and_28_out, and_29_out, and_30_out, and_31_out, and_32_out, and_33_out,
       and_34_out, and_35_out, and_36_out, and_37_out, and_38_out, and_39_out, and_40_out, and_41_out,
       and_42_out, and_43_out, and_44_out, and_45_out, and_46_out, and_47_out, and_48_out, and_49_out,
       and_50_out, and_51_out, and_52_out, and_53_out, and_54_out, and_55_out, and_56_out, and_57_out,
       and_58_out, and_59_out, and_60_out, and_61_out, and_62_out, and_63_out, and_64_out, and_65_out,
       and_66_out, and_67_out, and_68_out, and_69_out, and_70_out, and_71_out, and_72_out, and_73_out,
       and_74_out, and_75_out, and_76_out, button_1_out, button_2_out, button_3_out, button_4_out,
       clock_1_out, d_ff_1_q, d_ff_2_q, d_ff_3_q, d_ff_4_q, d_ff_5_q, d_ff_6_q, d_ff_7_q, d_ff_8_q, d_ff_9_q,
       d_ff_10_q, d_ff_11_q, d_ff_12_q, d_ff_13_q, d_ff_14_q, d_ff_15_q, d_ff_16_q, d_ff_17_q, d_ff_18_q,
       d_ff_19_q, d_ff_20_q, d_ff_21_q, d_ff_22_q, d_ff_23_q, d_ff_24_q, d_ff_25_q, d_ff_26_q, d_ff_27_q,
       d_ff_28_q, d_ff_29_q, d_ff_30_q, j_k_ff_1_q, j_k_ff_2_q, j_k_ff_3_q, j_k_ff_4_q, j_k_ff_5_q,
       j_k_ff_6_q, j_k_ff_7_q, j_k_ff_8_q, j_k_ff_9_q, j_k_ff_10_q, j_k_ff_11_q, j_k_ff_12_q, j_k_ff_13_q,
       j_k_ff_13_qn, j_k_ff_14_q, j_k_ff_15_q, j_k_ff_16_q, j_k_ff_17_q, j_k_ff_18_q, j_k_ff_19_q,
       j_k_ff_20_q, j_k_ff_21_q, j_k_ff_22_q, j_k_ff_23_q, j_k_ff_24_q, j_k_ff_25_q, j_k_ff_26_q,
       j_k_ff_27_q, nand_1_out, nand_2_out, not_1_out, not_2_out, not_3_out, not_4_out, not_5_out, or_1_out,
       or_2_out, or_3_out, or_4_out, or_5_out, or_6_out, or_7_out, or_8_out, or_9_out, or_10_out, or_11_out,
       or_12_out, or_22_out, or_23_out, or_27_out, or_28_out, or_29_out, or_30_out, or_31_out, or_32_out,
       or_33_out, switch_1_p2, xnor_1_out, xnor_2_out, xnor_3_out, xnor_4_out, xnor_5_out, xnor_6_out,
       xnor_7_out, xnor_8_out, xnor_9_out, xnor_10_out, xnor_11_out, xnor_12_out, xnor_13_out;
  wire [0:0] or_15_out;
  wire [2:0] or_17_out;
  wire [3:0] or_19_out, or_26_out;

  and and_1 (and_1_out, and_2_out, j_k_ff_6_q);
  or or_1 (or_1_out, and_1_out, and_3_out);
  or or_2 (or_2_out, or_1_out, and_4_out);
  D_Flip_Flop d_ff_1 (.D(and_7_out), .clk(and_19_out), .Q(d_ff_1_q));  // open: Qn, preset, reset
  and and_2 (and_2_out, and_7_out, or_4_out);
  D_Flip_Flop d_ff_2 (.D(and_2_out), .clk(and_19_out), .Q(d_ff_2_q));  // open: Qn, preset, reset
  and and_3 (and_3_out, and_2_out, and_4_out);
  D_Flip_Flop d_ff_3 (.D(or_2_out), .clk(and_19_out), .Q(d_ff_3_q));  // open: Qn, preset, reset
  and and_4 (and_4_out, j_k_ff_12_q, j_k_ff_4_q);
  and and_5 (and_5_out, d_ff_3_q, nand_1_out);
  or or_3 (or_3_out, and_5_out, and_22_out);
  J_K_Flip_Flop j_k_ff_1 (
    .J(switch_1_p2), .K(switch_1_p2), .clk(and_19_out), .Q(j_k_ff_1_q), .reset(or_9_out));  // open: Qn, preset
  and and_6 (and_6_out, j_k_ff_3_q, j_k_ff_11_q);
  or or_4 (or_4_out, and_6_out, and_20_out);
  or or_5 (or_5_out, d_ff_2_q, and_20_out);
  J_K_Flip_Flop j_k_ff_2 (
    .J(and_4_out), .K(and_4_out), .clk(or_3_out), .Q(j_k_ff_2_q), .reset(or_6_out));  // open: Qn, preset
  and and_7 (and_7_out, j_k_ff_1_q, j_k_ff_10_q);
  J_K_Flip_Flop j_k_ff_3 (
    .J(and_7_out), .K(and_7_out), .clk(d_ff_1_q), .Q(j_k_ff_3_q), .reset(or_10_out));  // open: Qn, preset
  J_K_Flip_Flop j_k_ff_4 (
    .J(or_4_out), .K(or_4_out), .clk(or_5_out), .Q(j_k_ff_4_q), .reset(button_4_out));  // open: Qn, preset
  or or_6 (or_6_out, button_4_out, and_16_out);
  D_Flip_Flop #(.trigger("falling")) d_ff_4 (
    .D(j_k_ff_2_q), .clk(or_3_out), .Q(d_ff_4_q), .reset(button_4_out));  // open: Qn, preset
  D_Flip_Flop d_ff_5 (.D(j_k_ff_1_q), .clk(and_19_out), .Q(d_ff_5_q), .reset(button_4_out));  // open: Qn, preset
  D_Flip_Flop #(.trigger("falling")) d_ff_6 (
    .D(j_k_ff_4_q), .clk(or_5_out), .Q(d_ff_6_q), .reset(button_4_out));  // open: Qn, preset
  J_K_Flip_Flop j_k_ff_5 (
    .J(j_k_ff_1_q), .K(j_k_ff_1_q), .clk(and_19_out), .Q(j_k_ff_5_q), .reset(or_9_out));  // open: Qn, preset
  D_Flip_Flop #(.trigger("falling")) d_ff_7 (
    .D(j_k_ff_3_q), .clk(d_ff_1_q), .Q(d_ff_7_q), .reset(button_4_out));  // open: Qn, preset
  J_K_Flip_Flop j_k_ff_6 (
    .J(j_k_ff_4_q), .K(j_k_ff_4_q), .clk(or_5_out), .Q(j_k_ff_6_q), .reset(or_7_out));  // open: Qn, preset
  D_Flip_Flop d_ff_8 (.D(j_k_ff_5_q), .clk(and_19_out), .Q(d_ff_8_q), .reset(button_4_out));  // open: Qn, preset
  J_K_Flip_Flop j_k_ff_7 (
    .J(j_k_ff_3_q), .K(j_k_ff_3_q), .clk(d_ff_1_q), .Q(j_k_ff_7_q), .reset(or_10_out));  // open: Qn, preset
  and and_8 (and_8_out, j_k_ff_1_q, j_k_ff_5_q);
  J_K_Flip_Flop j_k_ff_8 (
    .J(and_8_out), .K(and_8_out), .clk(and_19_out), .Q(j_k_ff_8_q), .reset(or_9_out));  // open: Qn, preset
  and and_9 (and_9_out, j_k_ff_4_q, j_k_ff_6_q);
  J_K_Flip_Flop j_k_ff_9 (
    .J(and_9_out), .K(and_9_out), .clk(or_5_out), .Q(j_k_ff_9_q), .reset(or_7_out));  // open: Qn, preset
  D_Flip_Flop #(.trigger("falling")) d_ff_9 (
    .D(j_k_ff_6_q), .clk(or_5_out), .Q(d_ff_9_q), .reset(button_4_out));  // open: Qn, preset
  D_Flip_Flop #(.trigger("falling")) d_ff_10 (
    .D(j_k_ff_7_q), .clk(d_ff_1_q), .Q(d_ff_10_q), .reset(button_4_out));  // open: Qn, preset
  D_Flip_Flop d_ff_11 (.D(j_k_ff_8_q), .clk(and_19_out), .Q(d_ff_11_q), .reset(button_4_out));  // open: Qn, preset
  and and_10 (and_10_out, j_k_ff_3_q, j_k_ff_7_q);
  D_Flip_Flop #(.trigger("falling")) d_ff_12 (
    .D(j_k_ff_9_q), .clk(or_5_out), .Q(d_ff_12_q), .reset(button_4_out));  // open: Qn, preset
  and and_11 (and_11_out, and_8_out, j_k_ff_8_q);
  J_K_Flip_Flop j_k_ff_10 (
    .J(and_11_out), .K(and_11_out), .clk(and_19_out), .Q(j_k_ff_10_q), .reset(or_9_out));  // open: Qn, preset
  J_K_Flip_Flop j_k_ff_11 (
    .J(and_10_out), .K(and_10_out), .clk(d_ff_1_q), .Q(j_k_ff_11_q), .reset(or_10_out));  // open: Qn, preset
  and and_12 (and_12_out, and_9_out, j_k_ff_9_q);
  J_K_Flip_Flop j_k_ff_12 (
    .J(and_12_out), .K(and_12_out), .clk(or_5_out), .Q(j_k_ff_12_q), .reset(or_7_out));  // open: Qn, preset
  or or_7 (or_7_out, button_4_out, or_8_out);
  D_Flip_Flop #(.trigger("falling")) d_ff_13 (
    .D(j_k_ff_11_q), .clk(d_ff_1_q), .Q(d_ff_13_q), .reset(button_4_out));  // open: Qn, preset
  or or_8 (or_8_out, and_15_out, and_16_out);
  and and_13 (and_13_out, j_k_ff_10_q, j_k_ff_5_q);
  or or_9 (or_9_out, and_13_out, button_4_out);
  D_Flip_Flop d_ff_14 (.D(j_k_ff_10_q), .clk(and_19_out), .Q(d_ff_14_q), .reset(button_4_out));  // open: Qn, preset
  and and_14 (and_14_out, j_k_ff_11_q, j_k_ff_7_q);
  or or_10 (or_10_out, and_14_out, button_4_out);
  and and_15 (and_15_out, j_k_ff_12_q, j_k_ff_6_q);
  D_Flip_Flop #(.trigger("falling")) d_ff_15 (
    .D(j_k_ff_12_q), .clk(or_5_out), .Q(d_ff_15_q), .reset(button_4_out));  // open: Qn, preset
  and and_16 (and_16_out, and_9_out, j_k_ff_2_q);
  or or_11 (or_11_out, and_19_out, and_20_out, and_21_out);
  J_K_Flip_Flop j_k_ff_13 (
    .J(j_k_ff_13_qn), .K(j_k_ff_13_qn), .clk(or_11_out), .Q(j_k_ff_13_q), .Qn(j_k_ff_13_qn),
    .reset(button_4_out));  // open: preset
  and and_17 (and_17_out, j_k_ff_2_q, nand_1_out);
  or or_12 (or_12_out, and_21_out, and_18_out);
  and and_18 (and_18_out, d_ff_9_q, and_17_out);
  nand nand_1 (nand_1_out, switch_1_p2, Set_alarm);
  and and_19 (and_19_out, Set_alarm, button_1_out);
  and and_20 (and_20_out, Set_alarm, button_2_out);
  and and_21 (and_21_out, Set_alarm, button_3_out);
  and and_22 (and_22_out, and_20_out, Set_alarm);
  J_K_Flip_Flop j_k_ff_14 (
    .J(switch_1_p2), .K(switch_1_p2), .clk(or_12_out), .Q(j_k_ff_14_q));  // open: Qn, preset, reset
  Hex_Digit_Display hex_digit_display_1 (.value({{3{in_3}}, or_15_out[0]}));  // open: dp
  or or_13 (or_17_out[1], and_23_out, and_24_out);
  and and_23 (and_23_out, Set_alarm, d_ff_10_q);
  and and_24 (and_24_out, d_ff_25_q, not_2_out);
  or or_14 (or_19_out[2], and_25_out, and_26_out);
  and and_25 (and_25_out, Set_alarm, d_ff_12_q);
  and and_26 (and_26_out, d_ff_27_q, not_3_out);
  or or_15 (or_15_out[0], and_27_out, and_30_out);
  and and_27 (and_27_out, Set_alarm, d_ff_4_q);
  xnor xnor_1 (xnor_1_out, d_ff_4_q, d_ff_19_q);
  xnor xnor_2 (xnor_2_out, d_ff_15_q, d_ff_30_q);
  LED led_1 (.in(j_k_ff_13_q));
  not not_1 (not_1_out, or_30_out);
  LED led_2 (.in(not_1_out));
  Hex_Digit_Display hex_digit_display_2 (.value(or_19_out));  // open: dp
  Hex_Digit_Display hex_digit_display_3 (.value({in_3, or_17_out}));  // open: dp
  or or_16 (or_19_out[3], and_28_out, and_29_out);
  and and_28 (and_28_out, Set_alarm, d_ff_15_q);
  and and_29 (and_29_out, d_ff_30_q, not_3_out);
  and and_30 (and_30_out, d_ff_19_q, not_3_out);
  xnor xnor_3 (xnor_3_out, d_ff_12_q, d_ff_27_q);
  xnor xnor_4 (xnor_4_out, d_ff_9_q, d_ff_24_q);
  LED led_3 (.in(and_43_out));
  LED led_4 (.in(not_4_out));
  LED led_5 (.in(Set_alarm));
  LED led_6 (.in(or_30_out));
  Hex_Digit_Display hex_digit_display_4 (.value(or_26_out));  // open: dp
  or or_17 (or_17_out[0], and_31_out, and_32_out);
  and and_31 (and_31_out, Set_alarm, d_ff_7_q);
  and and_32 (and_32_out, d_ff_21_q, not_2_out);
  or or_18 (or_17_out[2], and_33_out, and_34_out);
  and and_33 (and_33_out, Set_alarm, d_ff_13_q);
  and and_34 (and_34_out, d_ff_28_q, not_2_out);
  not not_2 (not_2_out, Set_alarm);
  or or_19 (or_19_out[0], and_35_out, and_36_out);
  and and_35 (and_35_out, Set_alarm, d_ff_6_q);
  and and_36 (and_36_out, d_ff_22_q, not_3_out);
  or or_20 (or_19_out[1], and_37_out, and_38_out);
  and and_37 (and_37_out, Set_alarm, d_ff_9_q);
  and and_38 (and_38_out, d_ff_24_q, not_3_out);
  not not_3 (not_3_out, Set_alarm);
  xnor xnor_5 (xnor_5_out, d_ff_7_q, d_ff_21_q);
  xnor xnor_6 (xnor_6_out, d_ff_6_q, d_ff_22_q);
  and and_39 (and_39_out, xnor_1_out, xnor_2_out, xnor_3_out, xnor_4_out, xnor_6_out, xnor_5_out, xnor_7_out, xnor_8_out, xnor_9_out, xnor_10_out, xnor_11_out, xnor_12_out, xnor_13_out);
  or or_21 (or_26_out[3], and_40_out, and_41_out);
  and and_40 (and_40_out, Set_alarm, d_ff_14_q);
  and and_41 (and_41_out, d_ff_29_q, not_2_out);
  and and_42 (and_42_out, and_46_out, j_k_ff_20_q);
  or or_22 (or_22_out, and_42_out, and_47_out);
  or or_23 (or_23_out, or_22_out, and_52_out);
  xnor xnor_7 (xnor_7_out, d_ff_10_q, d_ff_25_q);
  xnor xnor_8 (xnor_8_out, d_ff_13_q, d_ff_28_q);
  and and_43 (and_43_out, j_k_ff_13_q, and_39_out);
  not not_4 (not_4_out, Set_alarm);
  or or_24 (or_26_out[2], and_44_out, and_45_out);
  and and_44 (and_44_out, Set_alarm, d_ff_11_q);
  and and_45 (and_45_out, d_ff_26_q, not_2_out);
  D_Flip_Flop d_ff_16 (.D(and_54_out), .clk(and_66_out), .Q(d_ff_16_q));  // open: Qn, preset, reset
  and and_46 (and_46_out, and_54_out, or_28_out);
  D_Flip_Flop d_ff_17 (.D(and_46_out), .clk(and_66_out), .Q(d_ff_17_q));  // open: Qn, preset, reset
  and and_47 (and_47_out, and_46_out, and_52_out);
  D_Flip_Flop d_ff_18 (.D(or_23_out), .clk(and_66_out), .Q(d_ff_18_q));  // open: Qn, preset, reset
  xnor xnor_9 (xnor_9_out, d_ff_5_q, d_ff_20_q);
  xnor xnor_10 (xnor_10_out, d_ff_8_q, d_ff_23_q);
  or or_25 (or_26_out[1], and_48_out, and_49_out);
  and and_48 (and_48_out, Set_alarm, d_ff_8_q);
  and and_49 (and_49_out, d_ff_23_q, not_2_out);
  xnor xnor_11 (xnor_11_out, d_ff_11_q, d_ff_26_q);
  xnor xnor_12 (xnor_12_out, d_ff_14_q, d_ff_29_q);
  or or_26 (or_26_out[0], and_50_out, and_51_out);
  and and_50 (and_50_out, Set_alarm, d_ff_5_q);
  and and_51 (and_51_out, d_ff_20_q, not_2_out);
  and and_52 (and_52_out, j_k_ff_26_q, j_k_ff_17_q);
  J_K_Flip_Flop j_k_ff_15 (
    .J(and_52_out), .K(and_52_out), .clk(or_27_out), .Q(j_k_ff_15_q), .reset(and_67_out));  // open: Qn, preset
  and and_53 (and_53_out, d_ff_18_q, nand_2_out);
  or or_27 (or_27_out, and_53_out, and_76_out);
  xnor xnor_13 (xnor_13_out, j_k_ff_14_q, j_k_ff_27_q);
  J_K_Flip_Flop j_k_ff_16 (
    .J(switch_1_p2), .K(switch_1_p2), .clk(and_66_out), .Q(j_k_ff_16_q), .reset(and_63_out));  // open: Qn, preset
  and and_54 (and_54_out, j_k_ff_16_q, j_k_ff_24_q);
  and and_55 (and_55_out, j_k_ff_18_q, j_k_ff_25_q);
  or or_28 (or_28_out, and_55_out, and_75_out);
  J_K_Flip_Flop j_k_ff_17 (.J(or_28_out), .K(or_28_out), .clk(or_29_out), .Q(j_k_ff_17_q));  // open: Qn, preset, reset
  or or_29 (or_29_out, d_ff_17_q, and_75_out);
  D_Flip_Flop #(.trigger("falling")) d_ff_19 (
    .D(j_k_ff_15_q), .clk(or_27_out), .Q(d_ff_19_q));  // open: Qn, preset, reset
  D_Flip_Flop d_ff_20 (.D(j_k_ff_16_q), .clk(and_66_out), .Q(d_ff_20_q));  // open: Qn, preset, reset
  and and_56 (and_56_out, Set_alarm, j_k_ff_14_q);
  J_K_Flip_Flop j_k_ff_18 (
    .J(and_54_out), .K(and_54_out), .clk(d_ff_16_q), .Q(j_k_ff_18_q), .reset(and_64_out));  // open: Qn, preset
  or or_30 (or_30_out, and_56_out, and_57_out);
  and and_57 (and_57_out, j_k_ff_27_q, not_2_out);
  D_Flip_Flop #(.trigger("falling")) d_ff_21 (
    .D(j_k_ff_18_q), .clk(d_ff_16_q), .Q(d_ff_21_q));  // open: Qn, preset, reset
  D_Flip_Flop #(.trigger("falling")) d_ff_22 (
    .D(j_k_ff_17_q), .clk(or_29_out), .Q(d_ff_22_q));  // open: Qn, preset, reset
  J_K_Flip_Flop j_k_ff_19 (
    .J(j_k_ff_16_q), .K(j_k_ff_16_q), .clk(and_66_out), .Q(j_k_ff_19_q), .reset(and_63_out));  // open: Qn, preset
  J_K_Flip_Flop j_k_ff_20 (
    .J(j_k_ff_17_q), .K(j_k_ff_17_q), .clk(or_29_out), .Q(j_k_ff_20_q), .reset(or_31_out));  // open: Qn, preset
  D_Flip_Flop d_ff_23 (.D(j_k_ff_19_q), .clk(and_66_out), .Q(d_ff_23_q));  // open: Qn, preset, reset
  J_K_Flip_Flop j_k_ff_21 (
    .J(j_k_ff_18_q), .K(j_k_ff_18_q), .clk(d_ff_16_q), .Q(j_k_ff_21_q), .reset(and_64_out));  // open: Qn, preset
  D_Flip_Flop #(.trigger("falling")) d_ff_24 (
    .D(j_k_ff_20_q), .clk(or_29_out), .Q(d_ff_24_q));  // open: Qn, preset, reset
  and and_58 (and_58_out, j_k_ff_16_q, j_k_ff_19_q);
  J_K_Flip_Flop j_k_ff_22 (
    .J(and_58_out), .K(and_58_out), .clk(and_66_out), .Q(j_k_ff_22_q), .reset(and_63_out));  // open: Qn, preset
  and and_59 (and_59_out, j_k_ff_17_q, j_k_ff_20_q);
  J_K_Flip_Flop j_k_ff_23 (
    .J(and_59_out), .K(and_59_out), .clk(or_29_out), .Q(j_k_ff_23_q), .reset(or_31_out));  // open: Qn, preset
  and and_60 (and_60_out, j_k_ff_18_q, j_k_ff_21_q);
  D_Flip_Flop #(.trigger("falling")) d_ff_25 (
    .D(j_k_ff_21_q), .clk(d_ff_16_q), .Q(d_ff_25_q));  // open: Qn, preset, reset
  D_Flip_Flop d_ff_26 (.D(j_k_ff_22_q), .clk(and_66_out), .Q(d_ff_26_q));  // open: Qn, preset, reset
  D_Flip_Flop #(.trigger("falling")) d_ff_27 (
    .D(j_k_ff_23_q), .clk(or_29_out), .Q(d_ff_27_q));  // open: Qn, preset, reset
  and and_61 (and_61_out, and_58_out, j_k_ff_22_q);
  J_K_Flip_Flop j_k_ff_24 (
    .J(and_61_out), .K(and_61_out), .clk(and_66_out), .Q(j_k_ff_24_q), .reset(and_63_out));  // open: Qn, preset
  J_K_Flip_Flop j_k_ff_25 (
    .J(and_60_out), .K(and_60_out), .clk(d_ff_16_q), .Q(j_k_ff_25_q), .reset(and_64_out));  // open: Qn, preset
  and and_62 (and_62_out, and_59_out, j_k_ff_23_q);
  J_K_Flip_Flop j_k_ff_26 (
    .J(and_62_out), .K(and_62_out), .clk(or_29_out), .Q(j_k_ff_26_q), .reset(or_31_out));  // open: Qn, preset
  and and_63 (and_63_out, j_k_ff_24_q, j_k_ff_19_q);
  and and_64 (and_64_out, j_k_ff_25_q, j_k_ff_21_q);
  D_Flip_Flop #(.trigger("falling")) d_ff_28 (
    .D(j_k_ff_25_q), .clk(d_ff_16_q), .Q(d_ff_28_q));  // open: Qn, preset, reset
  or or_31 (or_31_out, and_65_out, and_67_out);
  D_Flip_Flop d_ff_29 (.D(j_k_ff_24_q), .clk(and_66_out), .Q(d_ff_29_q));  // open: Qn, preset, reset
  and and_65 (and_65_out, j_k_ff_26_q, j_k_ff_20_q);
  D_Flip_Flop #(.trigger("falling")) d_ff_30 (
    .D(j_k_ff_26_q), .clk(or_29_out), .Q(d_ff_30_q));  // open: Qn, preset, reset
  and and_66 (and_66_out, not_5_out, or_32_out);
  or or_32 (or_32_out, and_68_out, and_72_out);
  and and_67 (and_67_out, and_59_out, j_k_ff_15_q);
  and and_68 (and_68_out, clock_1_out, nand_2_out);
  and and_69 (and_69_out, d_ff_24_q, and_70_out);
  and and_70 (and_70_out, j_k_ff_15_q, nand_2_out);
  Clock clock_1 (.out(clock_1_out));
  and and_71 (and_71_out, not_5_out, and_74_out);
  J_K_Flip_Flop j_k_ff_27 (
    .J(switch_1_p2), .K(switch_1_p2), .clk(or_33_out), .Q(j_k_ff_27_q));  // open: Qn, preset, reset
  or or_33 (or_33_out, and_71_out, and_69_out);
  not not_5 (not_5_out, Set_alarm);
  nand nand_2 (nand_2_out, switch_1_p2, StopTimer);
  and and_72 (and_72_out, StopTimer, button_1_out);
  and and_73 (and_73_out, StopTimer, button_2_out);
  and and_74 (and_74_out, StopTimer, button_3_out);
  and and_75 (and_75_out, not_5_out, and_73_out);
  and and_76 (and_76_out, and_75_out, StopTimer);
  Button button_1 (.out(button_1_out));
  Button button_2 (.out(button_2_out));
  Button button_3 (.out(button_3_out));
  // Switch switch_1: pin names not known; wires that end beside it: 1'b1, switch_1_p2
  Button button_4 (.out(button_4_out));

  // Notes on the sheet:
  //   time
  //   alarm line
  //   alarm line
  //   Set minute
  //   Set hour
  //   Set am/pm
  //   alarm on/off
  //   a.m
  //   alarm line
  //   alarm
  //   clock mode
  //   alarm mode
  //   p.m
  //   clock line
  //   clock line
  //   Power on/off
  //   Reset Alarm
  //   Set minute
  //   Set hour
  //   Set am/pm
endmodule

module Test (
  input  in_1,
  input  in_2,
  input  in_3,
  input  in_4
);

  wire and_1_out, and_2_out, and_3_out, and_4_out, and_5_out, and_6_out, and_7_out, and_8_out, and_9_out,
       and_10_out, and_11_out, and_12_out, and_13_out, and_14_out, and_15_out, and_16_out, and_17_out,
       and_18_out, and_19_out, button_1_out, button_2_out, button_3_out, clock_1_out, d_ff_1_q, d_ff_2_q,
       d_ff_3_q, j_k_ff_1_q, j_k_ff_2_q, j_k_ff_3_q, j_k_ff_4_q, j_k_ff_5_q, j_k_ff_6_q, j_k_ff_7_q,
       j_k_ff_8_q, j_k_ff_9_q, j_k_ff_10_q, j_k_ff_11_q, j_k_ff_12_q, j_k_ff_13_q, j_k_ff_14_qn, not_1_out,
       or_1_out, or_2_out, or_3_out, or_4_out, or_5_out, or_6_out, or_7_out, or_8_out, or_9_out, or_10_out,
       or_12_out;
  wire [2:0] d_ff_6_q, d_ff_7_q;
  wire [3:0] d_ff_4_q, d_ff_5_q;

  or or_1 (or_1_out, or_3_out, and_19_out);
  and and_1 (and_1_out, and_3_out, or_7_out);
  or or_2 (or_2_out, and_2_out, and_19_out);
  or or_3 (or_3_out, or_10_out, and_19_out);
  or or_4 (or_4_out, or_1_out, and_19_out);
  and and_2 (and_2_out, and_1_out, or_6_out);
  D_Flip_Flop d_ff_1 (.D(or_2_out), .clk(or_4_out), .Q(d_ff_1_q));  // open: Qn, preset, reset
  D_Flip_Flop d_ff_2 (.D(or_8_out), .clk(or_3_out), .Q(d_ff_2_q));  // open: Qn, preset, reset
  and and_3 (and_3_out, or_8_out, or_7_out);
  D_Flip_Flop d_ff_3 (.D(and_3_out), .clk(or_4_out), .Q(d_ff_3_q));  // open: Qn, preset, reset
  or or_5 (or_5_out, d_ff_3_q, and_19_out);
  and and_4 (and_4_out, j_k_ff_13_q, j_k_ff_3_q);
  J_K_Flip_Flop j_k_ff_1 (.J(in_1), .K(in_1), .clk(or_10_out), .Q(j_k_ff_1_q), .reset(and_12_out));  // open: Qn, preset
  and and_5 (and_5_out, j_k_ff_2_q, j_k_ff_12_q);
  or or_6 (or_6_out, and_4_out, and_19_out);
  and and_6 (and_6_out, j_k_ff_1_q, j_k_ff_11_q);
  J_K_Flip_Flop j_k_ff_2 (
    .J(or_8_out), .K(or_8_out), .clk(d_ff_2_q), .Q(j_k_ff_2_q), .reset(and_13_out));  // open: Qn, preset
  or or_7 (or_7_out, and_5_out, and_19_out);
  J_K_Flip_Flop j_k_ff_3 (.J(or_7_out), .K(or_7_out), .clk(or_5_out), .Q(j_k_ff_3_q));  // open: Qn, preset, reset
  J_K_Flip_Flop j_k_ff_4 (
    .J(d_ff_1_q), .K(d_ff_1_q), .clk(d_ff_1_q), .Q(j_k_ff_4_q), .reset(and_15_out));  // open: Qn, preset
  D_Flip_Flop d_ff_4 (.D(j_k_ff_1_q), .clk(or_10_out), .Q(d_ff_4_q[0]));  // open: Qn, preset, reset
  or or_8 (or_8_out, and_6_out, and_19_out);
  D_Flip_Flop #(.trigger("falling")) d_ff_5 (
    .D(j_k_ff_3_q), .clk(or_5_out), .Q(d_ff_5_q[0]));  // open: Qn, preset, reset
  D_Flip_Flop #(.trigger("falling")) d_ff_6 (
    .D(j_k_ff_4_q), .clk(d_ff_1_q), .Q(d_ff_6_q[0]), .reset(and_15_out));  // open: Qn, preset
  J_K_Flip_Flop j_k_ff_5 (
    .J(j_k_ff_1_q), .K(j_k_ff_1_q), .clk(or_10_out), .Q(j_k_ff_5_q), .reset(and_12_out));  // open: Qn, preset
  D_Flip_Flop #(.trigger("falling")) d_ff_7 (
    .D(j_k_ff_2_q), .clk(d_ff_2_q), .Q(d_ff_7_q[0]));  // open: Qn, preset, reset
  J_K_Flip_Flop j_k_ff_6 (
    .J(j_k_ff_3_q), .K(j_k_ff_3_q), .clk(or_5_out), .Q(j_k_ff_6_q), .reset(or_9_out));  // open: Qn, preset
  D_Flip_Flop d_ff_8 (.D(j_k_ff_5_q), .clk(or_10_out), .Q(d_ff_4_q[1]));  // open: Qn, preset, reset
  J_K_Flip_Flop j_k_ff_7 (
    .J(j_k_ff_2_q), .K(j_k_ff_2_q), .clk(d_ff_2_q), .Q(j_k_ff_7_q), .reset(and_13_out));  // open: Qn, preset
  J_K_Flip_Flop j_k_ff_8 (
    .J(j_k_ff_4_q), .K(j_k_ff_4_q), .clk(d_ff_1_q), .Q(j_k_ff_8_q), .reset(and_15_out));  // open: Qn, preset
  and and_7 (and_7_out, j_k_ff_1_q, j_k_ff_5_q);
  J_K_Flip_Flop j_k_ff_9 (
    .J(and_7_out), .K(and_7_out), .clk(or_10_out), .Q(j_k_ff_9_q), .reset(and_12_out));  // open: Qn, preset
  and and_8 (and_8_out, j_k_ff_3_q, j_k_ff_6_q);
  D_Flip_Flop #(.trigger("falling")) d_ff_9 (
    .D(j_k_ff_6_q), .clk(or_5_out), .Q(d_ff_5_q[1]));  // open: Qn, preset, reset
  D_Flip_Flop #(.trigger("falling")) d_ff_10 (
    .D(j_k_ff_8_q), .clk(d_ff_1_q), .Q(d_ff_6_q[2]));  // open: Qn, preset, reset
  D_Flip_Flop #(.trigger("falling")) d_ff_11 (
    .D(j_k_ff_7_q), .clk(d_ff_2_q), .Q(d_ff_7_q[1]));  // open: Qn, preset, reset
  J_K_Flip_Flop j_k_ff_10 (
    .J(and_8_out), .K(and_8_out), .clk(or_5_out), .Q(j_k_ff_10_q), .reset(or_9_out));  // open: Qn, preset
  D_Flip_Flop d_ff_12 (.D(j_k_ff_9_q), .clk(or_10_out), .Q(d_ff_4_q[2]));  // open: Qn, preset, reset
  and and_9 (and_9_out, j_k_ff_2_q, j_k_ff_7_q);
  and and_10 (and_10_out, and_7_out, j_k_ff_9_q);
  J_K_Flip_Flop j_k_ff_11 (
    .J(and_10_out), .K(and_10_out), .clk(or_10_out), .Q(j_k_ff_11_q), .reset(and_12_out));  // open: Qn, preset
  J_K_Flip_Flop j_k_ff_12 (
    .J(and_9_out), .K(and_9_out), .clk(d_ff_2_q), .Q(j_k_ff_12_q), .reset(and_13_out));  // open: Qn, preset
  and and_11 (and_11_out, and_8_out, j_k_ff_10_q);
  J_K_Flip_Flop j_k_ff_13 (
    .J(and_11_out), .K(and_11_out), .clk(or_5_out), .Q(j_k_ff_13_q), .reset(or_9_out));  // open: Qn, preset
  D_Flip_Flop #(.trigger("falling")) d_ff_13 (
    .D(j_k_ff_10_q), .clk(or_5_out), .Q(d_ff_5_q[2]));  // open: Qn, preset, reset
  D_Flip_Flop #(.trigger("falling")) d_ff_14 (
    .D(j_k_ff_12_q), .clk(d_ff_2_q), .Q(d_ff_7_q[2]));  // open: Qn, preset, reset
  and and_12 (and_12_out, j_k_ff_11_q, j_k_ff_5_q);
  D_Flip_Flop d_ff_15 (.D(j_k_ff_11_q), .clk(or_10_out), .Q(d_ff_4_q[3]));  // open: Qn, preset, reset
  and and_13 (and_13_out, j_k_ff_12_q, j_k_ff_7_q);
  and and_14 (and_14_out, j_k_ff_13_q, j_k_ff_6_q);
  D_Flip_Flop #(.trigger("falling")) d_ff_16 (
    .D(j_k_ff_13_q), .clk(or_5_out), .Q(d_ff_5_q[3]));  // open: Qn, preset, reset
  or or_9 (or_9_out, and_14_out, and_15_out);
  Hex_Digit_Display hex_digit_display_1 (.value({in_4, {2{d_ff_6_q[2]}}, d_ff_6_q[0]}));  // open: dp
  or or_10 (or_10_out, and_16_out, and_17_out);
  // OR_Gate or_11 is placed but not wired
  Hex_Digit_Display hex_digit_display_2 (.value(d_ff_5_q));  // open: dp
  Hex_Digit_Display hex_digit_display_3 (.value({in_3, d_ff_7_q}));  // open: dp
  and and_15 (and_15_out, and_8_out, j_k_ff_4_q);
  and and_16 (and_16_out, clock_1_out, not_1_out);
  and and_17 (and_17_out, in_2, button_1_out);
  Hex_Digit_Display hex_digit_display_4 (.value(d_ff_4_q));  // open: dp
  LED led_1 (.in(j_k_ff_14_qn));
  Clock clock_1 (.out(clock_1_out));
  not not_1 (not_1_out, in_2);
  Button button_1 (.out(button_1_out));
  Button button_2 (.out(button_2_out));
  Button button_3 (.out(button_3_out));
  and and_18 (and_18_out, d_ff_5_q[1], j_k_ff_4_q);
  or or_12 (or_12_out, and_18_out, button_3_out);
  and and_19 (and_19_out, in_2, button_2_out);
  J_K_Flip_Flop j_k_ff_14 (.J(in_1), .K(in_1), .clk(or_12_out), .Qn(j_k_ff_14_qn));  // open: Q, preset, reset

  // Notes on the sheet:
  //   Set minute
  //   Set am/pm
endmodule

module Test2 (
  input  Power,
  input  StopTimer,
  input  in_3,
  input  in_4
);

  wire and_1_out, and_2_out, and_3_out, and_4_out, and_5_out, and_6_out, and_7_out, and_8_out, and_9_out,
       and_10_out, and_11_out, and_12_out, and_13_out, and_14_out, and_15_out, and_16_out, and_17_out,
       and_18_out, and_19_out, and_20_out, and_21_out, and_22_out, button_1_out, button_2_out, button_3_out,
       clock_1_out, d_ff_1_q, d_ff_2_q, d_ff_3_q, j_k_ff_1_q, j_k_ff_2_q, j_k_ff_3_q, j_k_ff_4_q, j_k_ff_5_q,
       j_k_ff_6_q, j_k_ff_7_q, j_k_ff_9_q, j_k_ff_10_q, j_k_ff_11_q, j_k_ff_12_q, j_k_ff_13_q, j_k_ff_14_qn,
       not_1_out, or_1_out, or_2_out, or_3_out, or_4_out, or_5_out, or_6_out;
  wire [0:0] d_ff_6_q;
  wire [2:0] d_ff_7_q;
  wire [3:0] d_ff_4_q, d_ff_5_q;

  and and_1 (and_1_out, and_3_out, or_2_out);
  or or_1 (or_1_out, d_ff_1_q, and_12_out);
  and and_2 (and_2_out, and_1_out, and_4_out);
  D_Flip_Flop d_ff_1 (.D(and_2_out), .clk(or_5_out), .Q(d_ff_1_q));  // open: Qn, preset, reset
  D_Flip_Flop d_ff_2 (.D(and_6_out), .clk(or_5_out), .Q(d_ff_2_q));  // open: Qn, preset, reset
  and and_3 (and_3_out, and_6_out, or_2_out);
  D_Flip_Flop d_ff_3 (.D(and_3_out), .clk(or_5_out), .Q(d_ff_3_q));  // open: Qn, preset, reset
  and and_4 (and_4_out, j_k_ff_13_q, j_k_ff_3_q);
  J_K_Flip_Flop j_k_ff_1 (
    .J(Power), .K(Power), .clk(or_5_out), .Q(j_k_ff_1_q), .reset(and_13_out));  // open: Qn, preset
  and and_5 (and_5_out, j_k_ff_2_q, j_k_ff_12_q);
  or or_2 (or_2_out, and_5_out, and_21_out);
  or or_3 (or_3_out, d_ff_3_q, and_21_out);
  and and_6 (and_6_out, j_k_ff_1_q, j_k_ff_11_q);
  J_K_Flip_Flop j_k_ff_2 (
    .J(and_6_out), .K(and_6_out), .clk(d_ff_2_q), .Q(j_k_ff_2_q), .reset(and_14_out));  // open: Qn, preset
  J_K_Flip_Flop j_k_ff_3 (.J(or_2_out), .K(or_2_out), .clk(or_3_out), .Q(j_k_ff_3_q));  // open: Qn, preset, reset
  J_K_Flip_Flop j_k_ff_4 (
    .J(or_1_out), .K(or_1_out), .clk(or_1_out), .Q(j_k_ff_4_q), .reset(and_16_out));  // open: Qn, preset
  D_Flip_Flop d_ff_4 (.D(j_k_ff_1_q), .clk(or_5_out), .Q(d_ff_4_q[0]));  // open: Qn, preset, reset
  D_Flip_Flop #(.trigger("falling")) d_ff_5 (
    .D(j_k_ff_3_q), .clk(or_3_out), .Q(d_ff_5_q[0]));  // open: Qn, preset, reset
  D_Flip_Flop #(.trigger("falling")) d_ff_6 (
    .D(j_k_ff_4_q), .clk(or_1_out), .Q(d_ff_6_q[0]), .reset(and_16_out));  // open: Qn, preset
  J_K_Flip_Flop j_k_ff_5 (
    .J(j_k_ff_1_q), .K(j_k_ff_1_q), .clk(or_5_out), .Q(j_k_ff_5_q), .reset(and_13_out));  // open: Qn, preset
  D_Flip_Flop #(.trigger("falling")) d_ff_7 (
    .D(j_k_ff_2_q), .clk(d_ff_2_q), .Q(d_ff_7_q[0]));  // open: Qn, preset, reset
  J_K_Flip_Flop j_k_ff_6 (
    .J(j_k_ff_3_q), .K(j_k_ff_3_q), .clk(or_3_out), .Q(j_k_ff_6_q), .reset(or_4_out));  // open: Qn, preset
  D_Flip_Flop d_ff_8 (.D(j_k_ff_5_q), .clk(or_5_out), .Q(d_ff_4_q[1]));  // open: Qn, preset, reset
  J_K_Flip_Flop j_k_ff_7 (
    .J(j_k_ff_2_q), .K(j_k_ff_2_q), .clk(d_ff_2_q), .Q(j_k_ff_7_q), .reset(and_14_out));  // open: Qn, preset
  J_K_Flip_Flop j_k_ff_8 (.J(j_k_ff_4_q), .K(j_k_ff_4_q), .clk(or_1_out));  // open: Q, Qn, preset, reset
  and and_7 (and_7_out, j_k_ff_1_q, j_k_ff_5_q);
  J_K_Flip_Flop j_k_ff_9 (
    .J(and_7_out), .K(and_7_out), .clk(or_5_out), .Q(j_k_ff_9_q), .reset(and_13_out));  // open: Qn, preset
  and and_8 (and_8_out, j_k_ff_3_q, j_k_ff_6_q);
  D_Flip_Flop #(.trigger("falling")) d_ff_9 (
    .D(j_k_ff_6_q), .clk(or_3_out), .Q(d_ff_5_q[1]));  // open: Qn, preset, reset
  D_Flip_Flop #(.trigger("falling")) d_ff_10 (
    .D(j_k_ff_7_q), .clk(d_ff_2_q), .Q(d_ff_7_q[1]));  // open: Qn, preset, reset
  J_K_Flip_Flop j_k_ff_10 (
    .J(and_8_out), .K(and_8_out), .clk(or_3_out), .Q(j_k_ff_10_q), .reset(or_4_out));  // open: Qn, preset
  D_Flip_Flop d_ff_11 (.D(j_k_ff_9_q), .clk(or_5_out), .Q(d_ff_4_q[2]));  // open: Qn, preset, reset
  and and_9 (and_9_out, j_k_ff_2_q, j_k_ff_7_q);
  and and_10 (and_10_out, and_7_out, j_k_ff_9_q);
  J_K_Flip_Flop j_k_ff_11 (
    .J(and_10_out), .K(and_10_out), .clk(or_5_out), .Q(j_k_ff_11_q), .reset(and_13_out));  // open: Qn, preset
  J_K_Flip_Flop j_k_ff_12 (
    .J(and_9_out), .K(and_9_out), .clk(d_ff_2_q), .Q(j_k_ff_12_q), .reset(and_14_out));  // open: Qn, preset
  and and_11 (and_11_out, and_8_out, j_k_ff_10_q);
  J_K_Flip_Flop j_k_ff_13 (
    .J(and_11_out), .K(and_11_out), .clk(or_3_out), .Q(j_k_ff_13_q), .reset(or_4_out));  // open: Qn, preset
  D_Flip_Flop #(.trigger("falling")) d_ff_12 (
    .D(j_k_ff_10_q), .clk(or_3_out), .Q(d_ff_5_q[2]));  // open: Qn, preset, reset
  D_Flip_Flop #(.trigger("falling")) d_ff_13 (
    .D(j_k_ff_12_q), .clk(d_ff_2_q), .Q(d_ff_7_q[2]));  // open: Qn, preset, reset
  and and_12 (and_12_out, j_k_ff_13_q, StopTimer);
  and and_13 (and_13_out, j_k_ff_11_q, j_k_ff_5_q);
  D_Flip_Flop d_ff_14 (.D(j_k_ff_11_q), .clk(or_5_out), .Q(d_ff_4_q[3]));  // open: Qn, preset, reset
  and and_14 (and_14_out, j_k_ff_12_q, j_k_ff_7_q);
  and and_15 (and_15_out, j_k_ff_13_q, j_k_ff_6_q);
  D_Flip_Flop #(.trigger("falling")) d_ff_15 (
    .D(j_k_ff_13_q), .clk(or_3_out), .Q(d_ff_5_q[3]));  // open: Qn, preset, reset
  or or_4 (or_4_out, and_15_out, and_16_out);
  or or_5 (or_5_out, and_17_out, and_18_out);
  Hex_Digit_Display hex_digit_display_1 (.value({{3{in_4}}, d_ff_6_q[0]}));  // open: dp
  Hex_Digit_Display hex_digit_display_2 (.value(d_ff_5_q));  // open: dp
  Hex_Digit_Display hex_digit_display_3 (.value({in_3, d_ff_7_q}));  // open: dp
  and and_16 (and_16_out, and_8_out, j_k_ff_4_q);
  and and_17 (and_17_out, clock_1_out, not_1_out);
  and and_18 (and_18_out, StopTimer, button_1_out);
  Hex_Digit_Display hex_digit_display_4 (.value(d_ff_4_q));  // open: dp
  LED led_1 (.in(j_k_ff_14_qn));
  and and_19 (and_19_out, d_ff_5_q[1], and_20_out);
  and and_20 (and_20_out, j_k_ff_4_q, not_1_out);
  Clock clock_1 (.out(clock_1_out));
  not not_1 (not_1_out, StopTimer);
  Button button_1 (.out(button_1_out));
  Button button_2 (.out(button_2_out));
  Button button_3 (.out(button_3_out));
  J_K_Flip_Flop j_k_ff_14 (.J(Power), .K(Power), .clk(or_6_out), .Qn(j_k_ff_14_qn));  // open: Q, preset, reset
  or or_6 (or_6_out, and_19_out, and_22_out);
  and and_21 (and_21_out, StopTimer, button_2_out);
  and and_22 (and_22_out, StopTimer, button_3_out);

  // Notes on the sheet:
  //   Time
  //   am/pm
  //   Set minute
  //   Set hour
  //   Set am/pm
endmodule

module Test3 (
  input  Power,
  input  StopTimer,
  input  in_3,
  input  in_4
);

  wire and_1_out, and_2_out, and_3_out, and_4_out, and_5_out, and_6_out, and_7_out, and_8_out, and_9_out,
       and_10_out, and_11_out, and_12_out, and_13_out, and_14_out, and_15_out, and_16_out, and_17_out,
       and_18_out, and_19_out, and_20_out, and_21_out, and_22_out, and_23_out, and_24_out, button_1_out,
       button_2_out, button_3_out, clock_1_out, d_ff_1_q, d_ff_2_q, d_ff_3_q, j_k_ff_1_q, j_k_ff_2_q,
       j_k_ff_3_q, j_k_ff_4_q, j_k_ff_5_q, j_k_ff_6_q, j_k_ff_7_q, j_k_ff_8_q, j_k_ff_9_q, j_k_ff_10_q,
       j_k_ff_11_q, j_k_ff_12_q, j_k_ff_13_qn, nand_1_out, or_1_out, or_2_out, or_3_out, or_4_out, or_5_out,
       or_6_out, or_7_out, or_8_out;
  wire [0:0] d_ff_6_q;
  wire [2:0] d_ff_7_q;
  wire [3:0] d_ff_4_q, d_ff_5_q;

  and and_1 (and_1_out, and_4_out, j_k_ff_6_q);
  or or_1 (or_1_out, and_1_out, and_2_out);
  D_Flip_Flop d_ff_1 (.D(and_4_out), .clk(or_7_out), .Q(d_ff_1_q));  // open: Qn, preset, reset
  and and_2 (and_2_out, and_4_out, and_5_out);
  or or_2 (or_2_out, or_1_out, and_5_out);
  D_Flip_Flop d_ff_2 (.D(or_2_out), .clk(or_7_out), .Q(d_ff_2_q));  // open: Qn, preset, reset
  and and_3 (and_3_out, d_ff_2_q, nand_1_out);
  D_Flip_Flop d_ff_3 (.D(and_8_out), .clk(or_7_out), .Q(d_ff_3_q));  // open: Qn, preset, reset
  and and_4 (and_4_out, and_8_out, or_4_out);
  and and_5 (and_5_out, j_k_ff_12_q, j_k_ff_3_q);
  or or_3 (or_3_out, and_3_out, and_14_out);
  J_K_Flip_Flop j_k_ff_1 (
    .J(Power), .K(Power), .clk(or_7_out), .Q(j_k_ff_1_q), .reset(and_15_out));  // open: Qn, preset
  and and_6 (and_6_out, j_k_ff_2_q, j_k_ff_11_q);
  or or_4 (or_4_out, and_6_out, and_23_out);
  and and_7 (and_7_out, nand_1_out, d_ff_1_q);
  or or_5 (or_5_out, and_7_out, and_23_out);
  and and_8 (and_8_out, j_k_ff_1_q, j_k_ff_10_q);
  J_K_Flip_Flop j_k_ff_2 (
    .J(and_8_out), .K(and_8_out), .clk(d_ff_3_q), .Q(j_k_ff_2_q), .reset(and_16_out));  // open: Qn, preset
  J_K_Flip_Flop j_k_ff_3 (.J(or_4_out), .K(or_4_out), .clk(or_5_out), .Q(j_k_ff_3_q));  // open: Qn, preset, reset
  J_K_Flip_Flop j_k_ff_4 (
    .J(and_5_out), .K(and_5_out), .clk(or_3_out), .Q(j_k_ff_4_q), .reset(and_18_out));  // open: Qn, preset
  D_Flip_Flop d_ff_4 (.D(j_k_ff_1_q), .clk(or_7_out), .Q(d_ff_4_q[0]));  // open: Qn, preset, reset
  D_Flip_Flop #(.trigger("falling")) d_ff_5 (
    .D(j_k_ff_3_q), .clk(or_5_out), .Q(d_ff_5_q[0]));  // open: Qn, preset, reset
  D_Flip_Flop #(.trigger("falling")) d_ff_6 (
    .D(j_k_ff_4_q), .clk(or_3_out), .Q(d_ff_6_q[0]));  // open: Qn, preset, reset
  J_K_Flip_Flop j_k_ff_5 (
    .J(j_k_ff_1_q), .K(j_k_ff_1_q), .clk(or_7_out), .Q(j_k_ff_5_q), .reset(and_15_out));  // open: Qn, preset
  D_Flip_Flop #(.trigger("falling")) d_ff_7 (
    .D(j_k_ff_2_q), .clk(d_ff_3_q), .Q(d_ff_7_q[0]));  // open: Qn, preset, reset
  J_K_Flip_Flop j_k_ff_6 (
    .J(j_k_ff_3_q), .K(j_k_ff_3_q), .clk(or_5_out), .Q(j_k_ff_6_q), .reset(or_6_out));  // open: Qn, preset
  D_Flip_Flop d_ff_8 (.D(j_k_ff_5_q), .clk(or_7_out), .Q(d_ff_4_q[1]));  // open: Qn, preset, reset
  J_K_Flip_Flop j_k_ff_7 (
    .J(j_k_ff_2_q), .K(j_k_ff_2_q), .clk(d_ff_3_q), .Q(j_k_ff_7_q), .reset(and_16_out));  // open: Qn, preset
  and and_9 (and_9_out, j_k_ff_1_q, j_k_ff_5_q);
  J_K_Flip_Flop j_k_ff_8 (
    .J(and_9_out), .K(and_9_out), .clk(or_7_out), .Q(j_k_ff_8_q), .reset(and_15_out));  // open: Qn, preset
  and and_10 (and_10_out, j_k_ff_3_q, j_k_ff_6_q);
  D_Flip_Flop #(.trigger("falling")) d_ff_9 (
    .D(j_k_ff_6_q), .clk(or_5_out), .Q(d_ff_5_q[1]));  // open: Qn, preset, reset
  D_Flip_Flop #(.trigger("falling")) d_ff_10 (
    .D(j_k_ff_7_q), .clk(d_ff_3_q), .Q(d_ff_7_q[1]));  // open: Qn, preset, reset
  J_K_Flip_Flop j_k_ff_9 (
    .J(and_10_out), .K(and_10_out), .clk(or_5_out), .Q(j_k_ff_9_q), .reset(or_6_out));  // open: Qn, preset
  D_Flip_Flop d_ff_11 (.D(j_k_ff_8_q), .clk(or_7_out), .Q(d_ff_4_q[2]));  // open: Qn, preset, reset
  and and_11 (and_11_out, j_k_ff_2_q, j_k_ff_7_q);
  and and_12 (and_12_out, and_9_out, j_k_ff_8_q);
  J_K_Flip_Flop j_k_ff_10 (
    .J(and_12_out), .K(and_12_out), .clk(or_7_out), .Q(j_k_ff_10_q), .reset(and_15_out));  // open: Qn, preset
  J_K_Flip_Flop j_k_ff_11 (
    .J(and_11_out), .K(and_11_out), .clk(d_ff_3_q), .Q(j_k_ff_11_q), .reset(and_16_out));  // open: Qn, preset
  and and_13 (and_13_out, and_10_out, j_k_ff_9_q);
  J_K_Flip_Flop j_k_ff_12 (
    .J(and_13_out), .K(and_13_out), .clk(or_5_out), .Q(j_k_ff_12_q), .reset(or_6_out));  // open: Qn, preset
  D_Flip_Flop #(.trigger("falling")) d_ff_12 (
    .D(j_k_ff_9_q), .clk(or_5_out), .Q(d_ff_5_q[2]));  // open: Qn, preset, reset
  D_Flip_Flop #(.trigger("falling")) d_ff_13 (
    .D(j_k_ff_11_q), .clk(d_ff_3_q), .Q(d_ff_7_q[2]));  // open: Qn, preset, reset
  and and_14 (and_14_out, and_23_out, StopTimer);
  and and_15 (and_15_out, j_k_ff_10_q, j_k_ff_5_q);
  D_Flip_Flop d_ff_14 (.D(j_k_ff_10_q), .clk(or_7_out), .Q(d_ff_4_q[3]));  // open: Qn, preset, reset
  and and_16 (and_16_out, j_k_ff_11_q, j_k_ff_7_q);
  and and_17 (and_17_out, j_k_ff_12_q, j_k_ff_6_q);
  D_Flip_Flop #(.trigger("falling")) d_ff_15 (
    .D(j_k_ff_12_q), .clk(or_5_out), .Q(d_ff_5_q[3]));  // open: Qn, preset, reset
  or or_6 (or_6_out, and_17_out, and_18_out);
  or or_7 (or_7_out, and_19_out, and_20_out);
  Hex_Digit_Display hex_digit_display_1 (.value({{3{in_4}}, d_ff_6_q[0]}));  // open: dp
  Hex_Digit_Display hex_digit_display_2 (.value(d_ff_5_q));  // open: dp
  Hex_Digit_Display hex_digit_display_3 (.value({in_3, d_ff_7_q}));  // open: dp
  and and_18 (and_18_out, and_10_out, j_k_ff_4_q);
  and and_19 (and_19_out, clock_1_out, nand_1_out);
  and and_20 (and_20_out, StopTimer, button_1_out);
  Hex_Digit_Display hex_digit_display_4 (.value(d_ff_4_q));  // open: dp
  LED led_1 (.in(j_k_ff_13_qn));
  and and_21 (and_21_out, d_ff_5_q[1], and_22_out);
  and and_22 (and_22_out, j_k_ff_4_q, nand_1_out);
  Clock clock_1 (.out(clock_1_out));
  nand nand_1 (nand_1_out, Power, StopTimer);
  Button button_1 (.out(button_1_out));
  Button button_2 (.out(button_2_out));
  Button button_3 (.out(button_3_out));
  J_K_Flip_Flop j_k_ff_13 (.J(Power), .K(Power), .clk(or_8_out), .Qn(j_k_ff_13_qn));  // open: Q, preset, reset
  or or_8 (or_8_out, and_21_out, and_24_out);
  and and_23 (and_23_out, StopTimer, button_2_out);
  and and_24 (and_24_out, StopTimer, button_3_out);

  // Notes on the sheet:
  //   Current Version
  //   Time
  //   am/pm
  //   Set minute
  //   Set hour
  //   Set am/pm
endmodule

module Test4 (
  input  Power,
  input  StopTimer,
  input  in_3,
  input  in_4
);

  wire and_1_out, and_2_out, and_3_out, and_4_out, and_5_out, and_6_out, and_7_out, and_8_out, and_9_out,
       and_10_out, and_11_out, and_12_out, and_13_out, and_14_out, and_15_out, and_16_out, and_17_out,
       and_18_out, and_19_out, and_20_out, and_21_out, and_22_out, and_23_out, button_1_out, button_2_out,
       button_3_out, clock_1_out, d_ff_1_q, d_ff_2_q, d_ff_3_q, j_k_ff_1_q, j_k_ff_2_q, j_k_ff_3_q,
       j_k_ff_4_q, j_k_ff_5_q, j_k_ff_6_q, j_k_ff_7_q, j_k_ff_8_q, j_k_ff_9_q, j_k_ff_10_q, j_k_ff_11_q,
       j_k_ff_12_q, j_k_ff_13_q, nand_1_out, or_1_out, or_2_out, or_3_out, or_4_out, or_5_out, or_6_out,
       or_7_out, or_8_out;
  wire [0:0] d_ff_6_q;
  wire [2:0] d_ff_7_q;
  wire [3:0] d_ff_4_q, d_ff_5_q;

  and and_1 (and_1_out, and_4_out, j_k_ff_6_q);
  or or_1 (or_1_out, and_1_out, and_2_out);
  D_Flip_Flop d_ff_1 (.D(and_4_out), .clk(or_7_out), .Q(d_ff_1_q));  // open: Qn, preset, reset
  and and_2 (and_2_out, and_4_out, and_5_out);
  or or_2 (or_2_out, or_1_out, and_5_out);
  D_Flip_Flop d_ff_2 (.D(or_2_out), .clk(or_7_out), .Q(d_ff_2_q));  // open: Qn, preset, reset
  and and_3 (and_3_out, d_ff_2_q, nand_1_out);
  D_Flip_Flop d_ff_3 (.D(and_7_out), .clk(or_7_out), .Q(d_ff_3_q));  // open: Qn, preset, reset
  and and_4 (and_4_out, and_7_out, or_4_out);
  and and_5 (and_5_out, j_k_ff_12_q, j_k_ff_3_q);
  or or_3 (or_3_out, and_3_out, and_13_out);
  J_K_Flip_Flop j_k_ff_1 (
    .J(Power), .K(Power), .clk(or_7_out), .Q(j_k_ff_1_q), .reset(and_14_out));  // open: Qn, preset
  and and_6 (and_6_out, j_k_ff_2_q, j_k_ff_11_q);
  or or_4 (or_4_out, and_6_out, and_22_out);
  or or_5 (or_5_out, d_ff_1_q, and_22_out);
  and and_7 (and_7_out, j_k_ff_1_q, j_k_ff_10_q);
  J_K_Flip_Flop j_k_ff_2 (
    .J(and_7_out), .K(and_7_out), .clk(d_ff_3_q), .Q(j_k_ff_2_q), .reset(and_15_out));  // open: Qn, preset
  J_K_Flip_Flop j_k_ff_3 (.J(or_4_out), .K(or_4_out), .clk(or_5_out), .Q(j_k_ff_3_q));  // open: Qn, preset, reset
  J_K_Flip_Flop j_k_ff_4 (
    .J(and_5_out), .K(and_5_out), .clk(or_3_out), .Q(j_k_ff_4_q), .reset(and_17_out));  // open: Qn, preset
  D_Flip_Flop d_ff_4 (.D(j_k_ff_1_q), .clk(or_7_out), .Q(d_ff_4_q[0]));  // open: Qn, preset, reset
  D_Flip_Flop #(.trigger("falling")) d_ff_5 (
    .D(j_k_ff_3_q), .clk(or_5_out), .Q(d_ff_5_q[0]));  // open: Qn, preset, reset
  D_Flip_Flop #(.trigger("falling")) d_ff_6 (
    .D(j_k_ff_4_q), .clk(or_3_out), .Q(d_ff_6_q[0]));  // open: Qn, preset, reset
  J_K_Flip_Flop j_k_ff_5 (
    .J(j_k_ff_1_q), .K(j_k_ff_1_q), .clk(or_7_out), .Q(j_k_ff_5_q), .reset(and_14_out));  // open: Qn, preset
  D_Flip_Flop #(.trigger("falling")) d_ff_7 (
    .D(j_k_ff_2_q), .clk(d_ff_3_q), .Q(d_ff_7_q[0]));  // open: Qn, preset, reset
  J_K_Flip_Flop j_k_ff_6 (
    .J(j_k_ff_3_q), .K(j_k_ff_3_q), .clk(or_5_out), .Q(j_k_ff_6_q), .reset(or_6_out));  // open: Qn, preset
  D_Flip_Flop d_ff_8 (.D(j_k_ff_5_q), .clk(or_7_out), .Q(d_ff_4_q[1]));  // open: Qn, preset, reset
  J_K_Flip_Flop j_k_ff_7 (
    .J(j_k_ff_2_q), .K(j_k_ff_2_q), .clk(d_ff_3_q), .Q(j_k_ff_7_q), .reset(and_15_out));  // open: Qn, preset
  and and_8 (and_8_out, j_k_ff_1_q, j_k_ff_5_q);
  J_K_Flip_Flop j_k_ff_8 (
    .J(and_8_out), .K(and_8_out), .clk(or_7_out), .Q(j_k_ff_8_q), .reset(and_14_out));  // open: Qn, preset
  and and_9 (and_9_out, j_k_ff_3_q, j_k_ff_6_q);
  D_Flip_Flop #(.trigger("falling")) d_ff_9 (
    .D(j_k_ff_6_q), .clk(or_5_out), .Q(d_ff_5_q[1]));  // open: Qn, preset, reset
  D_Flip_Flop #(.trigger("falling")) d_ff_10 (
    .D(j_k_ff_7_q), .clk(d_ff_3_q), .Q(d_ff_7_q[1]));  // open: Qn, preset, reset
  J_K_Flip_Flop j_k_ff_9 (
    .J(and_9_out), .K(and_9_out), .clk(or_5_out), .Q(j_k_ff_9_q), .reset(or_6_out));  // open: Qn, preset
  D_Flip_Flop d_ff_11 (.D(j_k_ff_8_q), .clk(or_7_out), .Q(d_ff_4_q[2]));  // open: Qn, preset, reset
  and and_10 (and_10_out, j_k_ff_2_q, j_k_ff_7_q);
  and and_11 (and_11_out, and_8_out, j_k_ff_8_q);
  J_K_Flip_Flop j_k_ff_10 (
    .J(and_11_out), .K(and_11_out), .clk(or_7_out), .Q(j_k_ff_10_q), .reset(and_14_out));  // open: Qn, preset
  J_K_Flip_Flop j_k_ff_11 (
    .J(and_10_out), .K(and_10_out), .clk(d_ff_3_q), .Q(j_k_ff_11_q), .reset(and_15_out));  // open: Qn, preset
  and and_12 (and_12_out, and_9_out, j_k_ff_9_q);
  J_K_Flip_Flop j_k_ff_12 (
    .J(and_12_out), .K(and_12_out), .clk(or_5_out), .Q(j_k_ff_12_q), .reset(or_6_out));  // open: Qn, preset
  D_Flip_Flop #(.trigger("falling")) d_ff_12 (
    .D(j_k_ff_9_q), .clk(or_5_out), .Q(d_ff_5_q[2]));  // open: Qn, preset, reset
  D_Flip_Flop #(.trigger("falling")) d_ff_13 (
    .D(j_k_ff_11_q), .clk(d_ff_3_q), .Q(d_ff_7_q[2]));  // open: Qn, preset, reset
  and and_13 (and_13_out, and_22_out, StopTimer);
  and and_14 (and_14_out, j_k_ff_10_q, j_k_ff_5_q);
  D_Flip_Flop d_ff_14 (.D(j_k_ff_10_q), .clk(or_7_out), .Q(d_ff_4_q[3]));  // open: Qn, preset, reset
  and and_15 (and_15_out, j_k_ff_11_q, j_k_ff_7_q);
  and and_16 (and_16_out, j_k_ff_12_q, j_k_ff_6_q);
  D_Flip_Flop #(.trigger("falling")) d_ff_15 (
    .D(j_k_ff_12_q), .clk(or_5_out), .Q(d_ff_5_q[3]));  // open: Qn, preset, reset
  or or_6 (or_6_out, and_16_out, and_17_out);
  or or_7 (or_7_out, and_18_out, and_19_out);
  Hex_Digit_Display hex_digit_display_1 (.value({{3{in_4}}, d_ff_6_q[0]}));  // open: dp
  Hex_Digit_Display hex_digit_display_2 (.value(d_ff_5_q));  // open: dp
  Hex_Digit_Display hex_digit_display_3 (.value({in_3, d_ff_7_q}));  // open: dp
  and and_17 (and_17_out, and_9_out, j_k_ff_4_q);
  and and_18 (and_18_out, clock_1_out, nand_1_out);
  and and_19 (and_19_out, StopTimer, button_1_out);
  Hex_Digit_Display hex_digit_display_4 (.value(d_ff_4_q));  // open: dp
  LED led_1 (.in(j_k_ff_13_q));
  and and_20 (and_20_out, d_ff_5_q[1], and_21_out);
  and and_21 (and_21_out, j_k_ff_4_q, nand_1_out);
  Clock clock_1 (.out(clock_1_out));
  nand nand_1 (nand_1_out, Power, StopTimer);
  Button button_1 (.out(button_1_out));
  Button button_2 (.out(button_2_out));
  Button button_3 (.out(button_3_out));
  J_K_Flip_Flop j_k_ff_13 (.J(Power), .K(Power), .clk(or_8_out), .Q(j_k_ff_13_q));  // open: Qn, preset, reset
  or or_8 (or_8_out, and_20_out, and_23_out);
  and and_22 (and_22_out, StopTimer, button_2_out);
  and and_23 (and_23_out, StopTimer, button_3_out);

  // Notes on the sheet:
  //   time
  //   off (black) = am
  //   on (red) = pm
  //   am/pm
  //   Set minute
  //   Set hour
  //   Set am/pm
endmodule

module testalarm1 (
  input  StopTimer,
  input  Set_alarm,
  input  in_3
);

  wire and_1_out, and_2_out, and_3_out, and_4_out, and_5_out, and_6_out, and_7_out, and_8_out, and_9_out,
       and_10_out, and_11_out, and_12_out, and_13_out, and_14_out, and_15_out, and_16_out, and_17_out,
       and_18_out, and_19_out, and_20_out, and_21_out, and_22_out, and_23_out, and_24_out, and_25_out,
       and_26_out, and_27_out, and_28_out, and_29_out, and_30_out, and_31_out, and_32_out, and_33_out,
       and_34_out, and_35_out, and_36_out, and_37_out, and_38_out, and_39_out, and_40_out, and_41_out,
       and_42_out, and_43_out, and_44_out, and_45_out, and_46_out, and_47_out, and_48_out, and_49_out,
       and_50_out, and_51_out, and_52_out, and_53_out, and_54_out, and_55_out, and_56_out, and_57_out,
       and_58_out, and_59_out, and_60_out, and_61_out, and_62_out, and_63_out, and_64_out, and_65_out,
       and_66_out, and_67_out, and_68_out, and_69_out, and_70_out, and_71_out, and_72_out, and_73_out,
       and_74_out, and_75_out, and_76_out, button_1_out, button_2_out, button_3_out, button_4_out,
       clock_1_out, d_ff_1_q, d_ff_2_q, d_ff_3_q, d_ff_4_q, d_ff_5_q, d_ff_6_q, d_ff_7_q, d_ff_8_q, d_ff_9_q,
       d_ff_10_q, d_ff_11_q, d_ff_12_q, d_ff_13_q, d_ff_14_q, d_ff_15_q, d_ff_16_q, d_ff_17_q, d_ff_18_q,
       d_ff_19_q, d_ff_20_q, d_ff_21_q, d_ff_22_q, d_ff_23_q, d_ff_24_q, d_ff_25_q, d_ff_26_q, d_ff_27_q,
       d_ff_28_q, d_ff_29_q, d_ff_30_q, j_k_ff_1_q, j_k_ff_2_q, j_k_ff_3_q, j_k_ff_4_q, j_k_ff_5_q,
       j_k_ff_6_q, j_k_ff_7_q, j_k_ff_8_q, j_k_ff_9_q, j_k_ff_10_q, j_k_ff_11_q, j_k_ff_12_q, j_k_ff_13_q,
       j_k_ff_13_qn, j_k_ff_14_q, j_k_ff_15_q, j_k_ff_16_q, j_k_ff_17_q, j_k_ff_18_q, j_k_ff_19_q,
       j_k_ff_20_q, j_k_ff_21_q, j_k_ff_22_q, j_k_ff_23_q, j_k_ff_24_q, j_k_ff_25_q, j_k_ff_26_q,
       j_k_ff_27_q, nand_1_out, nand_2_out, not_1_out, not_2_out, not_3_out, not_4_out, not_5_out, or_1_out,
       or_2_out, or_3_out, or_4_out, or_5_out, or_6_out, or_7_out, or_8_out, or_9_out, or_10_out, or_11_out,
       or_12_out, or_22_out, or_23_out, or_27_out, or_28_out, or_29_out, or_30_out, or_31_out, or_32_out,
       or_33_out, switch_1_p2, xnor_1_out, xnor_2_out, xnor_3_out, xnor_4_out, xnor_5_out, xnor_6_out,
       xnor_7_out, xnor_8_out, xnor_9_out, xnor_10_out, xnor_11_out, xnor_12_out, xnor_13_out;
  wire [0:0] or_15_out;
  wire [2:0] or_17_out;
  wire [3:0] or_19_out, or_26_out;

  and and_1 (and_1_out, and_2_out, j_k_ff_6_q);
  or or_1 (or_1_out, and_1_out, and_3_out);
  or or_2 (or_2_out, or_1_out, and_4_out);
  D_Flip_Flop d_ff_1 (.D(and_7_out), .clk(and_19_out), .Q(d_ff_1_q));  // open: Qn, preset, reset
  and and_2 (and_2_out, and_7_out, or_4_out);
  D_Flip_Flop d_ff_2 (.D(and_2_out), .clk(and_19_out), .Q(d_ff_2_q));  // open: Qn, preset, reset
  and and_3 (and_3_out, and_2_out, and_4_out);
  D_Flip_Flop d_ff_3 (.D(or_2_out), .clk(and_19_out), .Q(d_ff_3_q));  // open: Qn, preset, reset
  and and_4 (and_4_out, j_k_ff_12_q, j_k_ff_4_q);
  and and_5 (and_5_out, d_ff_3_q, nand_1_out);
  or or_3 (or_3_out, and_5_out, and_22_out);
  J_K_Flip_Flop j_k_ff_1 (
    .J(switch_1_p2), .K(switch_1_p2), .clk(and_19_out), .Q(j_k_ff_1_q), .reset(or_9_out));  // open: Qn, preset
  and and_6 (and_6_out, j_k_ff_3_q, j_k_ff_11_q);
  or or_4 (or_4_out, and_6_out, and_20_out);
  or or_5 (or_5_out, d_ff_2_q, and_20_out);
  J_K_Flip_Flop j_k_ff_2 (
    .J(and_4_out), .K(and_4_out), .clk(or_3_out), .Q(j_k_ff_2_q), .reset(or_6_out));  // open: Qn, preset
  and and_7 (and_7_out, j_k_ff_1_q, j_k_ff_10_q);
  J_K_Flip_Flop j_k_ff_3 (
    .J(and_7_out), .K(and_7_out), .clk(d_ff_1_q), .Q(j_k_ff_3_q), .reset(or_10_out));  // open: Qn, preset
  J_K_Flip_Flop j_k_ff_4 (
    .J(or_4_out), .K(or_4_out), .clk(or_5_out), .Q(j_k_ff_4_q), .reset(button_4_out));  // open: Qn, preset
  or or_6 (or_6_out, button_4_out, and_16_out);
  D_Flip_Flop #(.trigger("falling")) d_ff_4 (
    .D(j_k_ff_2_q), .clk(or_3_out), .Q(d_ff_4_q), .reset(button_4_out));  // open: Qn, preset
  D_Flip_Flop d_ff_5 (.D(j_k_ff_1_q), .clk(and_19_out), .Q(d_ff_5_q), .reset(button_4_out));  // open: Qn, preset
  D_Flip_Flop #(.trigger("falling")) d_ff_6 (
    .D(j_k_ff_4_q), .clk(or_5_out), .Q(d_ff_6_q), .reset(button_4_out));  // open: Qn, preset
  J_K_Flip_Flop j_k_ff_5 (
    .J(j_k_ff_1_q), .K(j_k_ff_1_q), .clk(and_19_out), .Q(j_k_ff_5_q), .reset(or_9_out));  // open: Qn, preset
  D_Flip_Flop #(.trigger("falling")) d_ff_7 (
    .D(j_k_ff_3_q), .clk(d_ff_1_q), .Q(d_ff_7_q), .reset(button_4_out));  // open: Qn, preset
  J_K_Flip_Flop j_k_ff_6 (
    .J(j_k_ff_4_q), .K(j_k_ff_4_q), .clk(or_5_out), .Q(j_k_ff_6_q), .reset(or_7_out));  // open: Qn, preset
  D_Flip_Flop d_ff_8 (.D(j_k_ff_5_q), .clk(and_19_out), .Q(d_ff_8_q), .reset(button_4_out));  // open: Qn, preset
  J_K_Flip_Flop j_k_ff_7 (
    .J(j_k_ff_3_q), .K(j_k_ff_3_q), .clk(d_ff_1_q), .Q(j_k_ff_7_q), .reset(or_10_out));  // open: Qn, preset
  and and_8 (and_8_out, j_k_ff_1_q, j_k_ff_5_q);
  J_K_Flip_Flop j_k_ff_8 (
    .J(and_8_out), .K(and_8_out), .clk(and_19_out), .Q(j_k_ff_8_q), .reset(or_9_out));  // open: Qn, preset
  and and_9 (and_9_out, j_k_ff_4_q, j_k_ff_6_q);
  J_K_Flip_Flop j_k_ff_9 (
    .J(and_9_out), .K(and_9_out), .clk(or_5_out), .Q(j_k_ff_9_q), .reset(or_7_out));  // open: Qn, preset
  D_Flip_Flop #(.trigger("falling")) d_ff_9 (
    .D(j_k_ff_6_q), .clk(or_5_out), .Q(d_ff_9_q), .reset(button_4_out));  // open: Qn, preset
  D_Flip_Flop #(.trigger("falling")) d_ff_10 (
    .D(j_k_ff_7_q), .clk(d_ff_1_q), .Q(d_ff_10_q), .reset(button_4_out));  // open: Qn, preset
  D_Flip_Flop d_ff_11 (.D(j_k_ff_8_q), .clk(and_19_out), .Q(d_ff_11_q), .reset(button_4_out));  // open: Qn, preset
  and and_10 (and_10_out, j_k_ff_3_q, j_k_ff_7_q);
  D_Flip_Flop #(.trigger("falling")) d_ff_12 (
    .D(j_k_ff_9_q), .clk(or_5_out), .Q(d_ff_12_q), .reset(button_4_out));  // open: Qn, preset
  and and_11 (and_11_out, and_8_out, j_k_ff_8_q);
  J_K_Flip_Flop j_k_ff_10 (
    .J(and_11_out), .K(and_11_out), .clk(and_19_out), .Q(j_k_ff_10_q), .reset(or_9_out));  // open: Qn, preset
  J_K_Flip_Flop j_k_ff_11 (
    .J(and_10_out), .K(and_10_out), .clk(d_ff_1_q), .Q(j_k_ff_11_q), .reset(or_10_out));  // open: Qn, preset
  and and_12 (and_12_out, and_9_out, j_k_ff_9_q);
  J_K_Flip_Flop j_k_ff_12 (
    .J(and_12_out), .K(and_12_out), .clk(or_5_out), .Q(j_k_ff_12_q), .reset(or_7_out));  // open: Qn, preset
  or or_7 (or_7_out, button_4_out, or_8_out);
  D_Flip_Flop #(.trigger("falling")) d_ff_13 (
    .D(j_k_ff_11_q), .clk(d_ff_1_q), .Q(d_ff_13_q), .reset(button_4_out));  // open: Qn, preset
  or or_8 (or_8_out, and_15_out, and_16_out);
  and and_13 (and_13_out, j_k_ff_10_q, j_k_ff_5_q);
  or or_9 (or_9_out, and_13_out, button_4_out);
  D_Flip_Flop d_ff_14 (.D(j_k_ff_10_q), .clk(and_19_out), .Q(d_ff_14_q), .reset(button_4_out));  // open: Qn, preset
  and and_14 (and_14_out, j_k_ff_11_q, j_k_ff_7_q);
  or or_10 (or_10_out, and_14_out, button_4_out);
  and and_15 (and_15_out, j_k_ff_12_q, j_k_ff_6_q);
  D_Flip_Flop #(.trigger("falling")) d_ff_15 (
    .D(j_k_ff_12_q), .clk(or_5_out), .Q(d_ff_15_q), .reset(button_4_out));  // open: Qn, preset
  and and_16 (and_16_out, and_9_out, j_k_ff_2_q);
  or or_11 (or_11_out, and_19_out, and_20_out, and_21_out);
  J_K_Flip_Flop j_k_ff_13 (
    .J(j_k_ff_13_qn), .K(j_k_ff_13_qn), .clk(or_11_out), .Q(j_k_ff_13_q), .Qn(j_k_ff_13_qn),
    .reset(button_4_out));  // open: preset
  and and_17 (and_17_out, j_k_ff_2_q, nand_1_out);
  or or_12 (or_12_out, and_21_out, and_18_out);
  and and_18 (and_18_out, d_ff_9_q, and_17_out);
  nand nand_1 (nand_1_out, switch_1_p2, Set_alarm);
  and and_19 (and_19_out, Set_alarm, button_1_out);
  and and_20 (and_20_out, Set_alarm, button_2_out);
  and and_21 (and_21_out, Set_alarm, button_3_out);
  and and_22 (and_22_out, and_20_out, Set_alarm);
  J_K_Flip_Flop j_k_ff_14 (
    .J(switch_1_p2), .K(switch_1_p2), .clk(or_12_out), .Q(j_k_ff_14_q));  // open: Qn, preset, reset
  Hex_Digit_Display hex_digit_display_1 (.value({{3{in_3}}, or_15_out[0]}));  // open: dp
  or or_13 (or_17_out[1], and_23_out, and_24_out);
  and and_23 (and_23_out, Set_alarm, d_ff_10_q);
  and and_24 (and_24_out, d_ff_25_q, not_2_out);
  or or_14 (or_19_out[2], and_25_out, and_26_out);
  and and_25 (and_25_out, Set_alarm, d_ff_12_q);
  and and_26 (and_26_out, d_ff_27_q, not_3_out);
  or or_15 (or_15_out[0], and_27_out, and_30_out);
  and and_27 (and_27_out, Set_alarm, d_ff_4_q);
  xnor xnor_1 (xnor_1_out, d_ff_4_q, d_ff_19_q);
  xnor xnor_2 (xnor_2_out, d_ff_15_q, d_ff_30_q);
  LED led_1 (.in(j_k_ff_13_q));
  not not_1 (not_1_out, or_30_out);
  LED led_2 (.in(not_1_out));
  Hex_Digit_Display hex_digit_display_2 (.value(or_19_out));  // open: dp
  Hex_Digit_Display hex_digit_display_3 (.value({in_3, or_17_out}));  // open: dp
  or or_16 (or_19_out[3], and_28_out, and_29_out);
  and and_28 (and_28_out, Set_alarm, d_ff_15_q);
  and and_29 (and_29_out, d_ff_30_q, not_3_out);
  and and_30 (and_30_out, d_ff_19_q, not_3_out);
  xnor xnor_3 (xnor_3_out, d_ff_12_q, d_ff_27_q);
  xnor xnor_4 (xnor_4_out, d_ff_9_q, d_ff_24_q);
  LED led_3 (.in(and_43_out));
  LED led_4 (.in(not_4_out));
  LED led_5 (.in(Set_alarm));
  LED led_6 (.in(or_30_out));
  Hex_Digit_Display hex_digit_display_4 (.value(or_26_out));  // open: dp
  or or_17 (or_17_out[0], and_31_out, and_32_out);
  and and_31 (and_31_out, Set_alarm, d_ff_7_q);
  and and_32 (and_32_out, d_ff_21_q, not_2_out);
  or or_18 (or_17_out[2], and_33_out, and_34_out);
  and and_33 (and_33_out, Set_alarm, d_ff_13_q);
  and and_34 (and_34_out, d_ff_28_q, not_2_out);
  not not_2 (not_2_out, Set_alarm);
  or or_19 (or_19_out[0], and_35_out, and_36_out);
  and and_35 (and_35_out, Set_alarm, d_ff_6_q);
  and and_36 (and_36_out, d_ff_22_q, not_3_out);
  or or_20 (or_19_out[1], and_37_out, and_38_out);
  and and_37 (and_37_out, Set_alarm, d_ff_9_q);
  and and_38 (and_38_out, d_ff_24_q, not_3_out);
  not not_3 (not_3_out, Set_alarm);
  xnor xnor_5 (xnor_5_out, d_ff_7_q, d_ff_21_q);
  xnor xnor_6 (xnor_6_out, d_ff_6_q, d_ff_22_q);
  and and_39 (and_39_out, xnor_1_out, xnor_2_out, xnor_3_out, xnor_4_out, xnor_6_out, xnor_5_out, xnor_7_out, xnor_8_out, xnor_9_out, xnor_10_out, xnor_11_out, xnor_12_out, xnor_13_out);
  or or_21 (or_26_out[3], and_40_out, and_41_out);
  and and_40 (and_40_out, Set_alarm, d_ff_14_q);
  and and_41 (and_41_out, d_ff_29_q, not_2_out);
  and and_42 (and_42_out, and_46_out, j_k_ff_20_q);
  or or_22 (or_22_out, and_42_out, and_47_out);
  or or_23 (or_23_out, or_22_out, and_52_out);
  xnor xnor_7 (xnor_7_out, d_ff_10_q, d_ff_25_q);
  xnor xnor_8 (xnor_8_out, d_ff_13_q, d_ff_28_q);
  and and_43 (and_43_out, j_k_ff_13_q, and_39_out);
  not not_4 (not_4_out, Set_alarm);
  or or_24 (or_26_out[2], and_44_out, and_45_out);
  and and_44 (and_44_out, Set_alarm, d_ff_11_q);
  and and_45 (and_45_out, d_ff_26_q, not_2_out);
  D_Flip_Flop d_ff_16 (.D(and_54_out), .clk(and_66_out), .Q(d_ff_16_q));  // open: Qn, preset, reset
  and and_46 (and_46_out, and_54_out, or_28_out);
  D_Flip_Flop d_ff_17 (.D(and_46_out), .clk(and_66_out), .Q(d_ff_17_q));  // open: Qn, preset, reset
  and and_47 (and_47_out, and_46_out, and_52_out);
  D_Flip_Flop d_ff_18 (.D(or_23_out), .clk(and_66_out), .Q(d_ff_18_q));  // open: Qn, preset, reset
  xnor xnor_9 (xnor_9_out, d_ff_5_q, d_ff_20_q);
  xnor xnor_10 (xnor_10_out, d_ff_8_q, d_ff_23_q);
  or or_25 (or_26_out[1], and_48_out, and_49_out);
  and and_48 (and_48_out, Set_alarm, d_ff_8_q);
  and and_49 (and_49_out, d_ff_23_q, not_2_out);
  xnor xnor_11 (xnor_11_out, d_ff_11_q, d_ff_26_q);
  xnor xnor_12 (xnor_12_out, d_ff_14_q, d_ff_29_q);
  or or_26 (or_26_out[0], and_50_out, and_51_out);
  and and_50 (and_50_out, Set_alarm, d_ff_5_q);
  and and_51 (and_51_out, d_ff_20_q, not_2_out);
  and and_52 (and_52_out, j_k_ff_26_q, j_k_ff_17_q);
  J_K_Flip_Flop j_k_ff_15 (
    .J(and_52_out), .K(and_52_out), .clk(or_27_out), .Q(j_k_ff_15_q), .reset(and_67_out));  // open: Qn, preset
  and and_53 (and_53_out, d_ff_18_q, nand_2_out);
  or or_27 (or_27_out, and_53_out, and_76_out);
  xnor xnor_13 (xnor_13_out, j_k_ff_14_q, j_k_ff_27_q);
  J_K_Flip_Flop j_k_ff_16 (
    .J(switch_1_p2), .K(switch_1_p2), .clk(and_66_out), .Q(j_k_ff_16_q), .reset(and_63_out));  // open: Qn, preset
  and and_54 (and_54_out, j_k_ff_16_q, j_k_ff_24_q);
  and and_55 (and_55_out, j_k_ff_18_q, j_k_ff_25_q);
  or or_28 (or_28_out, and_55_out, and_75_out);
  J_K_Flip_Flop j_k_ff_17 (.J(or_28_out), .K(or_28_out), .clk(or_29_out), .Q(j_k_ff_17_q));  // open: Qn, preset, reset
  or or_29 (or_29_out, d_ff_17_q, and_75_out);
  D_Flip_Flop #(.trigger("falling")) d_ff_19 (
    .D(j_k_ff_15_q), .clk(or_27_out), .Q(d_ff_19_q));  // open: Qn, preset, reset
  D_Flip_Flop d_ff_20 (.D(j_k_ff_16_q), .clk(and_66_out), .Q(d_ff_20_q));  // open: Qn, preset, reset
  and and_56 (and_56_out, Set_alarm, j_k_ff_14_q);
  J_K_Flip_Flop j_k_ff_18 (
    .J(and_54_out), .K(and_54_out), .clk(d_ff_16_q), .Q(j_k_ff_18_q), .reset(and_64_out));  // open: Qn, preset
  or or_30 (or_30_out, and_56_out, and_57_out);
  and and_57 (and_57_out, j_k_ff_27_q, not_2_out);
  D_Flip_Flop #(.trigger("falling")) d_ff_21 (
    .D(j_k_ff_18_q), .clk(d_ff_16_q), .Q(d_ff_21_q));  // open: Qn, preset, reset
  D_Flip_Flop #(.trigger("falling")) d_ff_22 (
    .D(j_k_ff_17_q), .clk(or_29_out), .Q(d_ff_22_q));  // open: Qn, preset, reset
  J_K_Flip_Flop j_k_ff_19 (
    .J(j_k_ff_16_q), .K(j_k_ff_16_q), .clk(and_66_out), .Q(j_k_ff_19_q), .reset(and_63_out));  // open: Qn, preset
  J_K_Flip_Flop j_k_ff_20 (
    .J(j_k_ff_17_q), .K(j_k_ff_17_q), .clk(or_29_out), .Q(j_k_ff_20_q), .reset(or_31_out));  // open: Qn, preset
  D_Flip_Flop d_ff_23 (.D(j_k_ff_19_q), .clk(and_66_out), .Q(d_ff_23_q));  // open: Qn, preset, reset
  J_K_Flip_Flop j_k_ff_21 (
    .J(j_k_ff_18_q), .K(j_k_ff_18_q), .clk(d_ff_16_q), .Q(j_k_ff_21_q), .reset(and_64_out));  // open: Qn, preset
  D_Flip_Flop #(.trigger("falling")) d_ff_24 (
    .D(j_k_ff_20_q), .clk(or_29_out), .Q(d_ff_24_q));  // open: Qn, preset, reset
  and and_58 (and_58_out, j_k_ff_16_q, j_k_ff_19_q);
  J_K_Flip_Flop j_k_ff_22 (
    .J(and_58_out), .K(and_58_out), .clk(and_66_out), .Q(j_k_ff_22_q), .reset(and_63_out));  // open: Qn, preset
  and and_59 (and_59_out, j_k_ff_17_q, j_k_ff_20_q);
  J_K_Flip_Flop j_k_ff_23 (
    .J(and_59_out), .K(and_59_out), .clk(or_29_out), .Q(j_k_ff_23_q), .reset(or_31_out));  // open: Qn, preset
  and and_60 (and_60_out, j_k_ff_18_q, j_k_ff_21_q);
  D_Flip_Flop #(.trigger("falling")) d_ff_25 (
    .D(j_k_ff_21_q), .clk(d_ff_16_q), .Q(d_ff_25_q));  // open: Qn, preset, reset
  D_Flip_Flop d_ff_26 (.D(j_k_ff_22_q), .clk(and_66_out), .Q(d_ff_26_q));  // open: Qn, preset, reset
  D_Flip_Flop #(.trigger("falling")) d_ff_27 (
    .D(j_k_ff_23_q), .clk(or_29_out), .Q(d_ff_27_q));  // open: Qn, preset, reset
  and and_61 (and_61_out, and_58_out, j_k_ff_22_q);
  J_K_Flip_Flop j_k_ff_24 (
    .J(and_61_out), .K(and_61_out), .clk(and_66_out), .Q(j_k_ff_24_q), .reset(and_63_out));  // open: Qn, preset
  J_K_Flip_Flop j_k_ff_25 (
    .J(and_60_out), .K(and_60_out), .clk(d_ff_16_q), .Q(j_k_ff_25_q), .reset(and_64_out));  // open: Qn, preset
  and and_62 (and_62_out, and_59_out, j_k_ff_23_q);
  J_K_Flip_Flop j_k_ff_26 (
    .J(and_62_out), .K(and_62_out), .clk(or_29_out), .Q(j_k_ff_26_q), .reset(or_31_out));  // open: Qn, preset
  and and_63 (and_63_out, j_k_ff_24_q, j_k_ff_19_q);
  and and_64 (and_64_out, j_k_ff_25_q, j_k_ff_21_q);
  D_Flip_Flop #(.trigger("falling")) d_ff_28 (
    .D(j_k_ff_25_q), .clk(d_ff_16_q), .Q(d_ff_28_q));  // open: Qn, preset, reset
  or or_31 (or_31_out, and_65_out, and_67_out);
  D_Flip_Flop d_ff_29 (.D(j_k_ff_24_q), .clk(and_66_out), .Q(d_ff_29_q));  // open: Qn, preset, reset
  and and_65 (and_65_out, j_k_ff_26_q, j_k_ff_20_q);
  D_Flip_Flop #(.trigger("falling")) d_ff_30 (
    .D(j_k_ff_26_q), .clk(or_29_out), .Q(d_ff_30_q));  // open: Qn, preset, reset
  and and_66 (and_66_out, not_5_out, or_32_out);
  or or_32 (or_32_out, and_68_out, and_72_out);
  and and_67 (and_67_out, and_59_out, j_k_ff_15_q);
  and and_68 (and_68_out, clock_1_out, nand_2_out);
  and and_69 (and_69_out, d_ff_24_q, and_70_out);
  and and_70 (and_70_out, j_k_ff_15_q, nand_2_out);
  Clock clock_1 (.out(clock_1_out));
  and and_71 (and_71_out, not_5_out, and_74_out);
  J_K_Flip_Flop j_k_ff_27 (
    .J(switch_1_p2), .K(switch_1_p2), .clk(or_33_out), .Q(j_k_ff_27_q));  // open: Qn, preset, reset
  or or_33 (or_33_out, and_71_out, and_69_out);
  not not_5 (not_5_out, Set_alarm);
  nand nand_2 (nand_2_out, switch_1_p2, StopTimer);
  and and_72 (and_72_out, StopTimer, button_1_out);
  and and_73 (and_73_out, StopTimer, button_2_out);
  and and_74 (and_74_out, StopTimer, button_3_out);
  and and_75 (and_75_out, not_5_out, and_73_out);
  and and_76 (and_76_out, and_75_out, StopTimer);
  Button button_1 (.out(button_1_out));
  Button button_2 (.out(button_2_out));
  Button button_3 (.out(button_3_out));
  // Switch switch_1: pin names not known; wires that end beside it: 1'b1, switch_1_p2
  Button button_4 (.out(button_4_out));

  // Notes on the sheet:
  //   time
  //   alarm line
  //   alarm line
  //   Set minute
  //   Set hour
  //   Set am/pm
  //   alarm on/off
  //   a.m
  //   alarm line
  //   alarm
  //   clock mode
  //   alarm mode
  //   p.m
  //   clock line
  //   clock line
  //   Power on/off
  //   Reset Alarm
  //   Set minute
  //   Set hour
  //   Set am/pm
endmodule
module testresetalarm1 (
  input  StopTimer,
  input  Set_alarm,
  input  in_3
);

  wire and_1_out, and_2_out, and_3_out, and_4_out, and_5_out, and_6_out, and_7_out, and_8_out, and_9_out,
       and_10_out, and_11_out, and_12_out, and_13_out, and_14_out, and_15_out, and_16_out, and_17_out,
       and_18_out, and_19_out, and_20_out, and_21_out, and_22_out, and_23_out, and_24_out, and_25_out,
       and_26_out, and_27_out, and_28_out, and_29_out, and_30_out, and_31_out, and_32_out, and_33_out,
       and_34_out, and_35_out, and_36_out, and_37_out, and_38_out, and_39_out, and_40_out, and_41_out,
       and_42_out, and_43_out, and_44_out, and_45_out, and_46_out, and_47_out, and_48_out, and_49_out,
       and_50_out, and_51_out, and_52_out, and_53_out, and_54_out, and_55_out, and_56_out, and_57_out,
       and_58_out, and_59_out, and_60_out, and_61_out, and_62_out, and_63_out, and_64_out, and_65_out,
       and_66_out, and_67_out, and_68_out, and_69_out, and_70_out, and_71_out, and_72_out, and_73_out,
       and_74_out, and_75_out, and_76_out, and_77_out, and_78_out, and_79_out, and_80_out, button_1_out,
       button_2_out, button_3_out, button_4_out, clock_1_out, d_ff_1_q, d_ff_2_q, d_ff_3_q, d_ff_4_q,
       d_ff_5_q, d_ff_6_q, d_ff_7_q, d_ff_8_q, d_ff_9_q, d_ff_10_q, d_ff_11_q, d_ff_12_q, d_ff_13_q,
       d_ff_14_q, d_ff_15_q, d_ff_16_q, d_ff_17_q, d_ff_18_q, d_ff_19_q, d_ff_20_q, d_ff_21_q, d_ff_22_q,
       d_ff_23_q, d_ff_24_q, d_ff_25_q, d_ff_26_q, d_ff_27_q, d_ff_28_q, d_ff_29_q, d_ff_30_q, j_k_ff_1_q,
       j_k_ff_2_q, j_k_ff_3_q, j_k_ff_4_q, j_k_ff_5_q, j_k_ff_6_q, j_k_ff_7_q, j_k_ff_8_q, j_k_ff_9_q,
       j_k_ff_10_q, j_k_ff_11_q, j_k_ff_12_q, j_k_ff_13_q, j_k_ff_13_qn, j_k_ff_14_q, j_k_ff_15_q,
       j_k_ff_16_q, j_k_ff_17_q, j_k_ff_18_q, j_k_ff_19_q, j_k_ff_20_q, j_k_ff_21_q, j_k_ff_22_q,
       j_k_ff_23_q, j_k_ff_24_q, j_k_ff_25_q, j_k_ff_26_q, j_k_ff_27_q, nand_1_out, nand_2_out, not_1_out,
       not_2_out, not_3_out, not_4_out, not_5_out, not_6_out, not_7_out, or_1_out, or_2_out, or_3_out,
       or_4_out, or_5_out, or_6_out, or_7_out, or_8_out, or_9_out, or_10_out, or_11_out, or_12_out,
       or_22_out, or_23_out, or_27_out, or_28_out, or_29_out, or_30_out, or_31_out, or_32_out, or_33_out,
       switch_1_p2, xnor_1_out, xnor_2_out, xnor_3_out, xnor_4_out, xnor_5_out, xnor_6_out, xnor_7_out,
       xnor_8_out, xnor_9_out, xnor_10_out, xnor_11_out, xnor_12_out, xnor_13_out;
  wire [0:0] or_15_out;
  wire [2:0] or_17_out;
  wire [3:0] or_19_out, or_26_out;

  and and_1 (and_1_out, and_2_out, j_k_ff_6_q);
  or or_1 (or_1_out, and_1_out, and_3_out);
  or or_2 (or_2_out, or_1_out, and_4_out);
  D_Flip_Flop d_ff_1 (.D(and_7_out), .clk(and_21_out), .Q(d_ff_1_q));  // open: Qn, preset, reset
  and and_2 (and_2_out, and_7_out, or_4_out);
  D_Flip_Flop d_ff_2 (.D(and_2_out), .clk(and_21_out), .Q(d_ff_2_q));  // open: Qn, preset, reset
  and and_3 (and_3_out, and_2_out, and_4_out);
  D_Flip_Flop d_ff_3 (.D(or_2_out), .clk(and_21_out), .Q(d_ff_3_q));  // open: Qn, preset, reset
  and and_4 (and_4_out, j_k_ff_12_q, j_k_ff_4_q);
  and and_5 (and_5_out, d_ff_3_q, nand_1_out);
  or or_3 (or_3_out, and_5_out, and_24_out);
  J_K_Flip_Flop j_k_ff_1 (
    .J(switch_1_p2), .K(switch_1_p2), .clk(and_21_out), .Q(j_k_ff_1_q), .reset(or_9_out));  // open: Qn, preset
  and and_6 (and_6_out, j_k_ff_3_q, j_k_ff_11_q);
  or or_4 (or_4_out, and_6_out, and_22_out);
  or or_5 (or_5_out, d_ff_2_q, and_22_out);
  J_K_Flip_Flop j_k_ff_2 (
    .J(and_4_out), .K(and_4_out), .clk(or_3_out), .Q(j_k_ff_2_q), .reset(or_6_out));  // open: Qn, preset
  and and_7 (and_7_out, j_k_ff_1_q, j_k_ff_10_q);
  J_K_Flip_Flop j_k_ff_3 (
    .J(and_7_out), .K(and_7_out), .clk(d_ff_1_q), .Q(j_k_ff_3_q), .reset(or_10_out));  // open: Qn, preset
  J_K_Flip_Flop j_k_ff_4 (
    .J(or_4_out), .K(or_4_out), .clk(or_5_out), .Q(j_k_ff_4_q), .reset(button_4_out));  // open: Qn, preset
  or or_6 (or_6_out, button_4_out, and_16_out);
  D_Flip_Flop #(.trigger("falling")) d_ff_4 (
    .D(j_k_ff_2_q), .clk(or_3_out), .Q(d_ff_4_q), .reset(button_4_out));  // open: Qn, preset
  D_Flip_Flop d_ff_5 (.D(j_k_ff_1_q), .clk(and_21_out), .Q(d_ff_5_q), .reset(button_4_out));  // open: Qn, preset
  D_Flip_Flop #(.trigger("falling")) d_ff_6 (
    .D(j_k_ff_4_q), .clk(or_5_out), .Q(d_ff_6_q), .reset(button_4_out));  // open: Qn, preset
  J_K_Flip_Flop j_k_ff_5 (
    .J(j_k_ff_1_q), .K(j_k_ff_1_q), .clk(and_21_out), .Q(j_k_ff_5_q), .reset(or_9_out));  // open: Qn, preset
  D_Flip_Flop #(.trigger("falling")) d_ff_7 (
    .D(j_k_ff_3_q), .clk(d_ff_1_q), .Q(d_ff_7_q), .reset(button_4_out));  // open: Qn, preset
  J_K_Flip_Flop j_k_ff_6 (
    .J(j_k_ff_4_q), .K(j_k_ff_4_q), .clk(or_5_out), .Q(j_k_ff_6_q), .reset(or_7_out));  // open: Qn, preset
  D_Flip_Flop d_ff_8 (.D(j_k_ff_5_q), .clk(and_21_out), .Q(d_ff_8_q), .reset(button_4_out));  // open: Qn, preset
  J_K_Flip_Flop j_k_ff_7 (
    .J(j_k_ff_3_q), .K(j_k_ff_3_q), .clk(d_ff_1_q), .Q(j_k_ff_7_q), .reset(or_10_out));  // open: Qn, preset
  and and_8 (and_8_out, j_k_ff_1_q, j_k_ff_5_q);
  J_K_Flip_Flop j_k_ff_8 (
    .J(and_8_out), .K(and_8_out), .clk(and_21_out), .Q(j_k_ff_8_q), .reset(or_9_out));  // open: Qn, preset
  and and_9 (and_9_out, j_k_ff_4_q, j_k_ff_6_q);
  J_K_Flip_Flop j_k_ff_9 (
    .J(and_9_out), .K(and_9_out), .clk(or_5_out), .Q(j_k_ff_9_q), .reset(or_7_out));  // open: Qn, preset
  D_Flip_Flop #(.trigger("falling")) d_ff_9 (
    .D(j_k_ff_6_q), .clk(or_5_out), .Q(d_ff_9_q), .reset(button_4_out));  // open: Qn, preset
  D_Flip_Flop #(.trigger("falling")) d_ff_10 (
    .D(j_k_ff_7_q), .clk(d_ff_1_q), .Q(d_ff_10_q), .reset(button_4_out));  // open: Qn, preset
  D_Flip_Flop d_ff_11 (.D(j_k_ff_8_q), .clk(and_21_out), .Q(d_ff_11_q), .reset(button_4_out));  // open: Qn, preset
  and and_10 (and_10_out, j_k_ff_3_q, j_k_ff_7_q);
  D_Flip_Flop #(.trigger("falling")) d_ff_12 (
    .D(j_k_ff_9_q), .clk(or_5_out), .Q(d_ff_12_q), .reset(button_4_out));  // open: Qn, preset
  and and_11 (and_11_out, and_8_out, j_k_ff_8_q);
  J_K_Flip_Flop j_k_ff_10 (
    .J(and_11_out), .K(and_11_out), .clk(and_21_out), .Q(j_k_ff_10_q), .reset(or_9_out));  // open: Qn, preset
  J_K_Flip_Flop j_k_ff_11 (
    .J(and_10_out), .K(and_10_out), .clk(d_ff_1_q), .Q(j_k_ff_11_q), .reset(or_10_out));  // open: Qn, preset
  and and_12 (and_12_out, and_9_out, j_k_ff_9_q);
  J_K_Flip_Flop j_k_ff_12 (
    .J(and_12_out), .K(and_12_out), .clk(or_5_out), .Q(j_k_ff_12_q), .reset(or_7_out));  // open: Qn, preset
  or or_7 (or_7_out, button_4_out, or_8_out);
  D_Flip_Flop #(.trigger("falling")) d_ff_13 (
    .D(j_k_ff_11_q), .clk(d_ff_1_q), .Q(d_ff_13_q), .reset(button_4_out));  // open: Qn, preset
  or or_8 (or_8_out, and_15_out, and_16_out);
  and and_13 (and_13_out, j_k_ff_10_q, j_k_ff_5_q);
  or or_9 (or_9_out, and_13_out, button_4_out);
  D_Flip_Flop d_ff_14 (.D(j_k_ff_10_q), .clk(and_21_out), .Q(d_ff_14_q), .reset(button_4_out));  // open: Qn, preset
  and and_14 (and_14_out, j_k_ff_11_q, j_k_ff_7_q);
  or or_10 (or_10_out, and_14_out, button_4_out);
  and and_15 (and_15_out, j_k_ff_12_q, j_k_ff_6_q);
  D_Flip_Flop #(.trigger("falling")) d_ff_15 (
    .D(j_k_ff_12_q), .clk(or_5_out), .Q(d_ff_15_q), .reset(button_4_out));  // open: Qn, preset
  and and_16 (and_16_out, and_9_out, j_k_ff_2_q);
  or or_11 (or_11_out, and_21_out, and_22_out, and_23_out);
  J_K_Flip_Flop j_k_ff_13 (
    .J(j_k_ff_13_qn), .K(j_k_ff_13_qn), .clk(or_11_out), .Q(j_k_ff_13_q), .Qn(j_k_ff_13_qn),
    .reset(button_4_out));  // open: preset
  not not_1 (not_1_out, and_23_out);
  and and_17 (and_17_out, j_k_ff_2_q, d_ff_9_q);
  and and_18 (and_18_out, not_1_out, and_17_out);
  and and_19 (and_19_out, j_k_ff_2_q, nand_1_out);
  or or_12 (or_12_out, and_23_out, and_18_out, and_20_out);
  and and_20 (and_20_out, d_ff_9_q, and_19_out);
  nand nand_1 (nand_1_out, switch_1_p2, Set_alarm);
  and and_21 (and_21_out, Set_alarm, button_1_out);
  and and_22 (and_22_out, Set_alarm, button_2_out);
  and and_23 (and_23_out, Set_alarm, button_3_out);
  and and_24 (and_24_out, and_22_out, Set_alarm);
  J_K_Flip_Flop j_k_ff_14 (
    .J(switch_1_p2), .K(switch_1_p2), .clk(or_12_out), .Q(j_k_ff_14_q));  // open: Qn, preset, reset
  Hex_Digit_Display hex_digit_display_1 (.value({{3{in_3}}, or_15_out[0]}));  // open: dp
  or or_13 (or_17_out[1], and_25_out, and_26_out);
  and and_25 (and_25_out, Set_alarm, d_ff_10_q);
  and and_26 (and_26_out, d_ff_25_q, not_3_out);
  or or_14 (or_19_out[2], and_27_out, and_28_out);
  and and_27 (and_27_out, Set_alarm, d_ff_12_q);
  and and_28 (and_28_out, d_ff_27_q, not_4_out);
  or or_15 (or_15_out[0], and_29_out, and_32_out);
  and and_29 (and_29_out, Set_alarm, d_ff_4_q);
  xnor xnor_1 (xnor_1_out, d_ff_4_q, d_ff_19_q);
  xnor xnor_2 (xnor_2_out, d_ff_15_q, d_ff_30_q);
  LED led_1 (.in(j_k_ff_13_q));
  not not_2 (not_2_out, or_30_out);
  LED led_2 (.in(not_2_out));
  Hex_Digit_Display hex_digit_display_2 (.value(or_19_out));  // open: dp
  Hex_Digit_Display hex_digit_display_3 (.value({in_3, or_17_out}));  // open: dp
  or or_16 (or_19_out[3], and_30_out, and_31_out);
  and and_30 (and_30_out, Set_alarm, d_ff_15_q);
  and and_31 (and_31_out, d_ff_30_q, not_4_out);
  and and_32 (and_32_out, d_ff_19_q, not_4_out);
  xnor xnor_3 (xnor_3_out, d_ff_12_q, d_ff_27_q);
  xnor xnor_4 (xnor_4_out, d_ff_9_q, d_ff_24_q);
  LED led_3 (.in(and_45_out));
  LED led_4 (.in(not_5_out));
  LED led_5 (.in(Set_alarm));
  LED led_6 (.in(or_30_out));
  Hex_Digit_Display hex_digit_display_4 (.value(or_26_out));  // open: dp
  or or_17 (or_17_out[0], and_33_out, and_34_out);
  and and_33 (and_33_out, Set_alarm, d_ff_7_q);
  and and_34 (and_34_out, d_ff_21_q, not_3_out);
  or or_18 (or_17_out[2], and_35_out, and_36_out);
  and and_35 (and_35_out, Set_alarm, d_ff_13_q);
  and and_36 (and_36_out, d_ff_28_q, not_3_out);
  not not_3 (not_3_out, Set_alarm);
  or or_19 (or_19_out[0], and_37_out, and_38_out);
  and and_37 (and_37_out, Set_alarm, d_ff_6_q);
  and and_38 (and_38_out, d_ff_22_q, not_4_out);
  or or_20 (or_19_out[1], and_39_out, and_40_out);
  and and_39 (and_39_out, Set_alarm, d_ff_9_q);
  and and_40 (and_40_out, d_ff_24_q, not_4_out);
  not not_4 (not_4_out, Set_alarm);
  xnor xnor_5 (xnor_5_out, d_ff_7_q, d_ff_21_q);
  xnor xnor_6 (xnor_6_out, d_ff_6_q, d_ff_22_q);
  and and_41 (and_41_out, xnor_1_out, xnor_2_out, xnor_3_out, xnor_4_out, xnor_6_out, xnor_5_out, xnor_7_out, xnor_8_out, xnor_9_out, xnor_10_out, xnor_11_out, xnor_12_out, xnor_13_out);
  or or_21 (or_26_out[3], and_42_out, and_43_out);
  and and_42 (and_42_out, Set_alarm, d_ff_14_q);
  and and_43 (and_43_out, d_ff_29_q, not_3_out);
  and and_44 (and_44_out, and_48_out, j_k_ff_20_q);
  or or_22 (or_22_out, and_44_out, and_49_out);
  or or_23 (or_23_out, or_22_out, and_54_out);
  xnor xnor_7 (xnor_7_out, d_ff_10_q, d_ff_25_q);
  xnor xnor_8 (xnor_8_out, d_ff_13_q, d_ff_28_q);
  and and_45 (and_45_out, j_k_ff_13_q, and_41_out);
  not not_5 (not_5_out, Set_alarm);
  or or_24 (or_26_out[2], and_46_out, and_47_out);
  and and_46 (and_46_out, Set_alarm, d_ff_11_q);
  and and_47 (and_47_out, d_ff_26_q, not_3_out);
  D_Flip_Flop d_ff_16 (.D(and_56_out), .clk(and_68_out), .Q(d_ff_16_q));  // open: Qn, preset, reset
  and and_48 (and_48_out, and_56_out, or_28_out);
  D_Flip_Flop d_ff_17 (.D(and_48_out), .clk(and_68_out), .Q(d_ff_17_q));  // open: Qn, preset, reset
  and and_49 (and_49_out, and_48_out, and_54_out);
  D_Flip_Flop d_ff_18 (.D(or_23_out), .clk(and_68_out), .Q(d_ff_18_q));  // open: Qn, preset, reset
  xnor xnor_9 (xnor_9_out, d_ff_5_q, d_ff_20_q);
  xnor xnor_10 (xnor_10_out, d_ff_8_q, d_ff_23_q);
  or or_25 (or_26_out[1], and_50_out, and_51_out);
  and and_50 (and_50_out, Set_alarm, d_ff_8_q);
  and and_51 (and_51_out, d_ff_23_q, not_3_out);
  xnor xnor_11 (xnor_11_out, d_ff_11_q, d_ff_26_q);
  xnor xnor_12 (xnor_12_out, d_ff_14_q, d_ff_29_q);
  or or_26 (or_26_out[0], and_52_out, and_53_out);
  and and_52 (and_52_out, Set_alarm, d_ff_5_q);
  and and_53 (and_53_out, d_ff_20_q, not_3_out);
  and and_54 (and_54_out, j_k_ff_26_q, j_k_ff_17_q);
  J_K_Flip_Flop j_k_ff_15 (
    .J(and_54_out), .K(and_54_out), .clk(or_27_out), .Q(j_k_ff_15_q), .reset(and_69_out));  // open: Qn, preset
  and and_55 (and_55_out, d_ff_18_q, nand_2_out);
  or or_27 (or_27_out, and_55_out, and_80_out);
  xnor xnor_13 (xnor_13_out, j_k_ff_14_q, j_k_ff_27_q);
  J_K_Flip_Flop j_k_ff_16 (
    .J(switch_1_p2), .K(switch_1_p2), .clk(and_68_out), .Q(j_k_ff_16_q), .reset(and_65_out));  // open: Qn, preset
  and and_56 (and_56_out, j_k_ff_16_q, j_k_ff_24_q);
  and and_57 (and_57_out, j_k_ff_18_q, j_k_ff_25_q);
  or or_28 (or_28_out, and_57_out, and_79_out);
  J_K_Flip_Flop j_k_ff_17 (.J(or_28_out), .K(or_28_out), .clk(or_29_out), .Q(j_k_ff_17_q));  // open: Qn, preset, reset
  or or_29 (or_29_out, d_ff_17_q, and_79_out);
  D_Flip_Flop #(.trigger("falling")) d_ff_19 (
    .D(j_k_ff_15_q), .clk(or_27_out), .Q(d_ff_19_q));  // open: Qn, preset, reset
  D_Flip_Flop d_ff_20 (.D(j_k_ff_16_q), .clk(and_68_out), .Q(d_ff_20_q));  // open: Qn, preset, reset
  and and_58 (and_58_out, Set_alarm, j_k_ff_14_q);
  J_K_Flip_Flop j_k_ff_18 (
    .J(and_56_out), .K(and_56_out), .clk(d_ff_16_q), .Q(j_k_ff_18_q), .reset(and_66_out));  // open: Qn, preset
  or or_30 (or_30_out, and_58_out, and_59_out);
  and and_59 (and_59_out, j_k_ff_27_q, not_3_out);
  D_Flip_Flop #(.trigger("falling")) d_ff_21 (
    .D(j_k_ff_18_q), .clk(d_ff_16_q), .Q(d_ff_21_q));  // open: Qn, preset, reset
  D_Flip_Flop #(.trigger("falling")) d_ff_22 (
    .D(j_k_ff_17_q), .clk(or_29_out), .Q(d_ff_22_q));  // open: Qn, preset, reset
  J_K_Flip_Flop j_k_ff_19 (
    .J(j_k_ff_16_q), .K(j_k_ff_16_q), .clk(and_68_out), .Q(j_k_ff_19_q), .reset(and_65_out));  // open: Qn, preset
  J_K_Flip_Flop j_k_ff_20 (
    .J(j_k_ff_17_q), .K(j_k_ff_17_q), .clk(or_29_out), .Q(j_k_ff_20_q), .reset(or_31_out));  // open: Qn, preset
  D_Flip_Flop d_ff_23 (.D(j_k_ff_19_q), .clk(and_68_out), .Q(d_ff_23_q));  // open: Qn, preset, reset
  J_K_Flip_Flop j_k_ff_21 (
    .J(j_k_ff_18_q), .K(j_k_ff_18_q), .clk(d_ff_16_q), .Q(j_k_ff_21_q), .reset(and_66_out));  // open: Qn, preset
  D_Flip_Flop #(.trigger("falling")) d_ff_24 (
    .D(j_k_ff_20_q), .clk(or_29_out), .Q(d_ff_24_q));  // open: Qn, preset, reset
  and and_60 (and_60_out, j_k_ff_16_q, j_k_ff_19_q);
  J_K_Flip_Flop j_k_ff_22 (
    .J(and_60_out), .K(and_60_out), .clk(and_68_out), .Q(j_k_ff_22_q), .reset(and_65_out));  // open: Qn, preset
  and and_61 (and_61_out, j_k_ff_17_q, j_k_ff_20_q);
  J_K_Flip_Flop j_k_ff_23 (
    .J(and_61_out), .K(and_61_out), .clk(or_29_out), .Q(j_k_ff_23_q), .reset(or_31_out));  // open: Qn, preset
  and and_62 (and_62_out, j_k_ff_18_q, j_k_ff_21_q);
  D_Flip_Flop #(.trigger("falling")) d_ff_25 (
    .D(j_k_ff_21_q), .clk(d_ff_16_q), .Q(d_ff_25_q));  // open: Qn, preset, reset
  D_Flip_Flop d_ff_26 (.D(j_k_ff_22_q), .clk(and_68_out), .Q(d_ff_26_q));  // open: Qn, preset, reset
  D_Flip_Flop #(.trigger("falling")) d_ff_27 (
    .D(j_k_ff_23_q), .clk(or_29_out), .Q(d_ff_27_q));  // open: Qn, preset, reset
  and and_63 (and_63_out, and_60_out, j_k_ff_22_q);
  J_K_Flip_Flop j_k_ff_24 (
    .J(and_63_out), .K(and_63_out), .clk(and_68_out), .Q(j_k_ff_24_q), .reset(and_65_out));  // open: Qn, preset
  J_K_Flip_Flop j_k_ff_25 (
    .J(and_62_out), .K(and_62_out), .clk(d_ff_16_q), .Q(j_k_ff_25_q), .reset(and_66_out));  // open: Qn, preset
  and and_64 (and_64_out, and_61_out, j_k_ff_23_q);
  J_K_Flip_Flop j_k_ff_26 (
    .J(and_64_out), .K(and_64_out), .clk(or_29_out), .Q(j_k_ff_26_q), .reset(or_31_out));  // open: Qn, preset
  and and_65 (and_65_out, j_k_ff_24_q, j_k_ff_19_q);
  and and_66 (and_66_out, j_k_ff_25_q, j_k_ff_21_q);
  D_Flip_Flop #(.trigger("falling")) d_ff_28 (
    .D(j_k_ff_25_q), .clk(d_ff_16_q), .Q(d_ff_28_q));  // open: Qn, preset, reset
  or or_31 (or_31_out, and_67_out, and_69_out);
  D_Flip_Flop d_ff_29 (.D(j_k_ff_24_q), .clk(and_68_out), .Q(d_ff_29_q));  // open: Qn, preset, reset
  and and_67 (and_67_out, j_k_ff_26_q, j_k_ff_20_q);
  D_Flip_Flop #(.trigger("falling")) d_ff_30 (
    .D(j_k_ff_26_q), .clk(or_29_out), .Q(d_ff_30_q));  // open: Qn, preset, reset
  and and_68 (and_68_out, not_7_out, or_32_out);
  or or_32 (or_32_out, and_70_out, and_76_out);
  and and_69 (and_69_out, and_61_out, j_k_ff_15_q);
  and and_70 (and_70_out, clock_1_out, nand_2_out);
  not not_6 (not_6_out, and_75_out);
  and and_71 (and_71_out, j_k_ff_15_q, d_ff_24_q);
  and and_72 (and_72_out, not_6_out, and_71_out);
  and and_73 (and_73_out, d_ff_24_q, and_74_out);
  and and_74 (and_74_out, j_k_ff_15_q, nand_2_out);
  Clock clock_1 (.out(clock_1_out));
  and and_75 (and_75_out, not_7_out, and_78_out);
  J_K_Flip_Flop j_k_ff_27 (
    .J(switch_1_p2), .K(switch_1_p2), .clk(or_33_out), .Q(j_k_ff_27_q));  // open: Qn, preset, reset
  or or_33 (or_33_out, and_75_out, and_72_out, and_73_out);
  not not_7 (not_7_out, Set_alarm);
  nand nand_2 (nand_2_out, switch_1_p2, StopTimer);
  and and_76 (and_76_out, StopTimer, button_1_out);
  and and_77 (and_77_out, StopTimer, button_2_out);
  and and_78 (and_78_out, StopTimer, button_3_out);
  and and_79 (and_79_out, not_7_out, and_77_out);
  and and_80 (and_80_out, and_79_out, StopTimer);
  Button button_1 (.out(button_1_out));
  Button button_2 (.out(button_2_out));
  Button button_3 (.out(button_3_out));
  // Switch switch_1: pin names not known; wires that end beside it: 1'b1, switch_1_p2
  Button button_4 (.out(button_4_out));

  // Notes on the sheet:
  //   time
  //   alarm line
  //   alarm line
  //   Set minute
  //   Set hour
  //   Set am/pm
  //   alarm on/off
  //   a.m
  //   alarm line
  //   alarm
  //   clock mode
  //   alarm mode
  //   p.m
  //   clock line
  //   clock line
  //   Power on/off
  //   Reset Alarm
  //   Set minute
  //   Set hour
  //   Set am/pm
endmodule
