// Logisim project Assignment1BackUp.circ as structural Verilog: 4 circuits, main circuit main
module main (
  input  Power,
  input  StopTimer,
  input  Set_alarm,
  input  in_4
);

  wire and_1_out, and_2_out, and_3_out, and_4_out, and_5_out, and_6_out, and_7_out, and_8_out, and_9_out,
       and_10_out, and_11_out, and_12_out, and_13_out, and_14_out, and_15_out, and_16_out, and_17_out,
       and_18_out, and_19_out, and_20_out, and_21_out, and_22_out, and_23_out, and_24_out, and_25_out,
       and_26_out, and_27_out, and_28_out, and_29_out, and_30_out, and_31_out, and_32_out, and_33_out,
       and_34_out, and_35_out, and_36_out, and_37_out, and_38_out, and_39_out, and_40_out, and_41_out,
       and_42_out, and_43_out, and_44_out, and_45_out, and_46_out, and_47_out, and_48_out, and_49_out,
       and_50_out, and_51_out, and_52_out, and_53_out, and_54_out, and_55_out, and_56_out, and_57_out,
       and_58_out, and_59_out, and_60_out, and_61_out, and_62_out, and_63_out, and_64_out, and_65_out,
       and_66_out, and_67_out, and_68_out, and_69_out, and_70_out, and_71_out, and_72_out, and_73_out,
       and_74_out, and_75_out, button_1_out, button_2_out, button_3_out, clock_1_out, d_ff_1_q, d_ff_2_q,
       d_ff_3_q, d_ff_4_q, d_ff_5_q, d_ff_6_q, d_ff_7_q, d_ff_8_q, d_ff_9_q, d_ff_10_q, d_ff_11_q, d_ff_12_q,
       d_ff_13_q, d_ff_14_q, d_ff_15_q, d_ff_16_q, d_ff_17_q, d_ff_18_q, d_ff_19_q, d_ff_20_q, d_ff_21_q,
       d_ff_22_q, d_ff_23_q, d_ff_24_q, d_ff_25_q, d_ff_26_q, d_ff_27_q, d_ff_28_q, d_ff_29_q, d_ff_30_q,
       j_k_ff_1_q, j_k_ff_2_q, j_k_ff_3_q, j_k_ff_4_q, j_k_ff_5_q, j_k_ff_6_q, j_k_ff_7_q, j_k_ff_8_q,
       j_k_ff_9_q, j_k_ff_10_q, j_k_ff_11_q, j_k_ff_12_q, j_k_ff_13_q, j_k_ff_14_q, j_k_ff_15_q, j_k_ff_16_q,
       j_k_ff_17_q, j_k_ff_18_q, j_k_ff_19_q, j_k_ff_20_q, j_k_ff_21_q, j_k_ff_22_q, j_k_ff_23_q,
       j_k_ff_24_q, j_k_ff_25_q, j_k_ff_26_q, nand_1_out, nand_2_out, not_1_out, not_2_out, not_3_out,
       or_1_out, or_2_out, or_3_out, or_4_out, or_5_out, or_6_out, or_7_out, or_17_out, or_18_out, or_22_out,
       or_23_out, or_24_out, or_25_out, or_26_out, or_27_out, or_28_out, xnor_1_out, xnor_2_out, xnor_3_out,
       xnor_4_out, xnor_5_out, xnor_6_out, xnor_7_out, xnor_8_out, xnor_9_out, xnor_10_out, xnor_11_out,
       xnor_12_out, xnor_13_out;
  wire [0:0] or_10_out;
  wire [2:0] or_12_out;
  wire [3:0] or_14_out, or_21_out;

  and and_1 (and_1_out, and_2_out, j_k_ff_6_q);
  or or_1 (or_1_out, and_1_out, and_3_out);
  or or_2 (or_2_out, or_1_out, and_4_out);
  D_Flip_Flop d_ff_1 (.D(and_7_out), .clk(and_19_out), .Q(d_ff_1_q));  // open: Qn, preset, reset
  and and_2 (and_2_out, and_7_out, or_4_out);
  D_Flip_Flop d_ff_2 (.D(and_2_out), .clk(and_19_out), .Q(d_ff_2_q));  // open: Qn, preset, reset
  and and_3 (and_3_out, and_2_out, and_4_out);
  D_Flip_Flop d_ff_3 (.D(or_2_out), .clk(and_19_out), .Q(d_ff_3_q));  // open: Qn, preset, reset
  and and_4 (and_4_out, j_k_ff_12_q, j_k_ff_4_q);
  and and_5 (and_5_out, d_ff_3_q, nand_1_out);
  or or_3 (or_3_out, and_5_out, and_22_out);
  J_K_Flip_Flop j_k_ff_1 (
    .J(Power), .K(Power), .clk(and_19_out), .Q(j_k_ff_1_q), .reset(and_13_out));  // open: Qn, preset
  and and_6 (and_6_out, j_k_ff_3_q, j_k_ff_11_q);
  or or_4 (or_4_out, and_6_out, and_20_out);
  or or_5 (or_5_out, d_ff_2_q, and_20_out);
  J_K_Flip_Flop j_k_ff_2 (
    .J(and_4_out), .K(and_4_out), .clk(or_3_out), .Q(j_k_ff_2_q), .reset(and_16_out));  // open: Qn, preset
  and and_7 (and_7_out, j_k_ff_1_q, j_k_ff_10_q);
  J_K_Flip_Flop j_k_ff_3 (
    .J(and_7_out), .K(and_7_out), .clk(d_ff_1_q), .Q(j_k_ff_3_q), .reset(and_14_out));  // open: Qn, preset
  J_K_Flip_Flop j_k_ff_4 (.J(or_4_out), .K(or_4_out), .clk(or_5_out), .Q(j_k_ff_4_q));  // open: Qn, preset, reset
  D_Flip_Flop #(.trigger("falling")) d_ff_4 (.D(j_k_ff_2_q), .clk(or_3_out), .Q(d_ff_4_q));  // open: Qn, preset, reset
  D_Flip_Flop d_ff_5 (.D(j_k_ff_1_q), .clk(and_19_out), .Q(d_ff_5_q));  // open: Qn, preset, reset
  D_Flip_Flop #(.trigger("falling")) d_ff_6 (.D(j_k_ff_4_q), .clk(or_5_out), .Q(d_ff_6_q));  // open: Qn, preset, reset
  J_K_Flip_Flop j_k_ff_5 (
    .J(j_k_ff_1_q), .K(j_k_ff_1_q), .clk(and_19_out), .Q(j_k_ff_5_q), .reset(and_13_out));  // open: Qn, preset
  D_Flip_Flop #(.trigger("falling")) d_ff_7 (.D(j_k_ff_3_q), .clk(d_ff_1_q), .Q(d_ff_7_q));  // open: Qn, preset, reset
  J_K_Flip_Flop j_k_ff_6 (
    .J(j_k_ff_4_q), .K(j_k_ff_4_q), .clk(or_5_out), .Q(j_k_ff_6_q), .reset(or_6_out));  // open: Qn, preset
  D_Flip_Flop d_ff_8 (.D(j_k_ff_5_q), .clk(and_19_out), .Q(d_ff_8_q));  // open: Qn, preset, reset
  J_K_Flip_Flop j_k_ff_7 (
    .J(j_k_ff_3_q), .K(j_k_ff_3_q), .clk(d_ff_1_q), .Q(j_k_ff_7_q), .reset(and_14_out));  // open: Qn, preset
  and and_8 (and_8_out, j_k_ff_1_q, j_k_ff_5_q);
  J_K_Flip_Flop j_k_ff_8 (
    .J(and_8_out), .K(and_8_out), .clk(and_19_out), .Q(j_k_ff_8_q), .reset(and_13_out));  // open: Qn, preset
  and and_9 (and_9_out, j_k_ff_4_q, j_k_ff_6_q);
  J_K_Flip_Flop j_k_ff_9 (
    .J(and_9_out), .K(and_9_out), .clk(or_5_out), .Q(j_k_ff_9_q), .reset(or_6_out));  // open: Qn, preset
  D_Flip_Flop #(.trigger("falling")) d_ff_9 (.D(j_k_ff_6_q), .clk(or_5_out), .Q(d_ff_9_q));  // open: Qn, preset, reset
  D_Flip_Flop #(.trigger("falling")) d_ff_10 (
    .D(j_k_ff_7_q), .clk(d_ff_1_q), .Q(d_ff_10_q));  // open: Qn, preset, reset
  D_Flip_Flop d_ff_11 (.D(j_k_ff_8_q), .clk(and_19_out), .Q(d_ff_11_q));  // open: Qn, preset, reset
  and and_10 (and_10_out, j_k_ff_3_q, j_k_ff_7_q);
  D_Flip_Flop #(.trigger("falling")) d_ff_12 (
    .D(j_k_ff_9_q), .clk(or_5_out), .Q(d_ff_12_q));  // open: Qn, preset, reset
  and and_11 (and_11_out, and_8_out, j_k_ff_8_q);
  J_K_Flip_Flop j_k_ff_10 (
    .J(and_11_out), .K(and_11_out), .clk(and_19_out), .Q(j_k_ff_10_q), .reset(and_13_out));  // open: Qn, preset
  J_K_Flip_Flop j_k_ff_11 (
    .J(and_10_out), .K(and_10_out), .clk(d_ff_1_q), .Q(j_k_ff_11_q), .reset(and_14_out));  // open: Qn, preset
  and and_12 (and_12_out, and_9_out, j_k_ff_9_q);
  J_K_Flip_Flop j_k_ff_12 (
    .J(and_12_out), .K(and_12_out), .clk(or_5_out), .Q(j_k_ff_12_q), .reset(or_6_out));  // open: Qn, preset
  D_Flip_Flop #(.trigger("falling")) d_ff_13 (
    .D(j_k_ff_11_q), .clk(d_ff_1_q), .Q(d_ff_13_q));  // open: Qn, preset, reset
  or or_6 (or_6_out, and_15_out, and_16_out);
  and and_13 (and_13_out, j_k_ff_10_q, j_k_ff_5_q);
  D_Flip_Flop d_ff_14 (.D(j_k_ff_10_q), .clk(and_19_out), .Q(d_ff_14_q));  // open: Qn, preset, reset
  and and_14 (and_14_out, j_k_ff_11_q, j_k_ff_7_q);
  and and_15 (and_15_out, j_k_ff_12_q, j_k_ff_6_q);
  D_Flip_Flop #(.trigger("falling")) d_ff_15 (
    .D(j_k_ff_12_q), .clk(or_5_out), .Q(d_ff_15_q));  // open: Qn, preset, reset
  and and_16 (and_16_out, and_9_out, j_k_ff_2_q);
  and and_17 (and_17_out, j_k_ff_2_q, nand_1_out);
  or or_7 (or_7_out, and_21_out, and_18_out);
  and and_18 (and_18_out, d_ff_9_q, and_17_out);
  nand nand_1 (nand_1_out, Power, Set_alarm);
  and and_19 (and_19_out, Set_alarm, button_1_out);
  and and_20 (and_20_out, Set_alarm, button_2_out);
  and and_21 (and_21_out, Set_alarm, button_3_out);
  and and_22 (and_22_out, and_20_out, Set_alarm);
  J_K_Flip_Flop j_k_ff_13 (.J(Power), .K(Power), .clk(or_7_out), .Q(j_k_ff_13_q));  // open: Qn, preset, reset
  Hex_Digit_Display hex_digit_display_1 (.value({{3{in_4}}, or_10_out[0]}));  // open: dp
  or or_8 (or_12_out[1], and_23_out, and_24_out);
  and and_23 (and_23_out, Set_alarm, d_ff_10_q);
  and and_24 (and_24_out, d_ff_25_q, not_1_out);
  or or_9 (or_14_out[2], and_25_out, and_26_out);
  and and_25 (and_25_out, Set_alarm, d_ff_12_q);
  and and_26 (and_26_out, d_ff_27_q, not_2_out);
  or or_10 (or_10_out[0], and_27_out, and_30_out);
  and and_27 (and_27_out, Set_alarm, d_ff_4_q);
  xnor xnor_1 (xnor_1_out, d_ff_4_q, d_ff_19_q);
  xnor xnor_2 (xnor_2_out, d_ff_15_q, d_ff_30_q);
  Hex_Digit_Display hex_digit_display_2 (.value(or_14_out));  // open: dp
  Hex_Digit_Display hex_digit_display_3 (.value({in_4, or_12_out}));  // open: dp
  or or_11 (or_14_out[3], and_28_out, and_29_out);
  and and_28 (and_28_out, Set_alarm, d_ff_15_q);
  and and_29 (and_29_out, d_ff_30_q, not_2_out);
  and and_30 (and_30_out, d_ff_19_q, not_2_out);
  xnor xnor_3 (xnor_3_out, d_ff_12_q, d_ff_27_q);
  xnor xnor_4 (xnor_4_out, d_ff_9_q, d_ff_24_q);
  LED led_1 (.in(and_39_out));
  LED led_2 (.in(Set_alarm));
  LED led_3 (.in(or_25_out));
  Hex_Digit_Display hex_digit_display_4 (.value(or_21_out));  // open: dp
  or or_12 (or_12_out[0], and_31_out, and_32_out);
  and and_31 (and_31_out, Set_alarm, d_ff_7_q);
  and and_32 (and_32_out, d_ff_21_q, not_1_out);
  or or_13 (or_12_out[2], and_33_out, and_34_out);
  and and_33 (and_33_out, Set_alarm, d_ff_13_q);
  and and_34 (and_34_out, d_ff_28_q, not_1_out);
  not not_1 (not_1_out, Set_alarm);
  or or_14 (or_14_out[0], and_35_out, and_36_out);
  and and_35 (and_35_out, Set_alarm, d_ff_6_q);
  and and_36 (and_36_out, d_ff_22_q, not_2_out);
  or or_15 (or_14_out[1], and_37_out, and_38_out);
  and and_37 (and_37_out, Set_alarm, d_ff_9_q);
  and and_38 (and_38_out, d_ff_24_q, not_2_out);
  not not_2 (not_2_out, Set_alarm);
  xnor xnor_5 (xnor_5_out, d_ff_7_q, d_ff_21_q);
  xnor xnor_6 (xnor_6_out, d_ff_6_q, d_ff_22_q);
  and and_39 (and_39_out, xnor_1_out, xnor_2_out, xnor_3_out, xnor_4_out, xnor_6_out, xnor_5_out, xnor_7_out, xnor_8_out, xnor_9_out, xnor_10_out, xnor_11_out, xnor_12_out, xnor_13_out);
  or or_16 (or_21_out[3], and_40_out, and_41_out);
  and and_40 (and_40_out, Set_alarm, d_ff_14_q);
  and and_41 (and_41_out, d_ff_29_q, not_1_out);
  and and_42 (and_42_out, and_45_out, j_k_ff_19_q);
  or or_17 (or_17_out, and_42_out, and_46_out);
  or or_18 (or_18_out, or_17_out, and_51_out);
  xnor xnor_7 (xnor_7_out, d_ff_10_q, d_ff_25_q);
  xnor xnor_8 (xnor_8_out, d_ff_13_q, d_ff_28_q);
  or or_19 (or_21_out[2], and_43_out, and_44_out);
  and and_43 (and_43_out, Set_alarm, d_ff_11_q);
  and and_44 (and_44_out, d_ff_26_q, not_1_out);
  D_Flip_Flop d_ff_16 (.D(and_53_out), .clk(and_65_out), .Q(d_ff_16_q));  // open: Qn, preset, reset
  and and_45 (and_45_out, and_53_out, or_23_out);
  D_Flip_Flop d_ff_17 (.D(and_45_out), .clk(and_65_out), .Q(d_ff_17_q));  // open: Qn, preset, reset
  and and_46 (and_46_out, and_45_out, and_51_out);
  D_Flip_Flop d_ff_18 (.D(or_18_out), .clk(and_65_out), .Q(d_ff_18_q));  // open: Qn, preset, reset
  xnor xnor_9 (xnor_9_out, d_ff_5_q, d_ff_20_q);
  xnor xnor_10 (xnor_10_out, d_ff_8_q, d_ff_23_q);
  or or_20 (or_21_out[1], and_47_out, and_48_out);
  and and_47 (and_47_out, Set_alarm, d_ff_8_q);
  and and_48 (and_48_out, d_ff_23_q, not_1_out);
  xnor xnor_11 (xnor_11_out, d_ff_11_q, d_ff_26_q);
  xnor xnor_12 (xnor_12_out, d_ff_14_q, d_ff_29_q);
  or or_21 (or_21_out[0], and_49_out, and_50_out);
  and and_49 (and_49_out, Set_alarm, d_ff_5_q);
  and and_50 (and_50_out, d_ff_20_q, not_1_out);
  and and_51 (and_51_out, j_k_ff_25_q, j_k_ff_16_q);
  J_K_Flip_Flop j_k_ff_14 (
    .J(and_51_out), .K(and_51_out), .clk(or_22_out), .Q(j_k_ff_14_q), .reset(and_66_out));  // open: Qn, preset
  and and_52 (and_52_out, d_ff_18_q, nand_2_out);
  or or_22 (or_22_out, and_52_out, and_75_out);
  xnor xnor_13 (xnor_13_out, j_k_ff_13_q, j_k_ff_26_q);
  J_K_Flip_Flop j_k_ff_15 (
    .J(Power), .K(Power), .clk(and_65_out), .Q(j_k_ff_15_q), .reset(and_62_out));  // open: Qn, preset
  and and_53 (and_53_out, j_k_ff_15_q, j_k_ff_23_q);
  and and_54 (and_54_out, j_k_ff_17_q, j_k_ff_24_q);
  or or_23 (or_23_out, and_54_out, and_74_out);
  J_K_Flip_Flop j_k_ff_16 (.J(or_23_out), .K(or_23_out), .clk(or_24_out), .Q(j_k_ff_16_q));  // open: Qn, preset, reset
  or or_24 (or_24_out, d_ff_17_q, and_74_out);
  D_Flip_Flop #(.trigger("falling")) d_ff_19 (
    .D(j_k_ff_14_q), .clk(or_22_out), .Q(d_ff_19_q));  // open: Qn, preset, reset
  D_Flip_Flop d_ff_20 (.D(j_k_ff_15_q), .clk(and_65_out), .Q(d_ff_20_q));  // open: Qn, preset, reset
  and and_55 (and_55_out, Set_alarm, j_k_ff_13_q);
  J_K_Flip_Flop j_k_ff_17 (
    .J(and_53_out), .K(and_53_out), .clk(d_ff_16_q), .Q(j_k_ff_17_q), .reset(and_63_out));  // open: Qn, preset
  or or_25 (or_25_out, and_55_out, and_56_out);
  and and_56 (and_56_out, j_k_ff_26_q, not_1_out);
  D_Flip_Flop #(.trigger("falling")) d_ff_21 (
    .D(j_k_ff_17_q), .clk(d_ff_16_q), .Q(d_ff_21_q));  // open: Qn, preset, reset
  D_Flip_Flop #(.trigger("falling")) d_ff_22 (
    .D(j_k_ff_16_q), .clk(or_24_out), .Q(d_ff_22_q));  // open: Qn, preset, reset
  J_K_Flip_Flop j_k_ff_18 (
    .J(j_k_ff_15_q), .K(j_k_ff_15_q), .clk(and_65_out), .Q(j_k_ff_18_q), .reset(and_62_out));  // open: Qn, preset
  J_K_Flip_Flop j_k_ff_19 (
    .J(j_k_ff_16_q), .K(j_k_ff_16_q), .clk(or_24_out), .Q(j_k_ff_19_q), .reset(or_26_out));  // open: Qn, preset
  D_Flip_Flop d_ff_23 (.D(j_k_ff_18_q), .clk(and_65_out), .Q(d_ff_23_q));  // open: Qn, preset, reset
  J_K_Flip_Flop j_k_ff_20 (
    .J(j_k_ff_17_q), .K(j_k_ff_17_q), .clk(d_ff_16_q), .Q(j_k_ff_20_q), .reset(and_63_out));  // open: Qn, preset
  D_Flip_Flop #(.trigger("falling")) d_ff_24 (
    .D(j_k_ff_19_q), .clk(or_24_out), .Q(d_ff_24_q));  // open: Qn, preset, reset
  and and_57 (and_57_out, j_k_ff_15_q, j_k_ff_18_q);
  J_K_Flip_Flop j_k_ff_21 (
    .J(and_57_out), .K(and_57_out), .clk(and_65_out), .Q(j_k_ff_21_q), .reset(and_62_out));  // open: Qn, preset
  and and_58 (and_58_out, j_k_ff_16_q, j_k_ff_19_q);
  J_K_Flip_Flop j_k_ff_22 (
    .J(and_58_out), .K(and_58_out), .clk(or_24_out), .Q(j_k_ff_22_q), .reset(or_26_out));  // open: Qn, preset
  and and_59 (and_59_out, j_k_ff_17_q, j_k_ff_20_q);
  D_Flip_Flop #(.trigger("falling")) d_ff_25 (
    .D(j_k_ff_20_q), .clk(d_ff_16_q), .Q(d_ff_25_q));  // open: Qn, preset, reset
  D_Flip_Flop d_ff_26 (.D(j_k_ff_21_q), .clk(and_65_out), .Q(d_ff_26_q));  // open: Qn, preset, reset
  D_Flip_Flop #(.trigger("falling")) d_ff_27 (
    .D(j_k_ff_22_q), .clk(or_24_out), .Q(d_ff_27_q));  // open: Qn, preset, reset
  and and_60 (and_60_out, and_57_out, j_k_ff_21_q);
  J_K_Flip_Flop j_k_ff_23 (
    .J(and_60_out), .K(and_60_out), .clk(and_65_out), .Q(j_k_ff_23_q), .reset(and_62_out));  // open: Qn, preset
  J_K_Flip_Flop j_k_ff_24 (
    .J(and_59_out), .K(and_59_out), .clk(d_ff_16_q), .Q(j_k_ff_24_q), .reset(and_63_out));  // open: Qn, preset
  and and_61 (and_61_out, and_58_out, j_k_ff_22_q);
  J_K_Flip_Flop j_k_ff_25 (
    .J(and_61_out), .K(and_61_out), .clk(or_24_out), .Q(j_k_ff_25_q), .reset(or_26_out));  // open: Qn, preset
  and and_62 (and_62_out, j_k_ff_23_q, j_k_ff_18_q);
  and and_63 (and_63_out, j_k_ff_24_q, j_k_ff_20_q);
  D_Flip_Flop #(.trigger("falling")) d_ff_28 (
    .D(j_k_ff_24_q), .clk(d_ff_16_q), .Q(d_ff_28_q));  // open: Qn, preset, reset
  or or_26 (or_26_out, and_64_out, and_66_out);
  D_Flip_Flop d_ff_29 (.D(j_k_ff_23_q), .clk(and_65_out), .Q(d_ff_29_q));  // open: Qn, preset, reset
  and and_64 (and_64_out, j_k_ff_25_q, j_k_ff_19_q);
  D_Flip_Flop #(.trigger("falling")) d_ff_30 (
    .D(j_k_ff_25_q), .clk(or_24_out), .Q(d_ff_30_q));  // open: Qn, preset, reset
  and and_65 (and_65_out, not_3_out, or_27_out);
  or or_27 (or_27_out, and_67_out, and_71_out);
  and and_66 (and_66_out, and_58_out, j_k_ff_14_q);
  and and_67 (and_67_out, clock_1_out, nand_2_out);
  and and_68 (and_68_out, d_ff_24_q, and_69_out);
  and and_69 (and_69_out, j_k_ff_14_q, nand_2_out);
  Clock clock_1 (.out(clock_1_out));
  and and_70 (and_70_out, not_3_out, and_73_out);
  J_K_Flip_Flop j_k_ff_26 (.J(Power), .K(Power), .clk(or_28_out), .Q(j_k_ff_26_q));  // open: Qn, preset, reset
  or or_28 (or_28_out, and_70_out, and_68_out);
  not not_3 (not_3_out, Set_alarm);
  nand nand_2 (nand_2_out, Power, StopTimer);
  and and_71 (and_71_out, StopTimer, button_1_out);
  and and_72 (and_72_out, StopTimer, button_2_out);
  and and_73 (and_73_out, StopTimer, button_3_out);
  and and_74 (and_74_out, not_3_out, and_72_out);
  and and_75 (and_75_out, and_74_out, StopTimer);
  Button button_1 (.out(button_1_out));
  Button button_2 (.out(button_2_out));
  Button button_3 (.out(button_3_out));

  // Notes on the sheet:
  //   alarm line
  //   alarm line
  //   Set minute
  //   Set hour
  //   Set am/pm
  //   time
  //   alarm line
  //   alarm
  //   alarm mode
  //   am/pm
  //   clock line
  //   clock line
  //   on (red) = pm
  //   off (black) = am
  //   Set minute
  //   Set hour
  //   Set am/pm
endmodule

module Test (
  input  in_1,
  input  in_2,
  input  in_3,
  input  in_4
);

  wire and_1_out, and_2_out, and_3_out, and_4_out, and_5_out, and_6_out, and_7_out, and_8_out, and_9_out,
       and_10_out, and_11_out, and_12_out, and_13_out, and_14_out, and_15_out, and_16_out, and_17_out,
       and_18_out, and_19_out, button_1_out, button_2_out, button_3_out, clock_1_out, d_ff_1_q, d_ff_2_q,
       d_ff_3_q, j_k_ff_1_q, j_k_ff_2_q, j_k_ff_3_q, j_k_ff_4_q, j_k_ff_5_q, j_k_ff_6_q, j_k_ff_7_q,
       j_k_ff_8_q, j_k_ff_9_q, j_k_ff_10_q, j_k_ff_11_q, j_k_ff_12_q, j_k_ff_13_q, j_k_ff_14_qn, not_1_out,
       or_1_out, or_2_out, or_3_out, or_4_out, or_5_out, or_6_out, or_7_out, or_8_out, or_9_out, or_10_out,
       or_12_out;
  wire [2:0] d_ff_6_q, d_ff_7_q;
  wire [3:0] d_ff_4_q, d_ff_5_q;

  or or_1 (or_1_out, or_3_out, and_19_out);
  and and_1 (and_1_out, and_3_out, or_7_out);
  or or_2 (or_2_out, and_2_out, and_19_out);
  or or_3 (or_3_out, or_10_out, and_19_out);
  or or_4 (or_4_out, or_1_out, and_19_out);
  and and_2 (and_2_out, and_1_out, or_6_out);
  D_Flip_Flop d_ff_1 (.D(or_2_out), .clk(or_4_out), .Q(d_ff_1_q));  // open: Qn, preset, reset
  D_Flip_Flop d_ff_2 (.D(or_8_out), .clk(or_3_out), .Q(d_ff_2_q));  // open: Qn, preset, reset
  and and_3 (and_3_out, or_8_out, or_7_out);
  D_Flip_Flop d_ff_3 (.D(and_3_out), .clk(or_4_out), .Q(d_ff_3_q));  // open: Qn, preset, reset
  or or_5 (or_5_out, d_ff_3_q, and_19_out);
  and and_4 (and_4_out, j_k_ff_13_q, j_k_ff_3_q);
  J_K_Flip_Flop j_k_ff_1 (.J(in_1), .K(in_1), .clk(or_10_out), .Q(j_k_ff_1_q), .reset(and_12_out));  // open: Qn, preset
  and and_5 (and_5_out, j_k_ff_2_q, j_k_ff_12_q);
  or or_6 (or_6_out, and_4_out, and_19_out);
  and and_6 (and_6_out, j_k_ff_1_q, j_k_ff_11_q);
  J_K_Flip_Flop j_k_ff_2 (
    .J(or_8_out), .K(or_8_out), .clk(d_ff_2_q), .Q(j_k_ff_2_q), .reset(and_13_out));  // open: Qn, preset
  or or_7 (or_7_out, and_5_out, and_19_out);
  J_K_Flip_Flop j_k_ff_3 (.J(or_7_out), .K(or_7_out), .clk(or_5_out), .Q(j_k_ff_3_q));  // open: Qn, preset, reset
  J_K_Flip_Flop j_k_ff_4 (
    .J(d_ff_1_q), .K(d_ff_1_q), .clk(d_ff_1_q), .Q(j_k_ff_4_q), .reset(and_15_out));  // open: Qn, preset
  D_Flip_Flop d_ff_4 (.D(j_k_ff_1_q), .clk(or_10_out), .Q(d_ff_4_q[0]));  // open: Qn, preset, reset
  or or_8 (or_8_out, and_6_out, and_19_out);
  D_Flip_Flop #(.trigger("falling")) d_ff_5 (
    .D(j_k_ff_3_q), .clk(or_5_out), .Q(d_ff_5_q[0]));  // open: Qn, preset, reset
  D_Flip_Flop #(.trigger("falling")) d_ff_6 (
    .D(j_k_ff_4_q), .clk(d_ff_1_q), .Q(d_ff_6_q[0]), .reset(and_15_out));  // open: Qn, preset
  J_K_Flip_Flop j_k_ff_5 (
    .J(j_k_ff_1_q), .K(j_k_ff_1_q), .clk(or_10_out), .Q(j_k_ff_5_q), .reset(and_12_out));  // open: Qn, preset
  D_Flip_Flop #(.trigger("falling")) d_ff_7 (
    .D(j_k_ff_2_q), .clk(d_ff_2_q), .Q(d_ff_7_q[0]));  // open: Qn, preset, reset
  J_K_Flip_Flop j_k_ff_6 (
    .J(j_k_ff_3_q), .K(j_k_ff_3_q), .clk(or_5_out), .Q(j_k_ff_6_q), .reset(or_9_out));  // open: Qn, preset
  D_Flip_Flop d_ff_8 (.D(j_k_ff_5_q), .clk(or_10_out), .Q(d_ff_4_q[1]));  // open: Qn, preset, reset
  J_K_Flip_Flop j_k_ff_7 (
    .J(j_k_ff_2_q), .K(j_k_ff_2_q), .clk(d_ff_2_q), .Q(j_k_ff_7_q), .reset(and_13_out));  // open: Qn, preset
  J_K_Flip_Flop j_k_ff_8 (
    .J(j_k_ff_4_q), .K(j_k_ff_4_q), .clk(d_ff_1_q), .Q(j_k_ff_8_q), .reset(and_15_out));  // open: Qn, preset
  and and_7 (and_7_out, j_k_ff_1_q, j_k_ff_5_q);
  J_K_Flip_Flop j_k_ff_9 (
    .J(and_7_out), .K(and_7_out), .clk(or_10_out), .Q(j_k_ff_9_q), .reset(and_12_out));  // open: Qn, preset
  and and_8 (and_8_out, j_k_ff_3_q, j_k_ff_6_q);
  D_Flip_Flop #(.trigger("falling")) d_ff_9 (
    .D(j_k_ff_6_q), .clk(or_5_out), .Q(d_ff_5_q[1]));  // open: Qn, preset, reset
  D_Flip_Flop #(.trigger("falling")) d_ff_10 (
    .D(j_k_ff_8_q), .clk(d_ff_1_q), .Q(d_ff_6_q[2]));  // open: Qn, preset, reset
  D_Flip_Flop #(.trigger("falling")) d_ff_11 (
    .D(j_k_ff_7_q), .clk(d_ff_2_q), .Q(d_ff_7_q[1]));  // open: Qn, preset, reset
  J_K_Flip_Flop j_k_ff_10 (
    .J(and_8_out), .K(and_8_out), .clk(or_5_out), .Q(j_k_ff_10_q), .reset(or_9_out));  // open: Qn, preset
  D_Flip_Flop d_ff_12 (.D(j_k_ff_9_q), .clk(or_10_out), .Q(d_ff_4_q[2]));  // open: Qn, preset, reset
  and and_9 (and_9_out, j_k_ff_2_q, j_k_ff_7_q);
  and and_10 (and_10_out, and_7_out, j_k_ff_9_q);
  J_K_Flip_Flop j_k_ff_11 (
    .J(and_10_out), .K(and_10_out), .clk(or_10_out), .Q(j_k_ff_11_q), .reset(and_12_out));  // open: Qn, preset
  J_K_Flip_Flop j_k_ff_12 (
    .J(and_9_out), .K(and_9_out), .clk(d_ff_2_q), .Q(j_k_ff_12_q), .reset(and_13_out));  // open: Qn, preset
  and and_11 (and_11_out, and_8_out, j_k_ff_10_q);
  J_K_Flip_Flop j_k_ff_13 (
    .J(and_11_out), .K(and_11_out), .clk(or_5_out), .Q(j_k_ff_13_q), .reset(or_9_out));  // open: Qn, preset
  D_Flip_Flop #(.trigger("falling")) d_ff_13 (
    .D(j_k_ff_10_q), .clk(or_5_out), .Q(d_ff_5_q[2]));  // open: Qn, preset, reset
  D_Flip_Flop #(.trigger("falling")) d_ff_14 (
    .D(j_k_ff_12_q), .clk(d_ff_2_q), .Q(d_ff_7_q[2]));  // open: Qn, preset, reset
  and and_12 (and_12_out, j_k_ff_11_q, j_k_ff_5_q);
  D_Flip_Flop d_ff_15 (.D(j_k_ff_11_q), .clk(or_10_out), .Q(d_ff_4_q[3]));  // open: Qn, preset, reset
  and and_13 (and_13_out, j_k_ff_12_q, j_k_ff_7_q);
  and and_14 (and_14_out, j_k_ff_13_q, j_k_ff_6_q);
  D_Flip_Flop #(.trigger("falling")) d_ff_16 (
    .D(j_k_ff_13_q), .clk(or_5_out), .Q(d_ff_5_q[3]));  // open: Qn, preset, reset
  or or_9 (or_9_out, and_14_out, and_15_out);
  Hex_Digit_Display hex_digit_display_1 (.value({in_4, {2{d_ff_6_q[2]}}, d_ff_6_q[0]}));  // open: dp
  or or_10 (or_10_out, and_16_out, and_17_out);
  // OR_Gate or_11 is placed but not wired
  Hex_Digit_Display hex_digit_display_2 (.value(d_ff_5_q));  // open: dp
  Hex_Digit_Display hex_digit_display_3 (.value({in_3, d_ff_7_q}));  // open: dp
  and and_15 (and_15_out, and_8_out, j_k_ff_4_q);
  and and_16 (and_16_out, clock_1_out, not_1_out);
  and and_17 (and_17_out, in_2, button_1_out);
  Hex_Digit_Display hex_digit_display_4 (.value(d_ff_4_q));  // open: dp
  LED led_1 (.in(j_k_ff_14_qn));
  Clock clock_1 (.out(clock_1_out));
  not not_1 (not_1_out, in_2);
  Button button_1 (.out(button_1_out));
  Button button_2 (.out(button_2_out));
  Button button_3 (.out(button_3_out));
  and and_18 (and_18_out, d_ff_5_q[1], j_k_ff_4_q);
  or or_12 (or_12_out, and_18_out, button_3_out);
  and and_19 (and_19_out, in_2, button_2_out);
  J_K_Flip_Flop j_k_ff_14 (.J(in_1), .K(in_1), .clk(or_12_out), .Qn(j_k_ff_14_qn));  // open: Q, preset, reset

  // Notes on the sheet:
  //   Set minute
  //   Set am/pm
endmodule

module Test2 (
  input  Power,
  input  StopTimer,
  input  in_3,
  input  in_4
);

  wire and_1_out, and_2_out, and_3_out, and_4_out, and_5_out, and_6_out, and_7_out, and_8_out, and_9_out,
       and_10_out, and_11_out, and_12_out, and_13_out, and_14_out, and_15_out, and_16_out, and_17_out,
       and_18_out, and_19_out, and_20_out, and_21_out, and_22_out, button_1_out, button_2_out, button_3_out,
       clock_1_out, d_ff_1_q, d_ff_2_q, d_ff_3_q, j_k_ff_1_q, j_k_ff_2_q, j_k_ff_3_q, j_k_ff_4_q, j_k_ff_5_q,
       j_k_ff_6_q, j_k_ff_7_q, j_k_ff_9_q, j_k_ff_10_q, j_k_ff_11_q, j_k_ff_12_q, j_k_ff_13_q, j_k_ff_14_qn,
       not_1_out, or_1_out, or_2_out, or_3_out, or_4_out, or_5_out, or_6_out;
  wire [0:0] d_ff_6_q;
  wire [2:0] d_ff_7_q;
  wire [3:0] d_ff_4_q, d_ff_5_q;

  and and_1 (and_1_out, and_3_out, or_2_out);
  or or_1 (or_1_out, d_ff_1_q, and_12_out);
  and and_2 (and_2_out, and_1_out, and_4_out);
  D_Flip_Flop d_ff_1 (.D(and_2_out), .clk(or_5_out), .Q(d_ff_1_q));  // open: Qn, preset, reset
  D_Flip_Flop d_ff_2 (.D(and_6_out), .clk(or_5_out), .Q(d_ff_2_q));  // open: Qn, preset, reset
  and and_3 (and_3_out, and_6_out, or_2_out);
  D_Flip_Flop d_ff_3 (.D(and_3_out), .clk(or_5_out), .Q(d_ff_3_q));  // open: Qn, preset, reset
  and and_4 (and_4_out, j_k_ff_13_q, j_k_ff_3_q);
  J_K_Flip_Flop j_k_ff_1 (
    .J(Power), .K(Power), .clk(or_5_out), .Q(j_k_ff_1_q), .reset(and_13_out));  // open: Qn, preset
  and and_5 (and_5_out, j_k_ff_2_q, j_k_ff_12_q);
  or or_2 (or_2_out, and_5_out, and_21_out);
  or or_3 (or_3_out, d_ff_3_q, and_21_out);
  and and_6 (and_6_out, j_k_ff_1_q, j_k_ff_11_q);
  J_K_Flip_Flop j_k_ff_2 (
    .J(and_6_out), .K(and_6_out), .clk(d_ff_2_q), .Q(j_k_ff_2_q), .reset(and_14_out));  // open: Qn, preset
  J_K_Flip_Flop j_k_ff_3 (.J(or_2_out), .K(or_2_out), .clk(or_3_out), .Q(j_k_ff_3_q));  // open: Qn, preset, reset
  J_K_Flip_Flop j_k_ff_4 (
    .J(or_1_out), .K(or_1_out), .clk(or_1_out), .Q(j_k_ff_4_q), .reset(and_16_out));  // open: Qn, preset
  D_Flip_Flop d_ff_4 (.D(j_k_ff_1_q), .clk(or_5_out), .Q(d_ff_4_q[0]));  // open: Qn, preset, reset
  D_Flip_Flop #(.trigger("falling")) d_ff_5 (
    .D(j_k_ff_3_q), .clk(or_3_out), .Q(d_ff_5_q[0]));  // open: Qn, preset, reset
  D_Flip_Flop #(.trigger("falling")) d_ff_6 (
    .D(j_k_ff_4_q), .clk(or_1_out), .Q(d_ff_6_q[0]), .reset(and_16_out));  // open: Qn, preset
  J_K_Flip_Flop j_k_ff_5 (
    .J(j_k_ff_1_q), .K(j_k_ff_1_q), .clk(or_5_out), .Q(j_k_ff_5_q), .reset(and_13_out));  // open: Qn, preset
  D_Flip_Flop #(.trigger("falling")) d_ff_7 (
    .D(j_k_ff_2_q), .clk(d_ff_2_q), .Q(d_ff_7_q[0]));  // open: Qn, preset, reset
  J_K_Flip_Flop j_k_ff_6 (
    .J(j_k_ff_3_q), .K(j_k_ff_3_q), .clk(or_3_out), .Q(j_k_ff_6_q), .reset(or_4_out));  // open: Qn, preset
  D_Flip_Flop d_ff_8 (.D(j_k_ff_5_q), .clk(or_5_out), .Q(d_ff_4_q[1]));  // open: Qn, preset, reset
  J_K_Flip_Flop j_k_ff_7 (
    .J(j_k_ff_2_q), .K(j_k_ff_2_q), .clk(d_ff_2_q), .Q(j_k_ff_7_q), .reset(and_14_out));  // open: Qn, preset
  J_K_Flip_Flop j_k_ff_8 (.J(j_k_ff_4_q), .K(j_k_ff_4_q), .clk(or_1_out));  // open: Q, Qn, preset, reset
  and and_7 (and_7_out, j_k_ff_1_q, j_k_ff_5_q);
  J_K_Flip_Flop j_k_ff_9 (
    .J(and_7_out), .K(and_7_out), .clk(or_5_out), .Q(j_k_ff_9_q), .reset(and_13_out));  // open: Qn, preset
  and and_8 (and_8_out, j_k_ff_3_q, j_k_ff_6_q);
  D_Flip_Flop #(.trigger("falling")) d_ff_9 (
    .D(j_k_ff_6_q), .clk(or_3_out), .Q(d_ff_5_q[1]));  // open: Qn, preset, reset
  D_Flip_Flop #(.trigger("falling")) d_ff_10 (
    .D(j_k_ff_7_q), .clk(d_ff_2_q), .Q(d_ff_7_q[1]));  // open: Qn, preset, reset
  J_K_Flip_Flop j_k_ff_10 (
    .J(and_8_out), .K(and_8_out), .clk(or_3_out), .Q(j_k_ff_10_q), .reset(or_4_out));  // open: Qn, preset
  D_Flip_Flop d_ff_11 (.D(j_k_ff_9_q), .clk(or_5_out), .Q(d_ff_4_q[2]));  // open: Qn, preset, reset
  and and_9 (and_9_out, j_k_ff_2_q, j_k_ff_7_q);
  and and_10 (and_10_out, and_7_out, j_k_ff_9_q);
  J_K_Flip_Flop j_k_ff_11 (
    .J(and_10_out), .K(and_10_out), .clk(or_5_out), .Q(j_k_ff_11_q), .reset(and_13_out));  // open: Qn, preset
  J_K_Flip_Flop j_k_ff_12 (
    .J(and_9_out), .K(and_9_out), .clk(d_ff_2_q), .Q(j_k_ff_12_q), .reset(and_14_out));  // open: Qn, preset
  and and_11 (and_11_out, and_8_out, j_k_ff_10_q);
  J_K_Flip_Flop j_k_ff_13 (
    .J(and_11_out), .K(and_11_out), .clk(or_3_out), .Q(j_k_ff_13_q), .reset(or_4_out));  // open: Qn, preset
  D_Flip_Flop #(.trigger("falling")) d_ff_12 (
    .D(j_k_ff_10_q), .clk(or_3_out), .Q(d_ff_5_q[2]));  // open: Qn, preset, reset
  D_Flip_Flop #(.trigger("falling")) d_ff_13 (
    .D(j_k_ff_12_q), .clk(d_ff_2_q), .Q(d_ff_7_q[2]));  // open: Qn, preset, reset
  and and_12 (and_12_out, j_k_ff_13_q, StopTimer);
  and and_13 (and_13_out, j_k_ff_11_q, j_k_ff_5_q);
  D_Flip_Flop d_ff_14 (.D(j_k_ff_11_q), .clk(or_5_out), .Q(d_ff_4_q[3]));  // open: Qn, preset, reset
  and and_14 (and_14_out, j_k_ff_12_q, j_k_ff_7_q);
  and and_15 (and_15_out, j_k_ff_13_q, j_k_ff_6_q);
  D_Flip_Flop #(.trigger("falling")) d_ff_15 (
    .D(j_k_ff_13_q), .clk(or_3_out), .Q(d_ff_5_q[3]));  // open: Qn, preset, reset
  or or_4 (or_4_out, and_15_out, and_16_out);
  or or_5 (or_5_out, and_17_out, and_18_out);
  Hex_Digit_Display hex_digit_display_1 (.value({{3{in_4}}, d_ff_6_q[0]}));  // open: dp
  Hex_Digit_Display hex_digit_display_2 (.value(d_ff_5_q));  // open: dp
  Hex_Digit_Display hex_digit_display_3 (.value({in_3, d_ff_7_q}));  // open: dp
  and and_16 (and_16_out, and_8_out, j_k_ff_4_q);
  and and_17 (and_17_out, clock_1_out, not_1_out);
  and and_18 (and_18_out, StopTimer, button_1_out);
  Hex_Digit_Display hex_digit_display_4 (.value(d_ff_4_q));  // open: dp
  LED led_1 (.in(j_k_ff_14_qn));
  and and_19 (and_19_out, d_ff_5_q[1], and_20_out);
  and and_20 (and_20_out, j_k_ff_4_q, not_1_out);
  Clock clock_1 (.out(clock_1_out));
  not not_1 (not_1_out, StopTimer);
  Button button_1 (.out(button_1_out));
  Button button_2 (.out(button_2_out));
  Button button_3 (.out(button_3_out));
  J_K_Flip_Flop j_k_ff_14 (.J(Power), .K(Power), .clk(or_6_out), .Qn(j_k_ff_14_qn));  // open: Q, preset, reset
  or or_6 (or_6_out, and_19_out, and_22_out);
  and and_21 (and_21_out, StopTimer, button_2_out);
  and and_22 (and_22_out, StopTimer, button_3_out);

  // Notes on the sheet:
  //   Time
  //   am/pm
  //   Set minute
  //   Set hour
  //   Set am/pm
endmodule

module TestAlarm (
  input  Power,
  input  StopTimer,
  input  Set_alarm,
  input  in_4
);

  wire and_1_out, and_2_out, and_3_out, and_4_out, and_5_out, and_6_out, and_7_out, and_8_out, and_9_out,
       and_10_out, and_11_out, and_12_out, and_13_out, and_14_out, and_15_out, and_16_out, and_17_out,
       and_18_out, and_19_out, and_20_out, and_21_out, and_22_out, and_23_out, and_24_out, and_25_out,
       and_26_out, and_27_out, and_28_out, and_29_out, and_30_out, and_31_out, and_32_out, and_33_out,
       and_34_out, and_35_out, and_36_out, and_37_out, and_38_out, and_39_out, and_40_out, and_41_out,
       and_42_out, and_43_out, and_44_out, and_45_out, and_46_out, and_47_out, and_48_out, and_49_out,
       and_50_out, and_51_out, and_52_out, and_53_out, and_54_out, and_55_out, and_56_out, and_57_out,
       and_58_out, and_59_out, and_60_out, and_61_out, and_62_out, and_63_out, and_64_out, and_65_out,
       and_66_out, and_67_out, and_68_out, and_69_out, and_70_out, and_71_out, and_72_out, and_73_out,
       and_74_out, and_75_out, button_1_out, button_2_out, button_3_out, clock_1_out, d_ff_1_q, d_ff_2_q,
       d_ff_3_q, d_ff_4_q, d_ff_5_q, d_ff_6_q, d_ff_7_q, d_ff_8_q, d_ff_9_q, d_ff_10_q, d_ff_11_q, d_ff_12_q,
       d_ff_13_q, d_ff_14_q, d_ff_15_q, d_ff_16_q, d_ff_17_q, d_ff_18_q, d_ff_19_q, d_ff_20_q, d_ff_21_q,
       d_ff_22_q, d_ff_23_q, d_ff_24_q, d_ff_25_q, d_ff_26_q, d_ff_27_q, d_ff_28_q, d_ff_29_q, d_ff_30_q,
       j_k_ff_1_q, j_k_ff_2_q, j_k_ff_3_q, j_k_ff_4_q, j_k_ff_5_q, j_k_ff_6_q, j_k_ff_7_q, j_k_ff_8_q,
       j_k_ff_9_q, j_k_ff_10_q, j_k_ff_11_q, j_k_ff_12_q, j_k_ff_13_q, j_k_ff_14_q, j_k_ff_15_q, j_k_ff_16_q,
       j_k_ff_17_q, j_k_ff_18_q, j_k_ff_19_q, j_k_ff_20_q, j_k_ff_21_q, j_k_ff_22_q, j_k_ff_23_q,
       j_k_ff_24_q, j_k_ff_25_q, j_k_ff_26_q, nand_1_out, nand_2_out, not_1_out, not_2_out, not_3_out,
       or_1_out, or_2_out, or_3_out, or_4_out, or_5_out, or_6_out, or_7_out, or_17_out, or_18_out, or_22_out,
       or_23_out, or_24_out, or_25_out, or_26_out, or_27_out, or_28_out, xnor_1_out, xnor_2_out, xnor_3_out,
       xnor_4_out, xnor_5_out, xnor_6_out, xnor_7_out, xnor_8_out, xnor_9_out, xnor_10_out, xnor_11_out,
       xnor_12_out, xnor_13_out;
  wire [0:0] or_10_out;
  wire [2:0] or_12_out;
  wire [3:0] or_14_out, or_21_out;

  and and_1 (and_1_out, and_2_out, j_k_ff_6_q);
  or or_1 (or_1_out, and_1_out, and_3_out);
  or or_2 (or_2_out, or_1_out, and_4_out);
  D_Flip_Flop d_ff_1 (.D(and_7_out), .clk(and_19_out), .Q(d_ff_1_q));  // open: Qn, preset, reset
  and and_2 (and_2_out, and_7_out, or_4_out);
  D_Flip_Flop d_ff_2 (.D(and_2_out), .clk(and_19_out), .Q(d_ff_2_q));  // open: Qn, preset, reset
  and and_3 (and_3_out, and_2_out, and_4_out);
  D_Flip_Flop d_ff_3 (.D(or_2_out), .clk(and_19_out), .Q(d_ff_3_q));  // open: Qn, preset, reset
  and and_4 (and_4_out, j_k_ff_12_q, j_k_ff_4_q);
  and and_5 (and_5_out, d_ff_3_q, nand_1_out);
  or or_3 (or_3_out, and_5_out, and_22_out);
  J_K_Flip_Flop j_k_ff_1 (
    .J(Power), .K(Power), .clk(and_19_out), .Q(j_k_ff_1_q), .reset(and_13_out));  // open: Qn, preset
  and and_6 (and_6_out, j_k_ff_3_q, j_k_ff_11_q);
  or or_4 (or_4_out, and_6_out, and_20_out);
  or or_5 (or_5_out, d_ff_2_q, and_20_out);
  J_K_Flip_Flop j_k_ff_2 (
    .J(and_4_out), .K(and_4_out), .clk(or_3_out), .Q(j_k_ff_2_q), .reset(and_16_out));  // open: Qn, preset
  and and_7 (and_7_out, j_k_ff_1_q, j_k_ff_10_q);
  J_K_Flip_Flop j_k_ff_3 (
    .J(and_7_out), .K(and_7_out), .clk(d_ff_1_q), .Q(j_k_ff_3_q), .reset(and_14_out));  // open: Qn, preset
  J_K_Flip_Flop j_k_ff_4 (.J(or_4_out), .K(or_4_out), .clk(or_5_out), .Q(j_k_ff_4_q));  // open: Qn, preset, reset
  D_Flip_Flop #(.trigger("falling")) d_ff_4 (.D(j_k_ff_2_q), .clk(or_3_out), .Q(d_ff_4_q));  // open: Qn, preset, reset
  D_Flip_Flop d_ff_5 (.D(j_k_ff_1_q), .clk(and_19_out), .Q(d_ff_5_q));  // open: Qn, preset, reset
  D_Flip_Flop #(.trigger("falling")) d_ff_6 (.D(j_k_ff_4_q), .clk(or_5_out), .Q(d_ff_6_q));  // open: Qn, preset, reset
  J_K_Flip_Flop j_k_ff_5 (
    .J(j_k_ff_1_q), .K(j_k_ff_1_q), .clk(and_19_out), .Q(j_k_ff_5_q), .reset(and_13_out));  // open: Qn, preset
  D_Flip_Flop #(.trigger("falling")) d_ff_7 (.D(j_k_ff_3_q), .clk(d_ff_1_q), .Q(d_ff_7_q));  // open: Qn, preset, reset
  J_K_Flip_Flop j_k_ff_6 (
    .J(j_k_ff_4_q), .K(j_k_ff_4_q), .clk(or_5_out), .Q(j_k_ff_6_q), .reset(or_6_out));  // open: Qn, preset
  D_Flip_Flop d_ff_8 (.D(j_k_ff_5_q), .clk(and_19_out), .Q(d_ff_8_q));  // open: Qn, preset, reset
  J_K_Flip_Flop j_k_ff_7 (
    .J(j_k_ff_3_q), .K(j_k_ff_3_q), .clk(d_ff_1_q), .Q(j_k_ff_7_q), .reset(and_14_out));  // open: Qn, preset
  and and_8 (and_8_out, j_k_ff_1_q, j_k_ff_5_q);
  J_K_Flip_Flop j_k_ff_8 (
    .J(and_8_out), .K(and_8_out), .clk(and_19_out), .Q(j_k_ff_8_q), .reset(and_13_out));  // open: Qn, preset
  and and_9 (and_9_out, j_k_ff_4_q, j_k_ff_6_q);
  J_K_Flip_Flop j_k_ff_9 (
    .J(and_9_out), .K(and_9_out), .clk(or_5_out), .Q(j_k_ff_9_q), .reset(or_6_out));  // open: Qn, preset
  D_Flip_Flop #(.trigger("falling")) d_ff_9 (.D(j_k_ff_6_q), .clk(or_5_out), .Q(d_ff_9_q));  // open: Qn, preset, reset
  D_Flip_Flop #(.trigger("falling")) d_ff_10 (
    .D(j_k_ff_7_q), .clk(d_ff_1_q), .Q(d_ff_10_q));  // open: Qn, preset, reset
  D_Flip_Flop d_ff_11 (.D(j_k_ff_8_q), .clk(and_19_out), .Q(d_ff_11_q));  // open: Qn, preset, reset
  and and_10 (and_10_out, j_k_ff_3_q, j_k_ff_7_q);
  D_Flip_Flop #(.trigger("falling")) d_ff_12 (
    .D(j_k_ff_9_q), .clk(or_5_out), .Q(d_ff_12_q));  // open: Qn, preset, reset
  and and_11 (and_11_out, and_8_out, j_k_ff_8_q);
  J_K_Flip_Flop j_k_ff_10 (
    .J(and_11_out), .K(and_11_out), .clk(and_19_out), .Q(j_k_ff_10_q), .reset(and_13_out));  // open: Qn, preset
  J_K_Flip_Flop j_k_ff_11 (
    .J(and_10_out), .K(and_10_out), .clk(d_ff_1_q), .Q(j_k_ff_11_q), .reset(and_14_out));  // open: Qn, preset
  and and_12 (and_12_out, and_9_out, j_k_ff_9_q);
  J_K_Flip_Flop j_k_ff_12 (
    .J(and_12_out), .K(and_12_out), .clk(or_5_out), .Q(j_k_ff_12_q), .reset(or_6_out));  // open: Qn, preset
  D_Flip_Flop #(.trigger("falling")) d_ff_13 (
    .D(j_k_ff_11_q), .clk(d_ff_1_q), .Q(d_ff_13_q));  // open: Qn, preset, reset
  or or_6 (or_6_out, and_15_out, and_16_out);
  and and_13 (and_13_out, j_k_ff_10_q, j_k_ff_5_q);
  D_Flip_Flop d_ff_14 (.D(j_k_ff_10_q), .clk(and_19_out), .Q(d_ff_14_q));  // open: Qn, preset, reset
  and and_14 (and_14_out, j_k_ff_11_q, j_k_ff_7_q);
  and and_15 (and_15_out, j_k_ff_12_q, j_k_ff_6_q);
  D_Flip_Flop #(.trigger("falling")) d_ff_15 (
    .D(j_k_ff_12_q), .clk(or_5_out), .Q(d_ff_15_q));  // open: Qn, preset, reset
  and and_16 (and_16_out, and_9_out, j_k_ff_2_q);
  and and_17 (and_17_out, j_k_ff_2_q, nand_1_out);
  or or_7 (or_7_out, and_21_out, and_18_out);
  and and_18 (and_18_out, d_ff_9_q, and_17_out);
  nand nand_1 (nand_1_out, Power, Set_alarm);
  and and_19 (and_19_out, Set_alarm, button_1_out);
  and and_20 (and_20_out, Set_alarm, button_2_out);
  and and_21 (and_21_out, Set_alarm, button_3_out);
  and and_22 (and_22_out, and_20_out, Set_alarm);
  J_K_Flip_Flop j_k_ff_13 (.J(Power), .K(Power), .clk(or_7_out), .Q(j_k_ff_13_q));  // open: Qn, preset, reset
  Hex_Digit_Display hex_digit_display_1 (.value({{3{in_4}}, or_10_out[0]}));  // open: dp
  or or_8 (or_12_out[1], and_23_out, and_24_out);
  and and_23 (and_23_out, Set_alarm, d_ff_10_q);
  and and_24 (and_24_out, d_ff_25_q, not_1_out);
  or or_9 (or_14_out[2], and_25_out, and_26_out);
  and and_25 (and_25_out, Set_alarm, d_ff_12_q);
  and and_26 (and_26_out, d_ff_27_q, not_2_out);
  or or_10 (or_10_out[0], and_27_out, and_30_out);
  and and_27 (and_27_out, Set_alarm, d_ff_4_q);
  xnor xnor_1 (xnor_1_out, d_ff_4_q, d_ff_19_q);
  xnor xnor_2 (xnor_2_out, d_ff_15_q, d_ff_30_q);
  Hex_Digit_Display hex_digit_display_2 (.value(or_14_out));  // open: dp
  Hex_Digit_Display hex_digit_display_3 (.value({in_4, or_12_out}));  // open: dp
  or or_11 (or_14_out[3], and_28_out, and_29_out);
  and and_28 (and_28_out, Set_alarm, d_ff_15_q);
  and and_29 (and_29_out, d_ff_30_q, not_2_out);
  and and_30 (and_30_out, d_ff_19_q, not_2_out);
  xnor xnor_3 (xnor_3_out, d_ff_12_q, d_ff_27_q);
  xnor xnor_4 (xnor_4_out, d_ff_9_q, d_ff_24_q);
  LED led_1 (.in(and_39_out));
  LED led_2 (.in(Set_alarm));
  LED led_3 (.in(or_25_out));
  Hex_Digit_Display hex_digit_display_4 (.value(or_21_out));  // open: dp
  or or_12 (or_12_out[0], and_31_out, and_32_out);
  and and_31 (and_31_out, Set_alarm, d_ff_7_q);
  and and_32 (and_32_out, d_ff_21_q, not_1_out);
  or or_13 (or_12_out[2], and_33_out, and_34_out);
  and and_33 (and_33_out, Set_alarm, d_ff_13_q);
  and and_34 (and_34_out, d_ff_28_q, not_1_out);
  not not_1 (not_1_out, Set_alarm);
  or or_14 (or_14_out[0], and_35_out, and_36_out);
  and and_35 (and_35_out, Set_alarm, d_ff_6_q);
  and and_36 (and_36_out, d_ff_22_q, not_2_out);
  or or_15 (or_14_out[1], and_37_out, and_38_out);
  and and_37 (and_37_out, Set_alarm, d_ff_9_q);
  and and_38 (and_38_out, d_ff_24_q, not_2_out);
  not not_2 (not_2_out, Set_alarm);
  xnor xnor_5 (xnor_5_out, d_ff_7_q, d_ff_21_q);
  xnor xnor_6 (xnor_6_out, d_ff_6_q, d_ff_22_q);
  and and_39 (and_39_out, xnor_1_out, xnor_2_out, xnor_3_out, xnor_4_out, xnor_6_out, xnor_5_out, xnor_7_out, xnor_8_out, xnor_9_out, xnor_10_out, xnor_11_out, xnor_12_out, xnor_13_out);
  or or_16 (or_21_out[3], and_40_out, and_41_out);
  and and_40 (and_40_out, Set_alarm, d_ff_14_q);
  and and_41 (and_41_out, d_ff_29_q, not_1_out);
  and and_42 (and_42_out, and_45_out, j_k_ff_19_q);
  or or_17 (or_17_out, and_42_out, and_46_out);
  or or_18 (or_18_out, or_17_out, and_51_out);
  xnor xnor_7 (xnor_7_out, d_ff_10_q, d_ff_25_q);
  xnor xnor_8 (xnor_8_out, d_ff_13_q, d_ff_28_q);
  or or_19 (or_21_out[2], and_43_out, and_44_out);
  and and_43 (and_43_out, Set_alarm, d_ff_11_q);
  and and_44 (and_44_out, d_ff_26_q, not_1_out);
  D_Flip_Flop d_ff_16 (.D(and_53_out), .clk(and_65_out), .Q(d_ff_16_q));  // open: Qn, preset, reset
  and and_45 (and_45_out, and_53_out, or_23_out);
  D_Flip_Flop d_ff_17 (.D(and_45_out), .clk(and_65_out), .Q(d_ff_17_q));  // open: Qn, preset, reset
  and and_46 (and_46_out, and_45_out, and_51_out);
  D_Flip_Flop d_ff_18 (.D(or_18_out), .clk(and_65_out), .Q(d_ff_18_q));  // open: Qn, preset, reset
  xnor xnor_9 (xnor_9_out, d_ff_5_q, d_ff_20_q);
  xnor xnor_10 (xnor_10_out, d_ff_8_q, d_ff_23_q);
  or or_20 (or_21_out[1], and_47_out, and_48_out);
  and and_47 (and_47_out, Set_alarm, d_ff_8_q);
  and and_48 (and_48_out, d_ff_23_q, not_1_out);
  xnor xnor_11 (xnor_11_out, d_ff_11_q, d_ff_26_q);
  xnor xnor_12 (xnor_12_out, d_ff_14_q, d_ff_29_q);
  or or_21 (or_21_out[0], and_49_out, and_50_out);
  and and_49 (and_49_out, Set_alarm, d_ff_5_q);
  and and_50 (and_50_out, d_ff_20_q, not_1_out);
  and and_51 (and_51_out, j_k_ff_25_q, j_k_ff_16_q);
  J_K_Flip_Flop j_k_ff_14 (
    .J(and_51_out), .K(and_51_out), .clk(or_22_out), .Q(j_k_ff_14_q), .reset(and_66_out));  // open: Qn, preset
  and and_52 (and_52_out, d_ff_18_q, nand_2_out);
  or or_22 (or_22_out, and_52_out, and_75_out);
  xnor xnor_13 (xnor_13_out, j_k_ff_13_q, j_k_ff_26_q);
  J_K_Flip_Flop j_k_ff_15 (
    .J(Power), .K(Power), .clk(and_65_out), .Q(j_k_ff_15_q), .reset(and_62_out));  // open: Qn, preset
  and and_53 (and_53_out, j_k_ff_15_q, j_k_ff_23_q);
  and and_54 (and_54_out, j_k_ff_17_q, j_k_ff_24_q);
  or or_23 (or_23_out, and_54_out, and_74_out);
  J_K_Flip_Flop j_k_ff_16 (.J(or_23_out), .K(or_23_out), .clk(or_24_out), .Q(j_k_ff_16_q));  // open: Qn, preset, reset
  or or_24 (or_24_out, d_ff_17_q, and_74_out);
  D_Flip_Flop #(.trigger("falling")) d_ff_19 (
    .D(j_k_ff_14_q), .clk(or_22_out), .Q(d_ff_19_q));  // open: Qn, preset, reset
  D_Flip_Flop d_ff_20 (.D(j_k_ff_15_q), .clk(and_65_out), .Q(d_ff_20_q));  // open: Qn, preset, reset
  and and_55 (and_55_out, Set_alarm, j_k_ff_13_q);
  J_K_Flip_Flop j_k_ff_17 (
    .J(and_53_out), .K(and_53_out), .clk(d_ff_16_q), .Q(j_k_ff_17_q), .reset(and_63_out));  // open: Qn, preset
  or or_25 (or_25_out, and_55_out, and_56_out);
  and and_56 (and_56_out, j_k_ff_26_q, not_1_out);
  D_Flip_Flop #(.trigger("falling")) d_ff_21 (
    .D(j_k_ff_17_q), .clk(d_ff_16_q), .Q(d_ff_21_q));  // open: Qn, preset, reset
  D_Flip_Flop #(.trigger("falling")) d_ff_22 (
    .D(j_k_ff_16_q), .clk(or_24_out), .Q(d_ff_22_q));  // open: Qn, preset, reset
  J_K_Flip_Flop j_k_ff_18 (
    .J(j_k_ff_15_q), .K(j_k_ff_15_q), .clk(and_65_out), .Q(j_k_ff_18_q), .reset(and_62_out));  // open: Qn, preset
  J_K_Flip_Flop j_k_ff_19 (
    .J(j_k_ff_16_q), .K(j_k_ff_16_q), .clk(or_24_out), .Q(j_k_ff_19_q), .reset(or_26_out));  // open: Qn, preset
  D_Flip_Flop d_ff_23 (.D(j_k_ff_18_q), .clk(and_65_out), .Q(d_ff_23_q));  // open: Qn, preset, reset
  J_K_Flip_Flop j_k_ff_20 (
    .J(j_k_ff_17_q), .K(j_k_ff_17_q), .clk(d_ff_16_q), .Q(j_k_ff_20_q), .reset(and_63_out));  // open: Qn, preset
  D_Flip_Flop #(.trigger("falling")) d_ff_24 (
    .D(j_k_ff_19_q), .clk(or_24_out), .Q(d_ff_24_q));  // open: Qn, preset, reset
  and and_57 (and_57_out, j_k_ff_15_q, j_k_ff_18_q);
  J_K_Flip_Flop j_k_ff_21 (
    .J(and_57_out), .K(and_57_out), .clk(and_65_out), .Q(j_k_ff_21_q), .reset(and_62_out));  // open: Qn, preset
  and and_58 (and_58_out, j_k_ff_16_q, j_k_ff_19_q);
  J_K_Flip_Flop j_k_ff_22 (
    .J(and_58_out), .K(and_58_out), .clk(or_24_out), .Q(j_k_ff_22_q), .reset(or_26_out));  // open: Qn, preset
  and and_59 (and_59_out, j_k_ff_17_q, j_k_ff_20_q);
  D_Flip_Flop #(.trigger("falling")) d_ff_25 (
    .D(j_k_ff_20_q), .clk(d_ff_16_q), .Q(d_ff_25_q));  // open: Qn, preset, reset
  D_Flip_Flop d_ff_26 (.D(j_k_ff_21_q), .clk(and_65_out), .Q(d_ff_26_q));  // open: Qn, preset, reset
  D_Flip_Flop #(.trigger("falling")) d_ff_27 (
    .D(j_k_ff_22_q), .clk(or_24_out), .Q(d_ff_27_q));  // open: Qn, preset, reset
  and and_60 (and_60_out, and_57_out, j_k_ff_21_q);
  J_K_Flip_Flop j_k_ff_23 (
    .J(and_60_out), .K(and_60_out), .clk(and_65_out), .Q(j_k_ff_23_q), .reset(and_62_out));  // open: Qn, preset
  J_K_Flip_Flop j_k_ff_24 (
    .J(and_59_out), .K(and_59_out), .clk(d_ff_16_q), .Q(j_k_ff_24_q), .reset(and_63_out));  // open: Qn, preset
  and and_61 (and_61_out, and_58_out, j_k_ff_22_q);
  J_K_Flip_Flop j_k_ff_25 (
    .J(and_61_out), .K(and_61_out), .clk(or_24_out), .Q(j_k_ff_25_q), .reset(or_26_out));  // open: Qn, preset
  and and_62 (and_62_out, j_k_ff_23_q, j_k_ff_18_q);
  and and_63 (and_63_out, j_k_ff_24_q, j_k_ff_20_q);
  D_Flip_Flop #(.trigger("falling")) d_ff_28 (
    .D(j_k_ff_24_q), .clk(d_ff_16_q), .Q(d_ff_28_q));  // open: Qn, preset, reset
  or or_26 (or_26_out, and_64_out, and_66_out);
  D_Flip_Flop d_ff_29 (.D(j_k_ff_23_q), .clk(and_65_out), .Q(d_ff_29_q));  // open: Qn, preset, reset
  and and_64 (and_64_out, j_k_ff_25_q, j_k_ff_19_q);
  D_Flip_Flop #(.trigger("falling")) d_ff_30 (
    .D(j_k_ff_25_q), .clk(or_24_out), .Q(d_ff_30_q));  // open: Qn, preset, reset
  and and_65 (and_65_out, not_3_out, or_27_out);
  or or_27 (or_27_out, and_67_out, and_71_out);
  and and_66 (and_66_out, and_58_out, j_k_ff_14_q);
  and and_67 (and_67_out, clock_1_out, nand_2_out);
  and and_68 (and_68_out, d_ff_24_q, and_69_out);
  and and_69 (and_69_out, j_k_ff_14_q, nand_2_out);
  Clock clock_1 (.out(clock_1_out));
  and and_70 (and_70_out, not_3_out, and_73_out);
  J_K_Flip_Flop j_k_ff_26 (.J(Power), .K(Power), .clk(or_28_out), .Q(j_k_ff_26_q));  // open: Qn, preset, reset
  or or_28 (or_28_out, and_70_out, and_68_out);
  not not_3 (not_3_out, Set_alarm);
  nand nand_2 (nand_2_out, Power, StopTimer);
  and and_71 (and_71_out, StopTimer, button_1_out);
  and and_72 (and_72_out, StopTimer, button_2_out);
  and and_73 (and_73_out, StopTimer, button_3_out);
  and and_74 (and_74_out, not_3_out, and_72_out);
  and and_75 (and_75_out, and_74_out, StopTimer);
  Button button_1 (.out(button_1_out));
  Button button_2 (.out(button_2_out));
  Button button_3 (.out(button_3_out));

  // Notes on the sheet:
  //   alarm line
  //   alarm line
  //   Set minute
  //   Set hour
  //   Set am/pm
  //   time
  //   alarm line
  //   alarm
  //   alarm mode
  //   am/pm
  //   clock line
  //   clock line
  //   on (red) = pm
  //   off (black) = am
  //   Set minute
  //   Set hour
  //   Set am/pm
endmodule
